// Logisim project cpu.circ as structural Verilog: 17 circuits, main circuit FADDER
module FADDER (
  input  in_1,
  input  in_2,
  input  in_3,
  output out_4,
  output out_5
);

  wire and_1_out, and_2_out, xor_1_out;

  and and_1 (and_1_out, in_2, in_3);
  xor xor_1 (xor_1_out, in_2, in_3);
  and and_2 (and_2_out, in_1, xor_1_out);
  xor xor_2 (out_5, in_1, xor_1_out);
  or or_1 (out_4, and_2_out, and_1_out);
endmodule

module _8bit_ADD_SUB (
  input  [7:0] in_1,
  input  in_2,
  input  [7:0] in_3,
  output out_4,
  output [7:0] out_5
);

  wire fadder_2_out_4, fadder_3_out_4, fadder_4_out_4, fadder_5_out_4, fadder_6_out_4, fadder_7_out_4,
       fadder_8_out_4, xor_1_out, xor_2_out, xor_3_out, xor_4_out, xor_5_out, xor_6_out, xor_7_out, xor_8_out;

  xor xor_1 (xor_1_out, in_3[7], in_2);
  xor xor_2 (xor_2_out, in_3[6], in_2);
  xor xor_3 (xor_3_out, in_3[5], in_2);
  xor xor_4 (xor_4_out, in_3[4], in_2);
  xor xor_5 (xor_5_out, in_3[3], in_2);
  xor xor_6 (xor_6_out, in_3[2], in_2);
  xor xor_7 (xor_7_out, in_3[1], in_2);
  xor xor_8 (xor_8_out, in_3[0], in_2);
  FADDER fadder_1 (.in_1(fadder_2_out_4), .in_2(in_1[7]), .in_3(xor_1_out), .out_4(out_4), .out_5(out_5[7]));
  FADDER fadder_2 (.in_1(fadder_3_out_4), .in_2(in_1[6]), .in_3(xor_2_out), .out_4(fadder_2_out_4), .out_5(out_5[6]));
  FADDER fadder_3 (.in_1(fadder_4_out_4), .in_2(in_1[5]), .in_3(xor_3_out), .out_4(fadder_3_out_4), .out_5(out_5[5]));
  FADDER fadder_4 (.in_1(fadder_5_out_4), .in_2(in_1[4]), .in_3(xor_4_out), .out_4(fadder_4_out_4), .out_5(out_5[4]));
  FADDER fadder_5 (.in_1(fadder_6_out_4), .in_2(in_1[3]), .in_3(xor_5_out), .out_4(fadder_5_out_4), .out_5(out_5[3]));
  FADDER fadder_6 (.in_1(fadder_7_out_4), .in_2(in_1[2]), .in_3(xor_6_out), .out_4(fadder_6_out_4), .out_5(out_5[2]));
  FADDER fadder_7 (.in_1(fadder_8_out_4), .in_2(in_1[1]), .in_3(xor_7_out), .out_4(fadder_7_out_4), .out_5(out_5[1]));
  FADDER fadder_8 (.in_1(in_2), .in_2(in_1[0]), .in_3(xor_8_out), .out_4(fadder_8_out_4), .out_5(out_5[0]));
endmodule

module alu8 (
  input  SHR,
  input  SHL,
  input  XOR,
  input  OR,
  input  AND,
  input  ADD,
  input  SUB,
  input  [7:0] in_8,
  input  [7:0] in_9,
  output [7:0] out_10,
  output out_11,
  output out_12,
  output out_13
);

  wire and_2_out, n8b_shl_1_out_2, n8bit_add_sub_1_out_4, not_1_out, not_2_out, xor_2_out;
  wire [7:0] and_1_out, n8b_shl_1_out_3, n8b_shr_1_out_2, n8bit_add_sub_1_out_5, or_1_out, xor_1_out;

  assign and_1_out = in_8 & in_9;  // AND_Gate and_1, 8 bits wide
  assign or_1_out = in_8 | in_9;  // OR_Gate or_1, 8 bits wide
  assign xor_1_out = in_8 ^ in_9;  // XOR_Gate xor_1, 8 bits wide
  _8b_shl u_8b_shl_1 (.in_1(in_8), .out_3(n8b_shl_1_out_3), .out_2(n8b_shl_1_out_2));
  _8b_shr u_8b_shr_1 (.in_1(in_8), .out_2(n8b_shr_1_out_2));
  not not_1 (not_1_out, SUB);
  and and_2 (and_2_out, ADD, not_1_out);
  _8bit_ADD_SUB u_8bit_add_sub_1 (
    .in_1(in_8), .in_2(SUB), .in_3(in_9), .out_4(n8bit_add_sub_1_out_4), .out_5(n8bit_add_sub_1_out_5));
  xor xor_2 (xor_2_out, and_2_out, SUB);
  not not_2 (not_2_out, SHL);
  assign out_11 = not_2_out ? n8bit_add_sub_1_out_4 : 1'bz;  // Controlled_Buffer controlled_buffer_1
  assign out_11 = SHL ? n8b_shl_1_out_2 : 1'bz;  // Controlled_Buffer controlled_buffer_2
  assign out_10 = xor_2_out ? n8bit_add_sub_1_out_5 : 8'bz;  // Controlled_Buffer controlled_buffer_3
  assign out_10 = AND ? and_1_out : 8'bz;  // Controlled_Buffer controlled_buffer_4
  assign out_10 = OR ? or_1_out : 8'bz;  // Controlled_Buffer controlled_buffer_5
  assign out_10 = XOR ? xor_1_out : 8'bz;  // Controlled_Buffer controlled_buffer_6
  assign out_10 = SHL ? n8b_shl_1_out_3 : 8'bz;  // Controlled_Buffer controlled_buffer_7
  assign out_10 = SHR ? n8b_shr_1_out_2 : 8'bz;  // Controlled_Buffer controlled_buffer_8
  nor nor_1 (out_12, out_10[0], out_10[1], out_10[2], out_10[3], out_10[5], out_10[6], out_10[7], out_10[4]);

  assign out_13 = out_10[7];
endmodule

module _8b_shl (
  input  [7:0] in_1,
  output out_2,
  output [7:0] out_3
);


  assign out_2 = in_1[7];
  assign out_3 = {in_1[6:0], 1'b0};
endmodule

module _8b_shr (
  input  [7:0] in_1,
  output [7:0] out_2
);


  assign out_2 = {1'b0, in_1[7:1]};
endmodule

module sr_latch (
  input  in_1,
  input  in_2,
  input  in_3,
  output out_4
);

  wire and_1_out, and_2_out, nor_1_out, not_1_out, or_1_out;

  not not_1 (not_1_out, in_1);
  and and_1 (and_1_out, in_1, in_2);
  and and_2 (and_2_out, in_2, not_1_out);
  nor nor_1 (nor_1_out, and_1_out, out_4);
  nor nor_2 (out_4, nor_1_out, or_1_out);
  or or_1 (or_1_out, and_2_out, in_3);
endmodule

module ram (
  input  in_1,
  input  [4:0] in_2,
  input  in_3,
  input  in_4,
  input  [7:0] in_5,
  input  in_6,
  output [7:0] out_7
);

  wire and_1_out, and_2_out, and_3_out, and_4_out, and_5_out, and_6_out, and_7_out, and_8_out, and_9_out,
       and_10_out, and_11_out, and_12_out, and_13_out, and_14_out, and_15_out, and_16_out, and_17_out,
       and_18_out, and_19_out, and_20_out, and_21_out, and_22_out, and_23_out, and_24_out, and_25_out,
       and_26_out, and_27_out, and_28_out, and_29_out, and_30_out, and_31_out, and_32_out, and_33_out,
       and_34_out, and_35_out, and_36_out, and_37_out, and_38_out, and_39_out, and_40_out, and_41_out,
       and_42_out, and_43_out, and_44_out, and_45_out, and_46_out, and_47_out, and_48_out, and_49_out,
       and_50_out, and_51_out, and_52_out, and_53_out, and_54_out, and_55_out, and_56_out, and_57_out,
       and_58_out, and_59_out, and_60_out, and_61_out, and_62_out, and_63_out, and_64_out, decoder_1_out0,
       decoder_1_out1, decoder_1_out2, decoder_1_out3, decoder_1_out4, decoder_1_out5, decoder_1_out6,
       decoder_1_out7, decoder_1_out8, decoder_1_out9, decoder_1_out10, decoder_1_out11, decoder_1_out12,
       decoder_1_out13, decoder_1_out14, decoder_1_out15, decoder_1_out16, decoder_1_out17, decoder_1_out18,
       decoder_1_out19, decoder_1_out20, decoder_1_out21, decoder_1_out22, decoder_1_out23, decoder_1_out24,
       decoder_1_out25, decoder_1_out26, decoder_1_out27, decoder_1_out28, decoder_1_out29, decoder_1_out30,
       decoder_1_out31;
  wire [7:0] register_1_q, register_2_q, register_3_q, register_4_q, register_5_q, register_6_q,
       register_7_q, register_8_q, register_9_q, register_10_q, register_11_q, register_12_q, register_13_q,
       register_14_q, register_15_q, register_16_q, register_17_q, register_18_q, register_19_q,
       register_20_q, register_21_q, register_22_q, register_23_q, register_24_q, register_25_q,
       register_26_q, register_27_q, register_28_q, register_29_q, register_30_q, register_31_q,
       register_32_q;

  Decoder #(.select(5)) decoder_1 (
    .out0(decoder_1_out0), .out1(decoder_1_out1), .out2(decoder_1_out2), .out3(decoder_1_out3),
    .out4(decoder_1_out4), .out5(decoder_1_out5), .out6(decoder_1_out6), .out7(decoder_1_out7),
    .out8(decoder_1_out8), .out9(decoder_1_out9), .out10(decoder_1_out10), .out11(decoder_1_out11),
    .out12(decoder_1_out12), .out13(decoder_1_out13), .out14(decoder_1_out14), .out15(decoder_1_out15),
    .out16(decoder_1_out16), .out17(decoder_1_out17), .out18(decoder_1_out18), .out19(decoder_1_out19),
    .out20(decoder_1_out20), .out21(decoder_1_out21), .out22(decoder_1_out22), .out23(decoder_1_out23),
    .out24(decoder_1_out24), .out25(decoder_1_out25), .out26(decoder_1_out26), .out27(decoder_1_out27),
    .out28(decoder_1_out28), .out29(decoder_1_out29), .out30(decoder_1_out30), .out31(decoder_1_out31),
    .sel(in_2), .en(in_6));
  and and_1 (and_1_out, decoder_1_out0, in_3);
  and and_2 (and_2_out, decoder_1_out1, in_3);
  and and_3 (and_3_out, decoder_1_out2, in_3);
  and and_4 (and_4_out, decoder_1_out3, in_3);
  and and_5 (and_5_out, decoder_1_out4, in_3);
  and and_6 (and_6_out, decoder_1_out5, in_3);
  and and_7 (and_7_out, decoder_1_out6, in_3);
  and and_8 (and_8_out, decoder_1_out7, in_3);
  and and_9 (and_9_out, decoder_1_out8, in_3);
  and and_10 (and_10_out, decoder_1_out9, in_3);
  and and_11 (and_11_out, decoder_1_out10, in_3);
  and and_12 (and_12_out, decoder_1_out11, in_3);
  and and_13 (and_13_out, decoder_1_out12, in_3);
  and and_14 (and_14_out, decoder_1_out13, in_3);
  and and_15 (and_15_out, decoder_1_out14, in_3);
  and and_16 (and_16_out, decoder_1_out15, in_3);
  and and_17 (and_17_out, decoder_1_out16, in_3);
  and and_18 (and_18_out, decoder_1_out17, in_3);
  and and_19 (and_19_out, decoder_1_out18, in_3);
  and and_20 (and_20_out, decoder_1_out19, in_3);
  and and_21 (and_21_out, decoder_1_out20, in_3);
  and and_22 (and_22_out, decoder_1_out21, in_3);
  and and_23 (and_23_out, decoder_1_out22, in_3);
  and and_24 (and_24_out, decoder_1_out23, in_3);
  and and_25 (and_25_out, decoder_1_out24, in_3);
  and and_26 (and_26_out, decoder_1_out25, in_3);
  and and_27 (and_27_out, decoder_1_out26, in_3);
  and and_28 (and_28_out, decoder_1_out27, in_3);
  and and_29 (and_29_out, decoder_1_out28, in_3);
  and and_30 (and_30_out, decoder_1_out29, in_3);
  and and_31 (and_31_out, decoder_1_out30, in_3);
  and and_32 (and_32_out, decoder_1_out31, in_3);
  assign out_7 = in_1 ? in_5 : 8'bz;  // Controlled_Buffer controlled_buffer_1
  Register register_1 (.D(out_7), .en(and_1_out), .Q(register_1_q), .clk(in_4));  // open: clr
  and and_33 (and_33_out, decoder_1_out0, in_3);
  Register register_2 (.D(out_7), .en(and_2_out), .Q(register_2_q), .clk(in_4));  // open: clr
  and and_34 (and_34_out, decoder_1_out1, in_3);
  Register register_3 (.D(out_7), .en(and_3_out), .Q(register_3_q), .clk(in_4));  // open: clr
  and and_35 (and_35_out, decoder_1_out2, in_3);
  Register register_4 (.D(out_7), .en(and_4_out), .Q(register_4_q), .clk(in_4));  // open: clr
  and and_36 (and_36_out, decoder_1_out3, in_3);
  Register register_5 (.D(out_7), .en(and_5_out), .Q(register_5_q), .clk(in_4));  // open: clr
  and and_37 (and_37_out, decoder_1_out4, in_3);
  Register register_6 (.D(out_7), .en(and_6_out), .Q(register_6_q), .clk(in_4));  // open: clr
  and and_38 (and_38_out, decoder_1_out5, in_3);
  Register register_7 (.D(out_7), .en(and_7_out), .Q(register_7_q), .clk(in_4));  // open: clr
  and and_39 (and_39_out, decoder_1_out6, in_3);
  Register register_8 (.D(out_7), .en(and_8_out), .Q(register_8_q), .clk(in_4));  // open: clr
  and and_40 (and_40_out, decoder_1_out7, in_3);
  Register register_9 (.D(out_7), .en(and_9_out), .Q(register_9_q), .clk(in_4));  // open: clr
  and and_41 (and_41_out, decoder_1_out8, in_3);
  Register register_10 (.D(out_7), .en(and_10_out), .Q(register_10_q), .clk(in_4));  // open: clr
  and and_42 (and_42_out, decoder_1_out9, in_3);
  Register register_11 (.D(out_7), .en(and_11_out), .Q(register_11_q), .clk(in_4));  // open: clr
  and and_43 (and_43_out, decoder_1_out10, in_3);
  Register register_12 (.D(out_7), .en(and_12_out), .Q(register_12_q), .clk(in_4));  // open: clr
  and and_44 (and_44_out, decoder_1_out11, in_3);
  Register register_13 (.D(out_7), .en(and_13_out), .Q(register_13_q), .clk(in_4));  // open: clr
  and and_45 (and_45_out, decoder_1_out12, in_3);
  Register register_14 (.D(out_7), .en(and_14_out), .Q(register_14_q), .clk(in_4));  // open: clr
  and and_46 (and_46_out, decoder_1_out13, in_3);
  Register register_15 (.D(out_7), .en(and_15_out), .Q(register_15_q), .clk(in_4));  // open: clr
  and and_47 (and_47_out, decoder_1_out14, in_3);
  Register register_16 (.D(out_7), .en(and_16_out), .Q(register_16_q), .clk(in_4));  // open: clr
  and and_48 (and_48_out, decoder_1_out15, in_3);
  Register register_17 (.D(out_7), .en(and_17_out), .Q(register_17_q), .clk(in_4));  // open: clr
  and and_49 (and_49_out, decoder_1_out16, in_3);
  Register register_18 (.D(out_7), .en(and_18_out), .Q(register_18_q), .clk(in_4));  // open: clr
  and and_50 (and_50_out, decoder_1_out17, in_3);
  Register register_19 (.D(out_7), .en(and_19_out), .Q(register_19_q), .clk(in_4));  // open: clr
  and and_51 (and_51_out, decoder_1_out18, in_3);
  Register register_20 (.D(out_7), .en(and_20_out), .Q(register_20_q), .clk(in_4));  // open: clr
  and and_52 (and_52_out, decoder_1_out19, in_3);
  Register register_21 (.D(out_7), .en(and_21_out), .Q(register_21_q), .clk(in_4));  // open: clr
  and and_53 (and_53_out, decoder_1_out20, in_3);
  Register register_22 (.D(out_7), .en(and_22_out), .Q(register_22_q), .clk(in_4));  // open: clr
  and and_54 (and_54_out, decoder_1_out21, in_3);
  Register register_23 (.D(out_7), .en(and_23_out), .Q(register_23_q), .clk(in_4));  // open: clr
  and and_55 (and_55_out, decoder_1_out22, in_3);
  Register register_24 (.D(out_7), .en(and_24_out), .Q(register_24_q), .clk(in_4));  // open: clr
  and and_56 (and_56_out, decoder_1_out23, in_3);
  Register register_25 (.D(out_7), .en(and_25_out), .Q(register_25_q), .clk(in_4));  // open: clr
  and and_57 (and_57_out, decoder_1_out24, in_3);
  Register register_26 (.D(out_7), .en(and_26_out), .Q(register_26_q), .clk(in_4));  // open: clr
  and and_58 (and_58_out, decoder_1_out25, in_3);
  Register register_27 (.D(out_7), .en(and_27_out), .Q(register_27_q), .clk(in_4));  // open: clr
  and and_59 (and_59_out, decoder_1_out26, in_3);
  Register register_28 (.D(out_7), .en(and_28_out), .Q(register_28_q), .clk(in_4));  // open: clr
  and and_60 (and_60_out, decoder_1_out27, in_3);
  Register register_29 (.D(out_7), .en(and_29_out), .Q(register_29_q), .clk(in_4));  // open: clr
  and and_61 (and_61_out, decoder_1_out28, in_3);
  Register register_30 (.D(out_7), .en(and_30_out), .Q(register_30_q), .clk(in_4));  // open: clr
  and and_62 (and_62_out, decoder_1_out29, in_3);
  Register register_31 (.D(out_7), .en(and_31_out), .Q(register_31_q), .clk(in_4));  // open: clr
  and and_63 (and_63_out, decoder_1_out30, in_3);
  Register register_32 (.D(out_7), .en(and_32_out), .Q(register_32_q), .clk(in_4));  // open: clr
  and and_64 (and_64_out, decoder_1_out31, in_3);
  assign out_7 = and_33_out ? register_1_q : 8'bz;  // Controlled_Buffer controlled_buffer_2
  assign out_7 = and_34_out ? register_2_q : 8'bz;  // Controlled_Buffer controlled_buffer_3
  assign out_7 = and_35_out ? register_3_q : 8'bz;  // Controlled_Buffer controlled_buffer_4
  assign out_7 = and_36_out ? register_4_q : 8'bz;  // Controlled_Buffer controlled_buffer_5
  assign out_7 = and_37_out ? register_5_q : 8'bz;  // Controlled_Buffer controlled_buffer_6
  assign out_7 = and_38_out ? register_6_q : 8'bz;  // Controlled_Buffer controlled_buffer_7
  assign out_7 = and_39_out ? register_7_q : 8'bz;  // Controlled_Buffer controlled_buffer_8
  assign out_7 = and_40_out ? register_8_q : 8'bz;  // Controlled_Buffer controlled_buffer_9
  assign out_7 = and_41_out ? register_9_q : 8'bz;  // Controlled_Buffer controlled_buffer_10
  assign out_7 = and_42_out ? register_10_q : 8'bz;  // Controlled_Buffer controlled_buffer_11
  assign out_7 = and_43_out ? register_11_q : 8'bz;  // Controlled_Buffer controlled_buffer_12
  assign out_7 = and_44_out ? register_12_q : 8'bz;  // Controlled_Buffer controlled_buffer_13
  assign out_7 = and_45_out ? register_13_q : 8'bz;  // Controlled_Buffer controlled_buffer_14
  assign out_7 = and_46_out ? register_14_q : 8'bz;  // Controlled_Buffer controlled_buffer_15
  assign out_7 = and_47_out ? register_15_q : 8'bz;  // Controlled_Buffer controlled_buffer_16
  assign out_7 = and_48_out ? register_16_q : 8'bz;  // Controlled_Buffer controlled_buffer_17
  assign out_7 = and_49_out ? register_17_q : 8'bz;  // Controlled_Buffer controlled_buffer_18
  assign out_7 = and_50_out ? register_18_q : 8'bz;  // Controlled_Buffer controlled_buffer_19
  assign out_7 = and_51_out ? register_19_q : 8'bz;  // Controlled_Buffer controlled_buffer_20
  assign out_7 = and_52_out ? register_20_q : 8'bz;  // Controlled_Buffer controlled_buffer_21
  assign out_7 = and_53_out ? register_21_q : 8'bz;  // Controlled_Buffer controlled_buffer_22
  assign out_7 = and_54_out ? register_22_q : 8'bz;  // Controlled_Buffer controlled_buffer_23
  assign out_7 = and_55_out ? register_23_q : 8'bz;  // Controlled_Buffer controlled_buffer_24
  assign out_7 = and_56_out ? register_24_q : 8'bz;  // Controlled_Buffer controlled_buffer_25
  assign out_7 = and_57_out ? register_25_q : 8'bz;  // Controlled_Buffer controlled_buffer_26
  assign out_7 = and_58_out ? register_26_q : 8'bz;  // Controlled_Buffer controlled_buffer_27
  assign out_7 = and_59_out ? register_27_q : 8'bz;  // Controlled_Buffer controlled_buffer_28
  assign out_7 = and_60_out ? register_28_q : 8'bz;  // Controlled_Buffer controlled_buffer_29
  assign out_7 = and_61_out ? register_29_q : 8'bz;  // Controlled_Buffer controlled_buffer_30
  assign out_7 = and_62_out ? register_30_q : 8'bz;  // Controlled_Buffer controlled_buffer_31
  assign out_7 = and_63_out ? register_31_q : 8'bz;  // Controlled_Buffer controlled_buffer_32
  assign out_7 = and_64_out ? register_32_q : 8'bz;  // Controlled_Buffer controlled_buffer_33
endmodule

module counter (
  input  in_1,
  input  in_2,
  input  in_3,
  input  in_4,
  output out_5,
  output out_6
);

  wire multiplexer_1_out;

  Multiplexer #(.enable("false")) multiplexer_1 (.in0(in_1), .in1(out_6), .out(multiplexer_1_out), .sel(in_2));
  D_Flip_Flop d_ff_1 (.clk(in_3), .D(multiplexer_1_out), .Q(out_5), .Qn(out_6), .en(in_4));  // open: preset, reset
endmodule

module program_counter (
  input  in_1,
  input  in_2,
  input  in_3
);

  wire and_1_out, and_2_out, and_3_out, counter_1_out_5, counter_2_out_5, counter_3_out_5, undriven,
       undriven_2, undriven_3, undriven_4;

  counter counter_1 (.in_1(undriven), .in_2(in_1), .in_3(in_2), .in_4(in_3), .out_5(counter_1_out_5));  // open: out_6
  and and_1 (and_1_out, in_1, counter_1_out_5);
  counter counter_2 (
    .in_1(undriven_2), .in_2(and_1_out), .in_3(in_2), .in_4(in_3), .out_5(counter_2_out_5));  // open: out_6
  and and_2 (and_2_out, in_1, and_1_out, counter_2_out_5);
  counter counter_3 (
    .in_1(undriven_3), .in_2(and_2_out), .in_3(in_2), .in_4(in_3), .out_5(counter_3_out_5));  // open: out_6
  and and_3 (and_3_out, in_1, counter_1_out_5, counter_2_out_5, counter_3_out_5);
  counter counter_4 (.in_1(undriven_4), .in_2(and_3_out), .in_3(in_2), .in_4(in_3));  // open: out_5, out_6
endmodule

module _32bit_add_sub (
  input  [31:0] in_1,
  input  [31:0] in_2,
  input  in_3,
  output out_4,
  output [31:0] out_5
);

  wire fadder_2_out_4, fadder_3_out_4, fadder_4_out_4, fadder_5_out_4, fadder_6_out_4, fadder_7_out_4,
       fadder_8_out_4, fadder_9_out_4, fadder_10_out_4, fadder_11_out_4, fadder_12_out_4, fadder_13_out_4,
       fadder_14_out_4, fadder_15_out_4, fadder_16_out_4, fadder_17_out_4, fadder_18_out_4, fadder_19_out_4,
       fadder_20_out_4, fadder_21_out_4, fadder_22_out_4, fadder_23_out_4, fadder_24_out_4, fadder_25_out_4,
       fadder_26_out_4, fadder_27_out_4, fadder_28_out_4, fadder_29_out_4, fadder_30_out_4, fadder_31_out_4,
       fadder_32_out_4, xor_1_out, xor_2_out, xor_3_out, xor_4_out, xor_5_out, xor_6_out, xor_7_out,
       xor_8_out, xor_9_out, xor_10_out, xor_11_out, xor_12_out, xor_13_out, xor_14_out, xor_15_out,
       xor_16_out, xor_17_out, xor_18_out, xor_19_out, xor_20_out, xor_21_out, xor_22_out, xor_23_out,
       xor_24_out, xor_25_out, xor_26_out, xor_27_out, xor_28_out, xor_29_out, xor_30_out, xor_31_out,
       xor_32_out;

  xor xor_1 (xor_1_out, in_2[31], in_3);
  xor xor_2 (xor_2_out, in_2[30], in_3);
  xor xor_3 (xor_3_out, in_2[29], in_3);
  xor xor_4 (xor_4_out, in_2[28], in_3);
  xor xor_5 (xor_5_out, in_2[27], in_3);
  xor xor_6 (xor_6_out, in_2[26], in_3);
  xor xor_7 (xor_7_out, in_2[25], in_3);
  xor xor_8 (xor_8_out, in_2[24], in_3);
  xor xor_9 (xor_9_out, in_2[23], in_3);
  xor xor_10 (xor_10_out, in_2[22], in_3);
  xor xor_11 (xor_11_out, in_2[21], in_3);
  xor xor_12 (xor_12_out, in_2[20], in_3);
  xor xor_13 (xor_13_out, in_2[19], in_3);
  xor xor_14 (xor_14_out, in_2[18], in_3);
  xor xor_15 (xor_15_out, in_2[17], in_3);
  xor xor_16 (xor_16_out, in_2[16], in_3);
  xor xor_17 (xor_17_out, in_2[15], in_3);
  xor xor_18 (xor_18_out, in_2[14], in_3);
  xor xor_19 (xor_19_out, in_2[13], in_3);
  xor xor_20 (xor_20_out, in_2[12], in_3);
  xor xor_21 (xor_21_out, in_2[11], in_3);
  xor xor_22 (xor_22_out, in_2[10], in_3);
  xor xor_23 (xor_23_out, in_2[9], in_3);
  xor xor_24 (xor_24_out, in_2[8], in_3);
  xor xor_25 (xor_25_out, in_2[7], in_3);
  xor xor_26 (xor_26_out, in_2[6], in_3);
  xor xor_27 (xor_27_out, in_2[5], in_3);
  xor xor_28 (xor_28_out, in_2[4], in_3);
  xor xor_29 (xor_29_out, in_2[3], in_3);
  xor xor_30 (xor_30_out, in_2[2], in_3);
  xor xor_31 (xor_31_out, in_2[1], in_3);
  xor xor_32 (xor_32_out, in_2[0], in_3);
  FADDER fadder_1 (.in_1(fadder_2_out_4), .in_2(in_1[31]), .in_3(xor_1_out), .out_4(out_4), .out_5(out_5[31]));
  FADDER fadder_2 (.in_1(fadder_3_out_4), .in_2(in_1[30]), .in_3(xor_2_out), .out_4(fadder_2_out_4), .out_5(out_5[30]));
  FADDER fadder_3 (.in_1(fadder_4_out_4), .in_2(in_1[29]), .in_3(xor_3_out), .out_4(fadder_3_out_4), .out_5(out_5[29]));
  FADDER fadder_4 (.in_1(fadder_5_out_4), .in_2(in_1[28]), .in_3(xor_4_out), .out_4(fadder_4_out_4), .out_5(out_5[28]));
  FADDER fadder_5 (.in_1(fadder_6_out_4), .in_2(in_1[27]), .in_3(xor_5_out), .out_4(fadder_5_out_4), .out_5(out_5[27]));
  FADDER fadder_6 (.in_1(fadder_7_out_4), .in_2(in_1[26]), .in_3(xor_6_out), .out_4(fadder_6_out_4), .out_5(out_5[26]));
  FADDER fadder_7 (.in_1(fadder_8_out_4), .in_2(in_1[25]), .in_3(xor_7_out), .out_4(fadder_7_out_4), .out_5(out_5[25]));
  FADDER fadder_8 (.in_1(fadder_9_out_4), .in_2(in_1[24]), .in_3(xor_8_out), .out_4(fadder_8_out_4), .out_5(out_5[24]));
  FADDER fadder_9 (
    .in_1(fadder_10_out_4), .in_2(in_1[23]), .in_3(xor_9_out), .out_4(fadder_9_out_4), .out_5(out_5[23]));
  FADDER fadder_10 (
    .in_1(fadder_11_out_4), .in_2(in_1[22]), .in_3(xor_10_out), .out_4(fadder_10_out_4), .out_5(out_5[22]));
  FADDER fadder_11 (
    .in_1(fadder_12_out_4), .in_2(in_1[21]), .in_3(xor_11_out), .out_4(fadder_11_out_4), .out_5(out_5[21]));
  FADDER fadder_12 (
    .in_1(fadder_13_out_4), .in_2(in_1[20]), .in_3(xor_12_out), .out_4(fadder_12_out_4), .out_5(out_5[20]));
  FADDER fadder_13 (
    .in_1(fadder_14_out_4), .in_2(in_1[19]), .in_3(xor_13_out), .out_4(fadder_13_out_4), .out_5(out_5[19]));
  FADDER fadder_14 (
    .in_1(fadder_15_out_4), .in_2(in_1[18]), .in_3(xor_14_out), .out_4(fadder_14_out_4), .out_5(out_5[18]));
  FADDER fadder_15 (
    .in_1(fadder_16_out_4), .in_2(in_1[17]), .in_3(xor_15_out), .out_4(fadder_15_out_4), .out_5(out_5[17]));
  FADDER fadder_16 (
    .in_1(fadder_17_out_4), .in_2(in_1[16]), .in_3(xor_16_out), .out_4(fadder_16_out_4), .out_5(out_5[16]));
  FADDER fadder_17 (
    .in_1(fadder_18_out_4), .in_2(in_1[15]), .in_3(xor_17_out), .out_4(fadder_17_out_4), .out_5(out_5[15]));
  FADDER fadder_18 (
    .in_1(fadder_19_out_4), .in_2(in_1[14]), .in_3(xor_18_out), .out_4(fadder_18_out_4), .out_5(out_5[14]));
  FADDER fadder_19 (
    .in_1(fadder_20_out_4), .in_2(in_1[13]), .in_3(xor_19_out), .out_4(fadder_19_out_4), .out_5(out_5[13]));
  FADDER fadder_20 (
    .in_1(fadder_21_out_4), .in_2(in_1[12]), .in_3(xor_20_out), .out_4(fadder_20_out_4), .out_5(out_5[12]));
  FADDER fadder_21 (
    .in_1(fadder_22_out_4), .in_2(in_1[11]), .in_3(xor_21_out), .out_4(fadder_21_out_4), .out_5(out_5[11]));
  FADDER fadder_22 (
    .in_1(fadder_23_out_4), .in_2(in_1[10]), .in_3(xor_22_out), .out_4(fadder_22_out_4), .out_5(out_5[10]));
  FADDER fadder_23 (
    .in_1(fadder_24_out_4), .in_2(in_1[9]), .in_3(xor_23_out), .out_4(fadder_23_out_4), .out_5(out_5[9]));
  FADDER fadder_24 (
    .in_1(fadder_25_out_4), .in_2(in_1[8]), .in_3(xor_24_out), .out_4(fadder_24_out_4), .out_5(out_5[8]));
  FADDER fadder_25 (
    .in_1(fadder_26_out_4), .in_2(in_1[7]), .in_3(xor_25_out), .out_4(fadder_25_out_4), .out_5(out_5[7]));
  FADDER fadder_26 (
    .in_1(fadder_27_out_4), .in_2(in_1[6]), .in_3(xor_26_out), .out_4(fadder_26_out_4), .out_5(out_5[6]));
  FADDER fadder_27 (
    .in_1(fadder_28_out_4), .in_2(in_1[5]), .in_3(xor_27_out), .out_4(fadder_27_out_4), .out_5(out_5[5]));
  FADDER fadder_28 (
    .in_1(fadder_29_out_4), .in_2(in_1[4]), .in_3(xor_28_out), .out_4(fadder_28_out_4), .out_5(out_5[4]));
  FADDER fadder_29 (
    .in_1(fadder_30_out_4), .in_2(in_1[3]), .in_3(xor_29_out), .out_4(fadder_29_out_4), .out_5(out_5[3]));
  FADDER fadder_30 (
    .in_1(fadder_31_out_4), .in_2(in_1[2]), .in_3(xor_30_out), .out_4(fadder_30_out_4), .out_5(out_5[2]));
  FADDER fadder_31 (
    .in_1(fadder_32_out_4), .in_2(in_1[1]), .in_3(xor_31_out), .out_4(fadder_31_out_4), .out_5(out_5[1]));
  FADDER fadder_32 (.in_1(in_3), .in_2(in_1[0]), .in_3(xor_32_out), .out_4(fadder_32_out_4), .out_5(out_5[0]));
endmodule

module _32bit_multiply (
  input  [31:0] in_1,
  input  [31:0] in_2,
  output [31:0] out_3,
  output out_4
);

  wire n32b_shl_1_out_2, n32b_shl_2_out_2, n32b_shl_3_out_2, n32b_shl_4_out_2, n32b_shl_5_out_2,
       n32b_shl_6_out_2, n32b_shl_7_out_2, n32b_shl_8_out_2, n32b_shl_9_out_2, n32b_shl_10_out_2,
       n32b_shl_11_out_2, n32b_shl_12_out_2, n32b_shl_13_out_2, n32b_shl_14_out_2, n32b_shl_15_out_2,
       n32b_shl_16_out_2, n32b_shl_17_out_2, n32b_shl_18_out_2, n32b_shl_19_out_2, n32b_shl_20_out_2,
       n32b_shl_21_out_2, n32b_shl_22_out_2, n32b_shl_23_out_2, n32b_shl_24_out_2, n32b_shl_25_out_2,
       n32b_shl_26_out_2, n32b_shl_27_out_2, n32b_shl_28_out_2, n32b_shl_29_out_2, n32b_shl_30_out_2,
       n32b_shl_31_out_2, n32bit_add_sub_1_out_4, n32bit_add_sub_2_out_4, n32bit_add_sub_3_out_4,
       n32bit_add_sub_4_out_4, n32bit_add_sub_5_out_4, n32bit_add_sub_6_out_4, n32bit_add_sub_7_out_4,
       n32bit_add_sub_8_out_4, n32bit_add_sub_9_out_4, n32bit_add_sub_10_out_4, n32bit_add_sub_11_out_4,
       n32bit_add_sub_12_out_4, n32bit_add_sub_13_out_4, n32bit_add_sub_14_out_4, n32bit_add_sub_15_out_4,
       n32bit_add_sub_16_out_4, n32bit_add_sub_17_out_4, n32bit_add_sub_18_out_4, n32bit_add_sub_19_out_4,
       n32bit_add_sub_20_out_4, n32bit_add_sub_21_out_4, n32bit_add_sub_22_out_4, n32bit_add_sub_23_out_4,
       n32bit_add_sub_24_out_4, n32bit_add_sub_25_out_4, n32bit_add_sub_26_out_4, n32bit_add_sub_27_out_4,
       n32bit_add_sub_28_out_4, n32bit_add_sub_29_out_4, n32bit_add_sub_30_out_4, n32bit_add_sub_31_out_4,
       not_1_out, not_2_out, not_3_out, not_4_out, not_5_out, not_6_out, not_7_out, not_8_out, not_9_out,
       not_10_out, not_11_out, not_12_out, not_13_out, not_14_out, not_15_out, not_16_out, not_17_out,
       not_18_out, not_19_out, not_20_out, not_21_out, not_22_out, not_23_out, not_24_out, not_25_out,
       not_26_out, not_27_out, not_28_out, not_29_out, not_30_out, not_31_out, not_32_out, or_1_out,
       or_3_out, or_4_out, or_5_out, undriven;
  wire [31:0] controlled_buffer_1_out, controlled_buffer_3_out, controlled_buffer_5_out,
       controlled_buffer_7_out, controlled_buffer_9_out, controlled_buffer_11_out, controlled_buffer_13_out,
       controlled_buffer_15_out, controlled_buffer_17_out, controlled_buffer_19_out,
       controlled_buffer_21_out, controlled_buffer_23_out, controlled_buffer_25_out,
       controlled_buffer_27_out, controlled_buffer_29_out, controlled_buffer_31_out,
       controlled_buffer_33_out, controlled_buffer_35_out, controlled_buffer_37_out,
       controlled_buffer_39_out, controlled_buffer_41_out, controlled_buffer_43_out,
       controlled_buffer_45_out, controlled_buffer_47_out, controlled_buffer_49_out,
       controlled_buffer_51_out, controlled_buffer_53_out, controlled_buffer_55_out,
       controlled_buffer_57_out, controlled_buffer_59_out, controlled_buffer_61_out,
       controlled_buffer_63_out, n32b_shl_1_out_3, n32b_shl_2_out_3, n32b_shl_3_out_3, n32b_shl_4_out_3,
       n32b_shl_5_out_3, n32b_shl_6_out_3, n32b_shl_7_out_3, n32b_shl_8_out_3, n32b_shl_9_out_3,
       n32b_shl_10_out_3, n32b_shl_11_out_3, n32b_shl_12_out_3, n32b_shl_13_out_3, n32b_shl_14_out_3,
       n32b_shl_15_out_3, n32b_shl_16_out_3, n32b_shl_17_out_3, n32b_shl_18_out_3, n32b_shl_19_out_3,
       n32b_shl_20_out_3, n32b_shl_21_out_3, n32b_shl_22_out_3, n32b_shl_23_out_3, n32b_shl_24_out_3,
       n32b_shl_25_out_3, n32b_shl_26_out_3, n32b_shl_27_out_3, n32b_shl_28_out_3, n32b_shl_29_out_3,
       n32b_shl_30_out_3, n32b_shl_31_out_3, n32bit_add_sub_1_out_5, n32bit_add_sub_2_out_5,
       n32bit_add_sub_3_out_5, n32bit_add_sub_4_out_5, n32bit_add_sub_5_out_5, n32bit_add_sub_6_out_5,
       n32bit_add_sub_7_out_5, n32bit_add_sub_8_out_5, n32bit_add_sub_9_out_5, n32bit_add_sub_10_out_5,
       n32bit_add_sub_11_out_5, n32bit_add_sub_12_out_5, n32bit_add_sub_13_out_5, n32bit_add_sub_14_out_5,
       n32bit_add_sub_15_out_5, n32bit_add_sub_16_out_5, n32bit_add_sub_17_out_5, n32bit_add_sub_18_out_5,
       n32bit_add_sub_19_out_5, n32bit_add_sub_20_out_5, n32bit_add_sub_21_out_5, n32bit_add_sub_22_out_5,
       n32bit_add_sub_23_out_5, n32bit_add_sub_24_out_5, n32bit_add_sub_25_out_5, n32bit_add_sub_26_out_5,
       n32bit_add_sub_27_out_5, n32bit_add_sub_28_out_5, n32bit_add_sub_29_out_5, n32bit_add_sub_30_out_5;

  _32b_shl u_32b_shl_1 (.in_1(in_2), .out_2(n32b_shl_1_out_2), .out_3(n32b_shl_1_out_3));
  assign controlled_buffer_1_out = in_1[0] ? in_2 : 32'bz;  // Controlled_Buffer controlled_buffer_1
  not not_1 (not_1_out, in_1[0]);
  assign controlled_buffer_1_out = not_1_out ? {32{1'b0}} : 32'bz;  // Controlled_Buffer controlled_buffer_2
  assign controlled_buffer_3_out = in_1[1] ? n32b_shl_1_out_3 : 32'bz;  // Controlled_Buffer controlled_buffer_3
  not not_2 (not_2_out, in_1[1]);
  assign controlled_buffer_3_out = not_2_out ? {32{1'b0}} : 32'bz;  // Controlled_Buffer controlled_buffer_4
  _32b_shl u_32b_shl_2 (.in_1(n32b_shl_1_out_3), .out_2(n32b_shl_2_out_2), .out_3(n32b_shl_2_out_3));
  not not_3 (not_3_out, in_1[2]);
  assign controlled_buffer_5_out = not_3_out ? {32{1'b0}} : 32'bz;  // Controlled_Buffer controlled_buffer_5
  assign controlled_buffer_5_out = in_1[2] ? n32b_shl_2_out_3 : 32'bz;  // Controlled_Buffer controlled_buffer_6
  _32b_shl u_32b_shl_3 (.in_1(n32b_shl_2_out_3), .out_2(n32b_shl_3_out_2), .out_3(n32b_shl_3_out_3));
  assign controlled_buffer_7_out = in_1[3] ? n32b_shl_3_out_3 : 32'bz;  // Controlled_Buffer controlled_buffer_7
  not not_4 (not_4_out, in_1[3]);
  _32b_shl u_32b_shl_4 (.in_1(n32b_shl_3_out_3), .out_2(n32b_shl_4_out_2), .out_3(n32b_shl_4_out_3));
  assign controlled_buffer_7_out = not_4_out ? {32{1'b0}} : 32'bz;  // Controlled_Buffer controlled_buffer_8
  not not_5 (not_5_out, in_1[4]);
  assign controlled_buffer_9_out = not_5_out ? {32{1'b0}} : 32'bz;  // Controlled_Buffer controlled_buffer_9
  assign controlled_buffer_9_out = in_1[4] ? n32b_shl_4_out_3 : 32'bz;  // Controlled_Buffer controlled_buffer_10
  _32b_shl u_32b_shl_5 (.in_1(n32b_shl_4_out_3), .out_2(n32b_shl_5_out_2), .out_3(n32b_shl_5_out_3));
  not not_6 (not_6_out, in_1[5]);
  assign controlled_buffer_11_out = in_1[5] ? n32b_shl_5_out_3 : 32'bz;  // Controlled_Buffer controlled_buffer_11
  _32b_shl u_32b_shl_6 (.in_1(n32b_shl_5_out_3), .out_2(n32b_shl_6_out_2), .out_3(n32b_shl_6_out_3));
  assign controlled_buffer_11_out = not_6_out ? {32{1'b0}} : 32'bz;  // Controlled_Buffer controlled_buffer_12
  not not_7 (not_7_out, in_1[6]);
  assign controlled_buffer_13_out = not_7_out ? {32{1'b0}} : 32'bz;  // Controlled_Buffer controlled_buffer_13
  assign controlled_buffer_13_out = in_1[6] ? n32b_shl_6_out_3 : 32'bz;  // Controlled_Buffer controlled_buffer_14
  _32b_shl u_32b_shl_7 (.in_1(n32b_shl_6_out_3), .out_2(n32b_shl_7_out_2), .out_3(n32b_shl_7_out_3));
  not not_8 (not_8_out, in_1[7]);
  assign controlled_buffer_15_out = not_8_out ? {32{1'b0}} : 32'bz;  // Controlled_Buffer controlled_buffer_15
  assign controlled_buffer_15_out = in_1[7] ? n32b_shl_7_out_3 : 32'bz;  // Controlled_Buffer controlled_buffer_16
  _32b_shl u_32b_shl_8 (.in_1(n32b_shl_7_out_3), .out_2(n32b_shl_8_out_2), .out_3(n32b_shl_8_out_3));
  assign controlled_buffer_17_out = in_1[8] ? n32b_shl_8_out_3 : 32'bz;  // Controlled_Buffer controlled_buffer_17
  not not_9 (not_9_out, in_1[8]);
  assign controlled_buffer_17_out = not_9_out ? {32{1'b0}} : 32'bz;  // Controlled_Buffer controlled_buffer_18
  _32b_shl u_32b_shl_9 (.in_1(n32b_shl_8_out_3), .out_2(n32b_shl_9_out_2), .out_3(n32b_shl_9_out_3));
  not not_10 (not_10_out, in_1[9]);
  assign controlled_buffer_19_out = in_1[9] ? n32b_shl_9_out_3 : 32'bz;  // Controlled_Buffer controlled_buffer_19
  assign controlled_buffer_19_out = not_10_out ? {32{1'b0}} : 32'bz;  // Controlled_Buffer controlled_buffer_20
  _32b_shl u_32b_shl_10 (.in_1(n32b_shl_9_out_3), .out_2(n32b_shl_10_out_2), .out_3(n32b_shl_10_out_3));
  not not_11 (not_11_out, in_1[10]);
  assign controlled_buffer_21_out = in_1[10] ? n32b_shl_10_out_3 : 32'bz;  // Controlled_Buffer controlled_buffer_21
  _32b_shl u_32b_shl_11 (.in_1(n32b_shl_10_out_3), .out_2(n32b_shl_11_out_2), .out_3(n32b_shl_11_out_3));
  assign controlled_buffer_21_out = not_11_out ? {32{1'b0}} : 32'bz;  // Controlled_Buffer controlled_buffer_22
  not not_12 (not_12_out, in_1[11]);
  assign controlled_buffer_23_out = not_12_out ? {32{1'b0}} : 32'bz;  // Controlled_Buffer controlled_buffer_23
  assign controlled_buffer_23_out = in_1[11] ? n32b_shl_11_out_3 : 32'bz;  // Controlled_Buffer controlled_buffer_24
  _32b_shl u_32b_shl_12 (.in_1(n32b_shl_11_out_3), .out_2(n32b_shl_12_out_2), .out_3(n32b_shl_12_out_3));
  not not_13 (not_13_out, in_1[12]);
  assign controlled_buffer_25_out = not_13_out ? {32{1'b0}} : 32'bz;  // Controlled_Buffer controlled_buffer_25
  assign controlled_buffer_25_out = in_1[12] ? n32b_shl_12_out_3 : 32'bz;  // Controlled_Buffer controlled_buffer_26
  _32b_shl u_32b_shl_13 (.in_1(n32b_shl_12_out_3), .out_2(n32b_shl_13_out_2), .out_3(n32b_shl_13_out_3));
  assign controlled_buffer_27_out = in_1[13] ? n32b_shl_13_out_3 : 32'bz;  // Controlled_Buffer controlled_buffer_27
  not not_14 (not_14_out, in_1[13]);
  assign controlled_buffer_27_out = not_14_out ? {32{1'b0}} : 32'bz;  // Controlled_Buffer controlled_buffer_28
  _32b_shl u_32b_shl_14 (.in_1(n32b_shl_13_out_3), .out_2(n32b_shl_14_out_2), .out_3(n32b_shl_14_out_3));
  not not_15 (not_15_out, in_1[14]);
  assign controlled_buffer_29_out = not_15_out ? {32{1'b0}} : 32'bz;  // Controlled_Buffer controlled_buffer_29
  assign controlled_buffer_29_out = in_1[14] ? n32b_shl_14_out_3 : 32'bz;  // Controlled_Buffer controlled_buffer_30
  _32b_shl u_32b_shl_15 (.in_1(n32b_shl_14_out_3), .out_2(n32b_shl_15_out_2), .out_3(n32b_shl_15_out_3));
  not not_16 (not_16_out, in_1[15]);
  assign controlled_buffer_31_out = in_1[15] ? n32b_shl_15_out_3 : 32'bz;  // Controlled_Buffer controlled_buffer_31
  _32b_shl u_32b_shl_16 (.in_1(n32b_shl_15_out_3), .out_2(n32b_shl_16_out_2), .out_3(n32b_shl_16_out_3));
  assign controlled_buffer_31_out = not_16_out ? {32{1'b0}} : 32'bz;  // Controlled_Buffer controlled_buffer_32
  assign controlled_buffer_33_out = in_1[16] ? n32b_shl_16_out_3 : 32'bz;  // Controlled_Buffer controlled_buffer_33
  not not_17 (not_17_out, in_1[16]);
  assign controlled_buffer_33_out = not_17_out ? {32{1'b0}} : 32'bz;  // Controlled_Buffer controlled_buffer_34
  _32b_shl u_32b_shl_17 (.in_1(n32b_shl_16_out_3), .out_2(n32b_shl_17_out_2), .out_3(n32b_shl_17_out_3));
  not not_18 (not_18_out, in_1[17]);
  assign controlled_buffer_35_out = in_1[17] ? n32b_shl_17_out_3 : 32'bz;  // Controlled_Buffer controlled_buffer_35
  assign controlled_buffer_35_out = not_18_out ? {32{1'b0}} : 32'bz;  // Controlled_Buffer controlled_buffer_36
  _32b_shl u_32b_shl_18 (.in_1(n32b_shl_17_out_3), .out_2(n32b_shl_18_out_2), .out_3(n32b_shl_18_out_3));
  assign controlled_buffer_37_out = in_1[18] ? n32b_shl_18_out_3 : 32'bz;  // Controlled_Buffer controlled_buffer_37
  _32b_shl u_32b_shl_19 (.in_1(n32b_shl_18_out_3), .out_2(n32b_shl_19_out_2), .out_3(n32b_shl_19_out_3));
  not not_19 (not_19_out, in_1[18]);
  assign controlled_buffer_37_out = not_19_out ? {32{1'b0}} : 32'bz;  // Controlled_Buffer controlled_buffer_38
  not not_20 (not_20_out, in_1[19]);
  assign controlled_buffer_39_out = in_1[19] ? n32b_shl_19_out_3 : 32'bz;  // Controlled_Buffer controlled_buffer_39
  assign controlled_buffer_39_out = not_20_out ? {32{1'b0}} : 32'bz;  // Controlled_Buffer controlled_buffer_40
  _32b_shl u_32b_shl_20 (.in_1(n32b_shl_19_out_3), .out_2(n32b_shl_20_out_2), .out_3(n32b_shl_20_out_3));
  not not_21 (not_21_out, in_1[20]);
  assign controlled_buffer_41_out = in_1[20] ? n32b_shl_20_out_3 : 32'bz;  // Controlled_Buffer controlled_buffer_41
  _32b_shl u_32b_shl_21 (.in_1(n32b_shl_20_out_3), .out_2(n32b_shl_21_out_2), .out_3(n32b_shl_21_out_3));
  assign controlled_buffer_41_out = not_21_out ? {32{1'b0}} : 32'bz;  // Controlled_Buffer controlled_buffer_42
  not not_22 (not_22_out, in_1[21]);
  assign controlled_buffer_43_out = in_1[21] ? n32b_shl_21_out_3 : 32'bz;  // Controlled_Buffer controlled_buffer_43
  assign controlled_buffer_43_out = not_22_out ? {32{1'b0}} : 32'bz;  // Controlled_Buffer controlled_buffer_44
  _32b_shl u_32b_shl_22 (.in_1(n32b_shl_21_out_3), .out_2(n32b_shl_22_out_2), .out_3(n32b_shl_22_out_3));
  not not_23 (not_23_out, in_1[22]);
  assign controlled_buffer_45_out = not_23_out ? {32{1'b0}} : 32'bz;  // Controlled_Buffer controlled_buffer_45
  assign controlled_buffer_45_out = in_1[22] ? n32b_shl_22_out_3 : 32'bz;  // Controlled_Buffer controlled_buffer_46
  _32b_shl u_32b_shl_23 (.in_1(n32b_shl_22_out_3), .out_2(n32b_shl_23_out_2), .out_3(n32b_shl_23_out_3));
  assign controlled_buffer_47_out = in_1[23] ? n32b_shl_23_out_3 : 32'bz;  // Controlled_Buffer controlled_buffer_47
  not not_24 (not_24_out, in_1[23]);
  assign controlled_buffer_47_out = not_24_out ? {32{1'b0}} : 32'bz;  // Controlled_Buffer controlled_buffer_48
  _32b_shl u_32b_shl_24 (.in_1(n32b_shl_23_out_3), .out_2(n32b_shl_24_out_2), .out_3(n32b_shl_24_out_3));
  not not_25 (not_25_out, in_1[24]);
  assign controlled_buffer_49_out = not_25_out ? {32{1'b0}} : 32'bz;  // Controlled_Buffer controlled_buffer_49
  assign controlled_buffer_49_out = in_1[24] ? n32b_shl_24_out_3 : 32'bz;  // Controlled_Buffer controlled_buffer_50
  _32b_shl u_32b_shl_25 (.in_1(n32b_shl_24_out_3), .out_2(n32b_shl_25_out_2), .out_3(n32b_shl_25_out_3));
  not not_26 (not_26_out, in_1[25]);
  assign controlled_buffer_51_out = in_1[25] ? n32b_shl_25_out_3 : 32'bz;  // Controlled_Buffer controlled_buffer_51
  _32b_shl u_32b_shl_26 (.in_1(n32b_shl_25_out_3), .out_2(n32b_shl_26_out_2), .out_3(n32b_shl_26_out_3));
  assign controlled_buffer_51_out = not_26_out ? {32{1'b0}} : 32'bz;  // Controlled_Buffer controlled_buffer_52
  not not_27 (not_27_out, in_1[26]);
  assign controlled_buffer_53_out = not_27_out ? {32{1'b0}} : 32'bz;  // Controlled_Buffer controlled_buffer_53
  assign controlled_buffer_53_out = in_1[26] ? n32b_shl_26_out_3 : 32'bz;  // Controlled_Buffer controlled_buffer_54
  _32b_shl u_32b_shl_27 (.in_1(n32b_shl_26_out_3), .out_2(n32b_shl_27_out_2), .out_3(n32b_shl_27_out_3));
  not not_28 (not_28_out, in_1[27]);
  assign controlled_buffer_55_out = in_1[27] ? n32b_shl_27_out_3 : 32'bz;  // Controlled_Buffer controlled_buffer_55
  assign controlled_buffer_55_out = not_28_out ? {32{1'b0}} : 32'bz;  // Controlled_Buffer controlled_buffer_56
  _32b_shl u_32b_shl_28 (.in_1(n32b_shl_27_out_3), .out_2(n32b_shl_28_out_2), .out_3(n32b_shl_28_out_3));
  assign controlled_buffer_57_out = in_1[28] ? n32b_shl_28_out_3 : 32'bz;  // Controlled_Buffer controlled_buffer_57
  not not_29 (not_29_out, in_1[28]);
  assign controlled_buffer_57_out = not_29_out ? {32{1'b0}} : 32'bz;  // Controlled_Buffer controlled_buffer_58
  _32b_shl u_32b_shl_29 (.in_1(n32b_shl_28_out_3), .out_2(n32b_shl_29_out_2), .out_3(n32b_shl_29_out_3));
  not not_30 (not_30_out, in_1[29]);
  assign controlled_buffer_59_out = in_1[29] ? n32b_shl_29_out_3 : 32'bz;  // Controlled_Buffer controlled_buffer_59
  assign controlled_buffer_59_out = not_30_out ? {32{1'b0}} : 32'bz;  // Controlled_Buffer controlled_buffer_60
  _32b_shl u_32b_shl_30 (.in_1(n32b_shl_29_out_3), .out_2(n32b_shl_30_out_2), .out_3(n32b_shl_30_out_3));
  not not_31 (not_31_out, in_1[30]);
  assign controlled_buffer_61_out = in_1[30] ? n32b_shl_30_out_3 : 32'bz;  // Controlled_Buffer controlled_buffer_61
  _32b_shl u_32b_shl_31 (.in_1(n32b_shl_30_out_3), .out_2(n32b_shl_31_out_2), .out_3(n32b_shl_31_out_3));
  assign controlled_buffer_61_out = not_31_out ? {32{1'b0}} : 32'bz;  // Controlled_Buffer controlled_buffer_62
  not not_32 (not_32_out, in_1[31]);
  assign controlled_buffer_63_out = not_32_out ? {32{1'b0}} : 32'bz;  // Controlled_Buffer controlled_buffer_63
  assign controlled_buffer_63_out = in_1[31] ? n32b_shl_31_out_3 : 32'bz;  // Controlled_Buffer controlled_buffer_64
  _32bit_add_sub u_32bit_add_sub_1 (
    .in_1(controlled_buffer_1_out), .in_2(controlled_buffer_3_out), .in_3(1'b0),
    .out_4(n32bit_add_sub_1_out_4), .out_5(n32bit_add_sub_1_out_5));
  _32bit_add_sub u_32bit_add_sub_2 (
    .in_1(controlled_buffer_9_out), .in_2(controlled_buffer_11_out), .in_3(1'b0),
    .out_4(n32bit_add_sub_2_out_4), .out_5(n32bit_add_sub_2_out_5));
  _32bit_add_sub u_32bit_add_sub_3 (
    .in_1(controlled_buffer_17_out), .in_2(controlled_buffer_19_out), .in_3(1'b0),
    .out_4(n32bit_add_sub_3_out_4), .out_5(n32bit_add_sub_3_out_5));
  _32bit_add_sub u_32bit_add_sub_4 (
    .in_1(controlled_buffer_25_out), .in_2(controlled_buffer_27_out), .in_3(1'b0),
    .out_4(n32bit_add_sub_4_out_4), .out_5(n32bit_add_sub_4_out_5));
  _32bit_add_sub u_32bit_add_sub_5 (
    .in_1(controlled_buffer_33_out), .in_2(controlled_buffer_35_out), .in_3(1'b0),
    .out_4(n32bit_add_sub_5_out_4), .out_5(n32bit_add_sub_5_out_5));
  _32bit_add_sub u_32bit_add_sub_6 (
    .in_1(controlled_buffer_41_out), .in_2(controlled_buffer_43_out), .in_3(1'b0),
    .out_4(n32bit_add_sub_6_out_4), .out_5(n32bit_add_sub_6_out_5));
  _32bit_add_sub u_32bit_add_sub_7 (
    .in_1(controlled_buffer_49_out), .in_2(controlled_buffer_51_out), .in_3(1'b0),
    .out_4(n32bit_add_sub_7_out_4), .out_5(n32bit_add_sub_7_out_5));
  _32bit_add_sub u_32bit_add_sub_8 (
    .in_1(controlled_buffer_57_out), .in_2(controlled_buffer_59_out), .in_3(1'b0),
    .out_4(n32bit_add_sub_8_out_4), .out_5(n32bit_add_sub_8_out_5));
  _32bit_add_sub u_32bit_add_sub_9 (
    .in_1(controlled_buffer_5_out), .in_2(controlled_buffer_7_out), .in_3(1'b0),
    .out_4(n32bit_add_sub_9_out_4), .out_5(n32bit_add_sub_9_out_5));
  _32bit_add_sub u_32bit_add_sub_10 (
    .in_1(controlled_buffer_13_out), .in_2(controlled_buffer_15_out), .in_3(1'b0),
    .out_4(n32bit_add_sub_10_out_4), .out_5(n32bit_add_sub_10_out_5));
  _32bit_add_sub u_32bit_add_sub_11 (
    .in_1(controlled_buffer_21_out), .in_2(controlled_buffer_23_out), .in_3(1'b0),
    .out_4(n32bit_add_sub_11_out_4), .out_5(n32bit_add_sub_11_out_5));
  _32bit_add_sub u_32bit_add_sub_12 (
    .in_1(controlled_buffer_29_out), .in_2(controlled_buffer_31_out), .in_3(1'b0),
    .out_4(n32bit_add_sub_12_out_4), .out_5(n32bit_add_sub_12_out_5));
  _32bit_add_sub u_32bit_add_sub_13 (
    .in_1(controlled_buffer_37_out), .in_2(controlled_buffer_39_out), .in_3(1'b0),
    .out_4(n32bit_add_sub_13_out_4), .out_5(n32bit_add_sub_13_out_5));
  _32bit_add_sub u_32bit_add_sub_14 (
    .in_1(controlled_buffer_45_out), .in_2(controlled_buffer_47_out), .in_3(1'b0),
    .out_4(n32bit_add_sub_14_out_4), .out_5(n32bit_add_sub_14_out_5));
  _32bit_add_sub u_32bit_add_sub_15 (
    .in_1(controlled_buffer_53_out), .in_2(controlled_buffer_55_out), .in_3(1'b0),
    .out_4(n32bit_add_sub_15_out_4), .out_5(n32bit_add_sub_15_out_5));
  _32bit_add_sub u_32bit_add_sub_16 (
    .in_1(controlled_buffer_61_out), .in_2(controlled_buffer_63_out), .in_3(1'b0),
    .out_4(n32bit_add_sub_16_out_4), .out_5(n32bit_add_sub_16_out_5));
  or or_1 (or_1_out, n32bit_add_sub_16_out_4, n32bit_add_sub_8_out_4, n32bit_add_sub_15_out_4, n32bit_add_sub_7_out_4, n32bit_add_sub_14_out_4, n32bit_add_sub_6_out_4, n32bit_add_sub_13_out_4, n32bit_add_sub_5_out_4, n32bit_add_sub_12_out_4, n32bit_add_sub_4_out_4, n32bit_add_sub_11_out_4, n32bit_add_sub_3_out_4, n32bit_add_sub_10_out_4, n32bit_add_sub_2_out_4, n32bit_add_sub_9_out_4, n32bit_add_sub_1_out_4);
  // OR_Gate or_2 is placed but not wired
  _32bit_add_sub u_32bit_add_sub_17 (
    .in_1(n32bit_add_sub_1_out_5), .in_2(n32bit_add_sub_9_out_5), .in_3(1'b0),
    .out_4(n32bit_add_sub_17_out_4), .out_5(n32bit_add_sub_17_out_5));
  _32bit_add_sub u_32bit_add_sub_18 (
    .in_1(n32bit_add_sub_2_out_5), .in_2(n32bit_add_sub_10_out_5), .in_3(1'b0),
    .out_4(n32bit_add_sub_18_out_4), .out_5(n32bit_add_sub_18_out_5));
  _32bit_add_sub u_32bit_add_sub_19 (
    .in_1(n32bit_add_sub_3_out_5), .in_2(n32bit_add_sub_11_out_5), .in_3(1'b0),
    .out_4(n32bit_add_sub_19_out_4), .out_5(n32bit_add_sub_19_out_5));
  _32bit_add_sub u_32bit_add_sub_20 (
    .in_1(n32bit_add_sub_4_out_5), .in_2(n32bit_add_sub_12_out_5), .in_3(1'b0),
    .out_4(n32bit_add_sub_20_out_4), .out_5(n32bit_add_sub_20_out_5));
  _32bit_add_sub u_32bit_add_sub_21 (
    .in_1(n32bit_add_sub_5_out_5), .in_2(n32bit_add_sub_13_out_5), .in_3(1'b0),
    .out_4(n32bit_add_sub_21_out_4), .out_5(n32bit_add_sub_21_out_5));
  _32bit_add_sub u_32bit_add_sub_22 (
    .in_1(n32bit_add_sub_6_out_5), .in_2(n32bit_add_sub_14_out_5), .in_3(1'b0),
    .out_4(n32bit_add_sub_22_out_4), .out_5(n32bit_add_sub_22_out_5));
  _32bit_add_sub u_32bit_add_sub_23 (
    .in_1(n32bit_add_sub_7_out_5), .in_2(n32bit_add_sub_15_out_5), .in_3(1'b0),
    .out_4(n32bit_add_sub_23_out_4), .out_5(n32bit_add_sub_23_out_5));
  _32bit_add_sub u_32bit_add_sub_24 (
    .in_1(n32bit_add_sub_8_out_5), .in_2(n32bit_add_sub_16_out_5), .in_3(1'b0),
    .out_4(n32bit_add_sub_24_out_4), .out_5(n32bit_add_sub_24_out_5));
  or or_3 (or_3_out, n32bit_add_sub_17_out_4, n32bit_add_sub_18_out_4, n32bit_add_sub_19_out_4, n32bit_add_sub_20_out_4, n32bit_add_sub_22_out_4, n32bit_add_sub_23_out_4, n32bit_add_sub_24_out_4, n32bit_add_sub_21_out_4);
  _32bit_add_sub u_32bit_add_sub_25 (
    .in_1(n32bit_add_sub_23_out_5), .in_2(n32bit_add_sub_24_out_5), .in_3(1'b0),
    .out_4(n32bit_add_sub_25_out_4), .out_5(n32bit_add_sub_25_out_5));
  _32bit_add_sub u_32bit_add_sub_26 (
    .in_1(n32bit_add_sub_17_out_5), .in_2(n32bit_add_sub_18_out_5), .in_3(1'b0),
    .out_4(n32bit_add_sub_26_out_4), .out_5(n32bit_add_sub_26_out_5));
  _32bit_add_sub u_32bit_add_sub_27 (
    .in_1(n32bit_add_sub_19_out_5), .in_2(n32bit_add_sub_20_out_5), .in_3(1'b0),
    .out_4(n32bit_add_sub_27_out_4), .out_5(n32bit_add_sub_27_out_5));
  _32bit_add_sub u_32bit_add_sub_28 (
    .in_1(n32bit_add_sub_21_out_5), .in_2(n32bit_add_sub_22_out_5), .in_3(1'b0),
    .out_4(n32bit_add_sub_28_out_4), .out_5(n32bit_add_sub_28_out_5));
  or or_4 (or_4_out, n32bit_add_sub_26_out_4, n32bit_add_sub_27_out_4, n32bit_add_sub_28_out_4, n32bit_add_sub_25_out_4);
  _32bit_add_sub u_32bit_add_sub_29 (
    .in_1(n32bit_add_sub_26_out_5), .in_2(n32bit_add_sub_27_out_5), .in_3(1'b0),
    .out_4(n32bit_add_sub_29_out_4), .out_5(n32bit_add_sub_29_out_5));
  _32bit_add_sub u_32bit_add_sub_30 (
    .in_1(n32bit_add_sub_28_out_5), .in_2(n32bit_add_sub_25_out_5), .in_3(1'b0),
    .out_4(n32bit_add_sub_30_out_4), .out_5(n32bit_add_sub_30_out_5));
  or or_5 (or_5_out, n32bit_add_sub_29_out_4, n32bit_add_sub_30_out_4);
  _32bit_add_sub u_32bit_add_sub_31 (
    .in_1(n32bit_add_sub_29_out_5), .in_2(n32bit_add_sub_30_out_5), .in_3(1'b0),
    .out_4(n32bit_add_sub_31_out_4), .out_5(out_3));
  or or_6 (out_4, n32bit_add_sub_31_out_4, or_5_out, or_4_out, or_3_out, or_1_out, undriven);
endmodule
module _32bit_main_cpu (
  input  in_1,
  input  in_2,
  input  in_3,
  output [31:0] out_4,
  output [15:0] out_5
);

  wire alu32_1_out_11, alu32_1_out_13, alu32_1_out_14, alu32_1_out_15, alu32_1_out_16, and_1_out, and_2_out,
       and_3_out, and_4_out, and_5_out, and_6_out, and_7_out, and_8_out, and_9_out, and_10_out, and_11_out,
       and_12_out, and_13_out, and_14_out, and_15_out, and_16_out, and_17_out, and_18_out, and_19_out,
       and_20_out, and_21_out, and_22_out, and_23_out, and_24_out, and_25_out, and_26_out, and_27_out,
       and_28_out, and_29_out, and_30_out, and_31_out, and_32_out, and_33_out, and_34_out, and_35_out,
       and_36_out, and_37_out, and_38_out, and_39_out, and_40_out, and_41_out, and_42_out, and_43_out,
       and_44_out, and_45_out, and_46_out, and_47_out, and_48_out, and_49_out, and_50_out, and_51_out,
       and_52_out, and_53_out, and_54_out, and_55_out, and_56_out, and_57_out, and_58_out, and_59_out,
       and_60_out, and_61_out, and_62_out, and_63_out, and_64_out, and_65_out, and_66_out, and_67_out,
       and_68_out, and_69_out, and_70_out, and_71_out, and_72_out, and_73_out, and_74_out, and_75_out,
       and_76_out, and_77_out, and_78_out, and_79_out, and_80_out, and_81_out, and_82_out, and_83_out,
       and_84_out, and_85_out, and_86_out, and_87_out, and_88_out, and_89_out, and_90_out, and_91_out,
       and_92_out, and_93_out, and_94_out, and_95_out, and_96_out, and_97_out, and_98_out, and_99_out,
       and_100_out, and_101_out, and_102_out, and_103_out, and_104_out, and_105_out, and_106_out,
       and_107_out, and_108_out, and_109_out, and_110_out, and_111_out, and_112_out, and_113_out,
       and_114_out, and_115_out, and_116_out, and_117_out, and_118_out, and_119_out, and_120_out,
       and_121_out, and_122_out, and_123_out, and_124_out, and_125_out, and_126_out, and_127_out,
       and_128_out, and_129_out, and_130_out, and_131_out, and_132_out, and_133_out, and_134_out,
       and_135_out, and_136_out, and_137_out, and_138_out, and_139_out, and_140_out, and_141_out,
       and_142_out, and_143_out, and_144_out, and_145_out, and_146_out, and_147_out, and_148_out,
       and_149_out, and_150_out, and_151_out, and_152_out, and_153_out, and_154_out, and_155_out,
       and_156_out, and_157_out, and_158_out, and_159_out, and_160_out, and_161_out, and_162_out,
       and_163_out, and_164_out, and_165_out, and_166_out, and_167_out, and_168_out, and_169_out,
       and_170_out, and_171_out, and_172_out, and_173_out, and_174_out, and_175_out, and_176_out,
       and_177_out, and_178_out, and_179_out, and_180_out, and_181_out, and_182_out, and_183_out,
       and_184_out, and_185_out, and_186_out, and_187_out, and_188_out, and_189_out, and_190_out,
       and_191_out, and_192_out, and_193_out, and_194_out, and_195_out, and_196_out, and_197_out,
       and_198_out, and_199_out, and_200_out, and_201_out, and_202_out, and_203_out, and_204_out,
       and_205_out, and_206_out, and_207_out, and_208_out, and_209_out, and_210_out, and_211_out,
       and_212_out, and_213_out, and_214_out, and_215_out, and_216_out, and_217_out, and_218_out,
       and_219_out, and_220_out, and_221_out, and_222_out, and_223_out, and_224_out, and_225_out,
       and_226_out, and_227_out, and_228_out, and_229_out, and_230_out, and_231_out, and_232_out,
       and_233_out, and_234_out, and_235_out, and_236_out, and_237_out, and_238_out, and_239_out,
       and_240_out, and_241_out, and_242_out, and_243_out, and_244_out, and_245_out, and_246_out,
       and_247_out, and_248_out, and_249_out, and_250_out, and_251_out, and_252_out, and_253_out,
       and_254_out, and_255_out, and_256_out, and_257_out, and_258_out, and_259_out, and_260_out,
       and_261_out, and_262_out, and_263_out, and_264_out, and_265_out, and_266_out, and_267_out,
       and_268_out, and_269_out, and_270_out, and_271_out, and_272_out, and_273_out, and_274_out,
       and_275_out, and_276_out, and_277_out, and_278_out, and_279_out, and_280_out, and_281_out,
       and_282_out, and_283_out, and_284_out, and_285_out, and_286_out, and_287_out, and_288_out,
       and_289_out, and_290_out, and_291_out, and_292_out, and_293_out, and_294_out, and_295_out,
       and_296_out, and_297_out, and_298_out, and_299_out, and_300_out, and_301_out, and_302_out,
       and_303_out, and_304_out, and_305_out, and_306_out, and_307_out, and_308_out, and_309_out,
       and_310_out, and_311_out, and_312_out, and_313_out, and_314_out, and_315_out, and_316_out,
       and_317_out, and_318_out, and_319_out, and_320_out, and_321_out, and_322_out, and_323_out,
       and_326_out, and_327_out, and_328_out, and_329_out, and_330_out, and_331_out, and_333_out,
       and_334_out, and_335_out, and_336_out, and_337_out, and_338_out, and_339_out, and_340_out,
       and_341_out, and_342_out, and_343_out, and_344_out, and_345_out, and_346_out, and_347_out,
       and_348_out, and_349_out, and_350_out, and_351_out, and_352_out, and_353_out, and_354_out,
       and_355_out, and_356_out, and_357_out, and_358_out, and_359_out, and_360_out, and_361_out,
       and_362_out, and_363_out, and_364_out, and_365_out, and_366_out, and_367_out, and_368_out,
       and_369_out, and_370_out, and_371_out, and_372_out, and_373_out, and_374_out, and_375_out,
       and_376_out, and_377_out, and_378_out, and_379_out, and_380_out, and_381_out, and_382_out,
       and_383_out, and_384_out, and_385_out, and_386_out, and_387_out, and_388_out, and_389_out,
       and_390_out, and_391_out, and_392_out, and_393_out, and_394_out, and_395_out, and_396_out,
       and_397_out, and_398_out, and_399_out, and_400_out, and_401_out, and_402_out, and_403_out,
       and_404_out, and_405_out, and_406_out, and_407_out, and_408_out, and_409_out, and_410_out,
       and_411_out, and_412_out, and_413_out, and_414_out, and_415_out, and_416_out, and_417_out,
       and_418_out, and_419_out, and_420_out, and_421_out, and_422_out, and_423_out, and_424_out,
       and_425_out, and_426_out, and_427_out, and_428_out, and_429_out, and_430_out, and_431_out,
       and_432_out, and_433_out, and_434_out, and_435_out, and_436_out, and_437_out, and_438_out,
       and_439_out, and_440_out, and_441_out, and_442_out, and_443_out, and_444_out, and_445_out,
       and_446_out, and_447_out, and_448_out, and_449_out, clock_1_out, controlled_buffer_133_out, d_ff_1_q,
       d_ff_2_q, demultiplexer_1_out0, demultiplexer_1_out1, demultiplexer_1_out2, demultiplexer_1_out3,
       demultiplexer_1_out4, demultiplexer_1_out5, demultiplexer_1_out6, demultiplexer_1_out7, not_1_out,
       not_2_out, not_3_out, not_4_out, not_5_out, or_1_out, or_2_out, xor_1_out, xor_4_out;
  wire [1:0] controlled_buffer_1_out_6;
  wire [2:0] controlled_buffer_1_out_4;
  wire [3:0] controlled_buffer_1_out_2, controlled_buffer_1_out_3;
  wire [4:0] and_324_out, controlled_buffer_1_out_5, zf_q;
  wire [15:0] controlled_buffer_132_out, multiplexer_3_out, register_7_q, register_8_q;
  wire [29:0] controlled_buffer_1_out, undriven;
  wire [31:0] alu32_1_out_12, controlled_buffer_73_out, controlled_buffer_131_out, controlled_buffer_138_out,
       controlled_buffer_139_out, controlled_buffer_140_out, multiplexer_1_out, multiplexer_2_out,
       ram_1_data, register_1_q, register_2_q, register_3_q, register_4_q, register_5_q, register_6_q,
       register_9_q;

  assign {controlled_buffer_1_out_6, controlled_buffer_1_out[29:24], controlled_buffer_1_out_5, controlled_buffer_1_out_4, controlled_buffer_1_out_3, controlled_buffer_1_out_2, controlled_buffer_1_out[7:0]} = and_82_out ? 32'h1015410 : 32'bz;  // Controlled_Buffer controlled_buffer_1
  assign {controlled_buffer_1_out_6, controlled_buffer_1_out[29:24], controlled_buffer_1_out_5, controlled_buffer_1_out_4, controlled_buffer_1_out_3, controlled_buffer_1_out_2, controlled_buffer_1_out[7:0]} = and_100_out ? 32'h1000001 : 32'bz;  // Controlled_Buffer controlled_buffer_2
  assign {controlled_buffer_1_out_6, controlled_buffer_1_out[29:24], controlled_buffer_1_out_5, controlled_buffer_1_out_4, controlled_buffer_1_out_3, controlled_buffer_1_out_2, controlled_buffer_1_out[7:0]} = and_102_out ? 32'h1001001 : 32'bz;  // Controlled_Buffer controlled_buffer_3
  assign {controlled_buffer_1_out_6, controlled_buffer_1_out[29:24], controlled_buffer_1_out_5, controlled_buffer_1_out_4, controlled_buffer_1_out_3, controlled_buffer_1_out_2, controlled_buffer_1_out[7:0]} = and_15_out ? 32'h1013001 : 32'bz;  // Controlled_Buffer controlled_buffer_4
  assign {controlled_buffer_1_out_6, controlled_buffer_1_out[29:24], controlled_buffer_1_out_5, controlled_buffer_1_out_4, controlled_buffer_1_out_3, controlled_buffer_1_out_2, controlled_buffer_1_out[7:0]} = and_16_out ? 32'h1003001 : 32'bz;  // Controlled_Buffer controlled_buffer_5
  assign {controlled_buffer_1_out_6, controlled_buffer_1_out[29:24], controlled_buffer_1_out_5, controlled_buffer_1_out_4, controlled_buffer_1_out_3, controlled_buffer_1_out_2, controlled_buffer_1_out[7:0]} = and_17_out ? 32'h1014001 : 32'bz;  // Controlled_Buffer controlled_buffer_6
  assign {controlled_buffer_1_out_6, controlled_buffer_1_out[29:24], controlled_buffer_1_out_5, controlled_buffer_1_out_4, controlled_buffer_1_out_3, controlled_buffer_1_out_2, controlled_buffer_1_out[7:0]} = and_19_out ? 32'h1015001 : 32'bz;  // Controlled_Buffer controlled_buffer_7
  assign {controlled_buffer_1_out_6, controlled_buffer_1_out[29:24], controlled_buffer_1_out_5, controlled_buffer_1_out_4, controlled_buffer_1_out_3, controlled_buffer_1_out_2, controlled_buffer_1_out[7:0]} = and_23_out ? 32'h1000102 : 32'bz;  // Controlled_Buffer controlled_buffer_8
  assign {controlled_buffer_1_out_6, controlled_buffer_1_out[29:24], controlled_buffer_1_out_5, controlled_buffer_1_out_4, controlled_buffer_1_out_3, controlled_buffer_1_out_2, controlled_buffer_1_out[7:0]} = and_26_out ? 32'h1001102 : 32'bz;  // Controlled_Buffer controlled_buffer_9
  assign {controlled_buffer_1_out_6, controlled_buffer_1_out[29:24], controlled_buffer_1_out_5, controlled_buffer_1_out_4, controlled_buffer_1_out_3, controlled_buffer_1_out_2, controlled_buffer_1_out[7:0]} = and_29_out ? 32'h1002102 : 32'bz;  // Controlled_Buffer controlled_buffer_10
  assign {controlled_buffer_1_out_6, controlled_buffer_1_out[29:24], controlled_buffer_1_out_5, controlled_buffer_1_out_4, controlled_buffer_1_out_3, controlled_buffer_1_out_2, controlled_buffer_1_out[7:0]} = and_31_out ? 32'h1003102 : 32'bz;  // Controlled_Buffer controlled_buffer_11
  assign {controlled_buffer_1_out_6, controlled_buffer_1_out[29:24], controlled_buffer_1_out_5, controlled_buffer_1_out_4, controlled_buffer_1_out_3, controlled_buffer_1_out_2, controlled_buffer_1_out[7:0]} = and_34_out ? 32'h1004102 : 32'bz;  // Controlled_Buffer controlled_buffer_12
  assign {controlled_buffer_1_out_6, controlled_buffer_1_out[29:24], controlled_buffer_1_out_5, controlled_buffer_1_out_4, controlled_buffer_1_out_3, controlled_buffer_1_out_2, controlled_buffer_1_out[7:0]} = and_37_out ? 32'h1005102 : 32'bz;  // Controlled_Buffer controlled_buffer_13
  assign {controlled_buffer_1_out_6, controlled_buffer_1_out[29:24], controlled_buffer_1_out_5, controlled_buffer_1_out_4, controlled_buffer_1_out_3, controlled_buffer_1_out_2, controlled_buffer_1_out[7:0]} = and_40_out ? 32'h1000204 : 32'bz;  // Controlled_Buffer controlled_buffer_14
  assign {controlled_buffer_1_out_6, controlled_buffer_1_out[29:24], controlled_buffer_1_out_5, controlled_buffer_1_out_4, controlled_buffer_1_out_3, controlled_buffer_1_out_2, controlled_buffer_1_out[7:0]} = and_43_out ? 32'h1001204 : 32'bz;  // Controlled_Buffer controlled_buffer_15
  assign {controlled_buffer_1_out_6, controlled_buffer_1_out[29:24], controlled_buffer_1_out_5, controlled_buffer_1_out_4, controlled_buffer_1_out_3, controlled_buffer_1_out_2, controlled_buffer_1_out[7:0]} = and_46_out ? 32'h1002204 : 32'bz;  // Controlled_Buffer controlled_buffer_16
  assign {controlled_buffer_1_out_6, controlled_buffer_1_out[29:24], controlled_buffer_1_out_5, controlled_buffer_1_out_4, controlled_buffer_1_out_3, controlled_buffer_1_out_2, controlled_buffer_1_out[7:0]} = and_2_out ? 32'h1013204 : 32'bz;  // Controlled_Buffer controlled_buffer_17
  assign {controlled_buffer_1_out_6, controlled_buffer_1_out[29:24], controlled_buffer_1_out_5, controlled_buffer_1_out_4, controlled_buffer_1_out_3, controlled_buffer_1_out_2, controlled_buffer_1_out[7:0]} = and_48_out ? 32'h1003204 : 32'bz;  // Controlled_Buffer controlled_buffer_18
  assign {controlled_buffer_1_out_6, controlled_buffer_1_out[29:24], controlled_buffer_1_out_5, controlled_buffer_1_out_4, controlled_buffer_1_out_3, controlled_buffer_1_out_2, controlled_buffer_1_out[7:0]} = and_3_out ? 32'h1014204 : 32'bz;  // Controlled_Buffer controlled_buffer_19
  assign {controlled_buffer_1_out_6, controlled_buffer_1_out[29:24], controlled_buffer_1_out_5, controlled_buffer_1_out_4, controlled_buffer_1_out_3, controlled_buffer_1_out_2, controlled_buffer_1_out[7:0]} = and_50_out ? 32'h1004204 : 32'bz;  // Controlled_Buffer controlled_buffer_20
  assign {controlled_buffer_1_out_6, controlled_buffer_1_out[29:24], controlled_buffer_1_out_5, controlled_buffer_1_out_4, controlled_buffer_1_out_3, controlled_buffer_1_out_2, controlled_buffer_1_out[7:0]} = and_4_out ? 32'h1015204 : 32'bz;  // Controlled_Buffer controlled_buffer_21
  assign {controlled_buffer_1_out_6, controlled_buffer_1_out[29:24], controlled_buffer_1_out_5, controlled_buffer_1_out_4, controlled_buffer_1_out_3, controlled_buffer_1_out_2, controlled_buffer_1_out[7:0]} = and_52_out ? 32'h1005204 : 32'bz;  // Controlled_Buffer controlled_buffer_22
  assign {controlled_buffer_1_out_6, controlled_buffer_1_out[29:24], controlled_buffer_1_out_5, controlled_buffer_1_out_4, controlled_buffer_1_out_3, controlled_buffer_1_out_2, controlled_buffer_1_out[7:0]} = and_5_out ? 32'h1010308 : 32'bz;  // Controlled_Buffer controlled_buffer_23
  assign {controlled_buffer_1_out_6, controlled_buffer_1_out[29:24], controlled_buffer_1_out_5, controlled_buffer_1_out_4, controlled_buffer_1_out_3, controlled_buffer_1_out_2, controlled_buffer_1_out[7:0]} = and_54_out ? 32'h1000308 : 32'bz;  // Controlled_Buffer controlled_buffer_24
  assign {controlled_buffer_1_out_6, controlled_buffer_1_out[29:24], controlled_buffer_1_out_5, controlled_buffer_1_out_4, controlled_buffer_1_out_3, controlled_buffer_1_out_2, controlled_buffer_1_out[7:0]} = and_6_out ? 32'h1011308 : 32'bz;  // Controlled_Buffer controlled_buffer_25
  assign {controlled_buffer_1_out_6, controlled_buffer_1_out[29:24], controlled_buffer_1_out_5, controlled_buffer_1_out_4, controlled_buffer_1_out_3, controlled_buffer_1_out_2, controlled_buffer_1_out[7:0]} = and_56_out ? 32'h1001308 : 32'bz;  // Controlled_Buffer controlled_buffer_26
  assign {controlled_buffer_1_out_6, controlled_buffer_1_out[29:24], controlled_buffer_1_out_5, controlled_buffer_1_out_4, controlled_buffer_1_out_3, controlled_buffer_1_out_2, controlled_buffer_1_out[7:0]} = and_59_out ? 32'h1002308 : 32'bz;  // Controlled_Buffer controlled_buffer_27
  assign {controlled_buffer_1_out_6, controlled_buffer_1_out[29:24], controlled_buffer_1_out_5, controlled_buffer_1_out_4, controlled_buffer_1_out_3, controlled_buffer_1_out_2, controlled_buffer_1_out[7:0]} = and_62_out ? 32'h1003308 : 32'bz;  // Controlled_Buffer controlled_buffer_28
  assign {controlled_buffer_1_out_6, controlled_buffer_1_out[29:24], controlled_buffer_1_out_5, controlled_buffer_1_out_4, controlled_buffer_1_out_3, controlled_buffer_1_out_2, controlled_buffer_1_out[7:0]} = and_7_out ? 32'h1014308 : 32'bz;  // Controlled_Buffer controlled_buffer_29
  assign {controlled_buffer_1_out_6, controlled_buffer_1_out[29:24], controlled_buffer_1_out_5, controlled_buffer_1_out_4, controlled_buffer_1_out_3, controlled_buffer_1_out_2, controlled_buffer_1_out[7:0]} = and_64_out ? 32'h1004308 : 32'bz;  // Controlled_Buffer controlled_buffer_30
  assign {controlled_buffer_1_out_6, controlled_buffer_1_out[29:24], controlled_buffer_1_out_5, controlled_buffer_1_out_4, controlled_buffer_1_out_3, controlled_buffer_1_out_2, controlled_buffer_1_out[7:0]} = and_67_out ? 32'h1005308 : 32'bz;  // Controlled_Buffer controlled_buffer_31
  assign {controlled_buffer_1_out_6, controlled_buffer_1_out[29:24], controlled_buffer_1_out_5, controlled_buffer_1_out_4, controlled_buffer_1_out_3, controlled_buffer_1_out_2, controlled_buffer_1_out[7:0]} = and_70_out ? 32'h1000410 : 32'bz;  // Controlled_Buffer controlled_buffer_32
  assign {controlled_buffer_1_out_6, controlled_buffer_1_out[29:24], controlled_buffer_1_out_5, controlled_buffer_1_out_4, controlled_buffer_1_out_3, controlled_buffer_1_out_2, controlled_buffer_1_out[7:0]} = and_8_out ? 32'h1011410 : 32'bz;  // Controlled_Buffer controlled_buffer_33
  assign {controlled_buffer_1_out_6, controlled_buffer_1_out[29:24], controlled_buffer_1_out_5, controlled_buffer_1_out_4, controlled_buffer_1_out_3, controlled_buffer_1_out_2, controlled_buffer_1_out[7:0]} = and_72_out ? 32'h1001410 : 32'bz;  // Controlled_Buffer controlled_buffer_34
  assign {controlled_buffer_1_out_6, controlled_buffer_1_out[29:24], controlled_buffer_1_out_5, controlled_buffer_1_out_4, controlled_buffer_1_out_3, controlled_buffer_1_out_2, controlled_buffer_1_out[7:0]} = and_75_out ? 32'h1002410 : 32'bz;  // Controlled_Buffer controlled_buffer_35
  assign {controlled_buffer_1_out_6, controlled_buffer_1_out[29:24], controlled_buffer_1_out_5, controlled_buffer_1_out_4, controlled_buffer_1_out_3, controlled_buffer_1_out_2, controlled_buffer_1_out[7:0]} = and_78_out ? 32'h1003410 : 32'bz;  // Controlled_Buffer controlled_buffer_36
  assign {controlled_buffer_1_out_6, controlled_buffer_1_out[29:24], controlled_buffer_1_out_5, controlled_buffer_1_out_4, controlled_buffer_1_out_3, controlled_buffer_1_out_2, controlled_buffer_1_out[7:0]} = and_79_out ? 32'h1014410 : 32'bz;  // Controlled_Buffer controlled_buffer_37
  Controlled_Buffer #(.width(32)) controlled_buffer_38 (.in(32'h1004410), .en(and_81_out));  // open: out
  assign {controlled_buffer_1_out_6, controlled_buffer_1_out[29:24], controlled_buffer_1_out_5, controlled_buffer_1_out_4, controlled_buffer_1_out_3, controlled_buffer_1_out_2, controlled_buffer_1_out[7:0]} = and_84_out ? 32'h1005410 : 32'bz;  // Controlled_Buffer controlled_buffer_39
  assign {controlled_buffer_1_out_6, controlled_buffer_1_out[29:24], controlled_buffer_1_out_5, controlled_buffer_1_out_4, controlled_buffer_1_out_3, controlled_buffer_1_out_2, controlled_buffer_1_out[7:0]} = and_87_out ? 32'h1000520 : 32'bz;  // Controlled_Buffer controlled_buffer_40
  assign {controlled_buffer_1_out_6, controlled_buffer_1_out[29:24], controlled_buffer_1_out_5, controlled_buffer_1_out_4, controlled_buffer_1_out_3, controlled_buffer_1_out_2, controlled_buffer_1_out[7:0]} = and_9_out ? 32'h1011520 : 32'bz;  // Controlled_Buffer controlled_buffer_41
  assign {controlled_buffer_1_out_6, controlled_buffer_1_out[29:24], controlled_buffer_1_out_5, controlled_buffer_1_out_4, controlled_buffer_1_out_3, controlled_buffer_1_out_2, controlled_buffer_1_out[7:0]} = and_89_out ? 32'h1001520 : 32'bz;  // Controlled_Buffer controlled_buffer_42
  assign {controlled_buffer_1_out_6, controlled_buffer_1_out[29:24], controlled_buffer_1_out_5, controlled_buffer_1_out_4, controlled_buffer_1_out_3, controlled_buffer_1_out_2, controlled_buffer_1_out[7:0]} = and_10_out ? 32'h1012520 : 32'bz;  // Controlled_Buffer controlled_buffer_43
  assign {controlled_buffer_1_out_6, controlled_buffer_1_out[29:24], controlled_buffer_1_out_5, controlled_buffer_1_out_4, controlled_buffer_1_out_3, controlled_buffer_1_out_2, controlled_buffer_1_out[7:0]} = and_91_out ? 32'h1002520 : 32'bz;  // Controlled_Buffer controlled_buffer_44
  assign {controlled_buffer_1_out_6, controlled_buffer_1_out[29:24], controlled_buffer_1_out_5, controlled_buffer_1_out_4, controlled_buffer_1_out_3, controlled_buffer_1_out_2, controlled_buffer_1_out[7:0]} = and_11_out ? 32'h1013520 : 32'bz;  // Controlled_Buffer controlled_buffer_45
  assign {controlled_buffer_1_out_6, controlled_buffer_1_out[29:24], controlled_buffer_1_out_5, controlled_buffer_1_out_4, controlled_buffer_1_out_3, controlled_buffer_1_out_2, controlled_buffer_1_out[7:0]} = and_93_out ? 32'h1003520 : 32'bz;  // Controlled_Buffer controlled_buffer_46
  assign {controlled_buffer_1_out_6, controlled_buffer_1_out[29:24], controlled_buffer_1_out_5, controlled_buffer_1_out_4, controlled_buffer_1_out_3, controlled_buffer_1_out_2, controlled_buffer_1_out[7:0]} = and_96_out ? 32'h1004520 : 32'bz;  // Controlled_Buffer controlled_buffer_47
  assign {controlled_buffer_1_out_6, controlled_buffer_1_out[29:24], controlled_buffer_1_out_5, controlled_buffer_1_out_4, controlled_buffer_1_out_3, controlled_buffer_1_out_2, controlled_buffer_1_out[7:0]} = and_99_out ? 32'h1005520 : 32'bz;  // Controlled_Buffer controlled_buffer_48
  Clock clock_1 (.out(clock_1_out));
  assign {controlled_buffer_1_out_6, controlled_buffer_1_out[29:24], controlled_buffer_1_out_5, controlled_buffer_1_out_4, controlled_buffer_1_out_3, controlled_buffer_1_out_2, controlled_buffer_1_out[7:0]} = and_12_out ? 32'h1010001 : 32'bz;  // Controlled_Buffer controlled_buffer_49
  assign {controlled_buffer_1_out_6, controlled_buffer_1_out[29:24], controlled_buffer_1_out_5, controlled_buffer_1_out_4, controlled_buffer_1_out_3, controlled_buffer_1_out_2, controlled_buffer_1_out[7:0]} = and_13_out ? 32'h1012001 : 32'bz;  // Controlled_Buffer controlled_buffer_50
  assign {controlled_buffer_1_out_6, controlled_buffer_1_out[29:24], controlled_buffer_1_out_5, controlled_buffer_1_out_4, controlled_buffer_1_out_3, controlled_buffer_1_out_2, controlled_buffer_1_out[7:0]} = and_14_out ? 32'h1002001 : 32'bz;  // Controlled_Buffer controlled_buffer_51
  assign {controlled_buffer_1_out_6, controlled_buffer_1_out[29:24], controlled_buffer_1_out_5, controlled_buffer_1_out_4, controlled_buffer_1_out_3, controlled_buffer_1_out_2, controlled_buffer_1_out[7:0]} = and_18_out ? 32'h1004001 : 32'bz;  // Controlled_Buffer controlled_buffer_52
  assign {controlled_buffer_1_out_6, controlled_buffer_1_out[29:24], controlled_buffer_1_out_5, controlled_buffer_1_out_4, controlled_buffer_1_out_3, controlled_buffer_1_out_2, controlled_buffer_1_out[7:0]} = and_20_out ? 32'h1005001 : 32'bz;  // Controlled_Buffer controlled_buffer_53
  assign {controlled_buffer_1_out_6, controlled_buffer_1_out[29:24], controlled_buffer_1_out_5, controlled_buffer_1_out_4, controlled_buffer_1_out_3, controlled_buffer_1_out_2, controlled_buffer_1_out[7:0]} = and_21_out ? 32'h1010102 : 32'bz;  // Controlled_Buffer controlled_buffer_54
  assign {controlled_buffer_1_out_6, controlled_buffer_1_out[29:24], controlled_buffer_1_out_5, controlled_buffer_1_out_4, controlled_buffer_1_out_3, controlled_buffer_1_out_2, controlled_buffer_1_out[7:0]} = and_24_out ? 32'h1011102 : 32'bz;  // Controlled_Buffer controlled_buffer_55
  assign {controlled_buffer_1_out_6, controlled_buffer_1_out[29:24], controlled_buffer_1_out_5, controlled_buffer_1_out_4, controlled_buffer_1_out_3, controlled_buffer_1_out_2, controlled_buffer_1_out[7:0]} = and_27_out ? 32'h1012102 : 32'bz;  // Controlled_Buffer controlled_buffer_56
  assign {controlled_buffer_1_out_6, controlled_buffer_1_out[29:24], controlled_buffer_1_out_5, controlled_buffer_1_out_4, controlled_buffer_1_out_3, controlled_buffer_1_out_2, controlled_buffer_1_out[7:0]} = and_1_out ? 32'h1013102 : 32'bz;  // Controlled_Buffer controlled_buffer_57
  assign {controlled_buffer_1_out_6, controlled_buffer_1_out[29:24], controlled_buffer_1_out_5, controlled_buffer_1_out_4, controlled_buffer_1_out_3, controlled_buffer_1_out_2, controlled_buffer_1_out[7:0]} = and_32_out ? 32'h1014102 : 32'bz;  // Controlled_Buffer controlled_buffer_58
  assign {controlled_buffer_1_out_6, controlled_buffer_1_out[29:24], controlled_buffer_1_out_5, controlled_buffer_1_out_4, controlled_buffer_1_out_3, controlled_buffer_1_out_2, controlled_buffer_1_out[7:0]} = and_35_out ? 32'h1015102 : 32'bz;  // Controlled_Buffer controlled_buffer_59
  assign {controlled_buffer_1_out_6, controlled_buffer_1_out[29:24], controlled_buffer_1_out_5, controlled_buffer_1_out_4, controlled_buffer_1_out_3, controlled_buffer_1_out_2, controlled_buffer_1_out[7:0]} = and_38_out ? 32'h1010204 : 32'bz;  // Controlled_Buffer controlled_buffer_60
  assign {controlled_buffer_1_out_6, controlled_buffer_1_out[29:24], controlled_buffer_1_out_5, controlled_buffer_1_out_4, controlled_buffer_1_out_3, controlled_buffer_1_out_2, controlled_buffer_1_out[7:0]} = and_41_out ? 32'h1011204 : 32'bz;  // Controlled_Buffer controlled_buffer_61
  assign {controlled_buffer_1_out_6, controlled_buffer_1_out[29:24], controlled_buffer_1_out_5, controlled_buffer_1_out_4, controlled_buffer_1_out_3, controlled_buffer_1_out_2, controlled_buffer_1_out[7:0]} = and_44_out ? 32'h1012204 : 32'bz;  // Controlled_Buffer controlled_buffer_62
  assign {controlled_buffer_1_out_6, controlled_buffer_1_out[29:24], controlled_buffer_1_out_5, controlled_buffer_1_out_4, controlled_buffer_1_out_3, controlled_buffer_1_out_2, controlled_buffer_1_out[7:0]} = and_57_out ? 32'h1012308 : 32'bz;  // Controlled_Buffer controlled_buffer_63
  assign {controlled_buffer_1_out_6, controlled_buffer_1_out[29:24], controlled_buffer_1_out_5, controlled_buffer_1_out_4, controlled_buffer_1_out_3, controlled_buffer_1_out_2, controlled_buffer_1_out[7:0]} = and_60_out ? 32'h1013308 : 32'bz;  // Controlled_Buffer controlled_buffer_64
  assign {controlled_buffer_1_out_6, controlled_buffer_1_out[29:24], controlled_buffer_1_out_5, controlled_buffer_1_out_4, controlled_buffer_1_out_3, controlled_buffer_1_out_2, controlled_buffer_1_out[7:0]} = and_65_out ? 32'h1015308 : 32'bz;  // Controlled_Buffer controlled_buffer_65
  assign {controlled_buffer_1_out_6, controlled_buffer_1_out[29:24], controlled_buffer_1_out_5, controlled_buffer_1_out_4, controlled_buffer_1_out_3, controlled_buffer_1_out_2, controlled_buffer_1_out[7:0]} = and_68_out ? 32'h1010410 : 32'bz;  // Controlled_Buffer controlled_buffer_66
  assign {controlled_buffer_1_out_6, controlled_buffer_1_out[29:24], controlled_buffer_1_out_5, controlled_buffer_1_out_4, controlled_buffer_1_out_3, controlled_buffer_1_out_2, controlled_buffer_1_out[7:0]} = and_73_out ? 32'h1012410 : 32'bz;  // Controlled_Buffer controlled_buffer_67
  assign {controlled_buffer_1_out_6, controlled_buffer_1_out[29:24], controlled_buffer_1_out_5, controlled_buffer_1_out_4, controlled_buffer_1_out_3, controlled_buffer_1_out_2, controlled_buffer_1_out[7:0]} = and_76_out ? 32'h1013410 : 32'bz;  // Controlled_Buffer controlled_buffer_68
  assign {controlled_buffer_1_out_6, controlled_buffer_1_out[29:24], controlled_buffer_1_out_5, controlled_buffer_1_out_4, controlled_buffer_1_out_3, controlled_buffer_1_out_2, controlled_buffer_1_out[7:0]} = and_85_out ? 32'h1010520 : 32'bz;  // Controlled_Buffer controlled_buffer_69
  assign {controlled_buffer_1_out_6, controlled_buffer_1_out[29:24], controlled_buffer_1_out_5, controlled_buffer_1_out_4, controlled_buffer_1_out_3, controlled_buffer_1_out_2, controlled_buffer_1_out[7:0]} = and_94_out ? 32'h1014520 : 32'bz;  // Controlled_Buffer controlled_buffer_70
  assign {controlled_buffer_1_out_6, controlled_buffer_1_out[29:24], controlled_buffer_1_out_5, controlled_buffer_1_out_4, controlled_buffer_1_out_3, controlled_buffer_1_out_2, controlled_buffer_1_out[7:0]} = and_97_out ? 32'h1015520 : 32'bz;  // Controlled_Buffer controlled_buffer_71
  assign {controlled_buffer_1_out_6, controlled_buffer_1_out[29:24], controlled_buffer_1_out_5, controlled_buffer_1_out_4, controlled_buffer_1_out_3, controlled_buffer_1_out_2, controlled_buffer_1_out[7:0]} = and_101_out ? 32'h1011001 : 32'bz;  // Controlled_Buffer controlled_buffer_72
  and and_1 (and_1_out, and_156_out, and_151_out, and_111_out, d_ff_1_q);
  and and_2 (and_2_out, and_156_out, and_152_out, and_117_out, d_ff_1_q);
  and and_3 (and_3_out, and_156_out, and_152_out, and_118_out, d_ff_1_q);
  and and_4 (and_4_out, and_156_out, and_152_out, and_119_out, d_ff_1_q);
  and and_5 (and_5_out, and_156_out, and_153_out, and_120_out, d_ff_1_q);
  and and_6 (and_6_out, and_156_out, and_153_out, and_121_out, d_ff_1_q);
  and and_7 (and_7_out, and_156_out, and_153_out, and_124_out, d_ff_1_q);
  and and_8 (and_8_out, and_156_out, and_154_out, and_127_out, d_ff_1_q);
  and and_9 (and_9_out, and_156_out, and_155_out, and_133_out, d_ff_1_q);
  and and_10 (and_10_out, and_156_out, and_155_out, and_134_out, d_ff_1_q);
  and and_11 (and_11_out, and_156_out, and_155_out, and_135_out, d_ff_1_q);
  and and_12 (and_12_out, d_ff_1_q, and_156_out, and_138_out);
  and and_13 (and_13_out, and_156_out, and_156_out, and_104_out);
  and and_14 (and_14_out, d_ff_1_q, and_157_out, and_104_out);
  and and_15 (and_15_out, d_ff_1_q, and_156_out, and_105_out);
  and and_16 (and_16_out, d_ff_1_q, and_157_out, and_105_out);
  and and_17 (and_17_out, d_ff_1_q, and_156_out, and_106_out);
  and and_18 (and_18_out, and_157_out, and_106_out, d_ff_1_q);
  and and_19 (and_19_out, d_ff_1_q, and_156_out, and_107_out);
  and and_20 (and_20_out, and_157_out, and_107_out, d_ff_1_q);
  and and_21 (and_21_out, and_156_out, and_151_out, and_108_out, d_ff_1_q);
  and and_22 (and_22_out, and_157_out, and_151_out, and_108_out);
  and and_23 (and_23_out, and_22_out, d_ff_1_q);
  and and_24 (and_24_out, and_151_out, and_109_out, and_156_out, d_ff_1_q);
  and and_25 (and_25_out, and_157_out, and_151_out, and_109_out);
  and and_26 (and_26_out, and_25_out, d_ff_1_q);
  and and_27 (and_27_out, and_156_out, and_151_out, and_110_out, d_ff_1_q);
  and and_28 (and_28_out, and_157_out, and_151_out, and_110_out);
  and and_29 (and_29_out, and_28_out, d_ff_1_q);
  and and_30 (and_30_out, and_157_out, and_151_out, and_111_out);
  and and_31 (and_31_out, and_30_out, d_ff_1_q);
  and and_32 (and_32_out, and_156_out, and_151_out, and_112_out, d_ff_1_q);
  and and_33 (and_33_out, and_157_out, and_151_out, and_112_out);
  and and_34 (and_34_out, and_33_out, d_ff_1_q);
  and and_35 (and_35_out, and_156_out, and_151_out, and_113_out, d_ff_1_q);
  and and_36 (and_36_out, and_157_out, and_151_out, and_113_out);
  and and_37 (and_37_out, and_36_out, d_ff_1_q);
  and and_38 (and_38_out, and_156_out, and_152_out, and_114_out, d_ff_1_q);
  and and_39 (and_39_out, and_157_out, and_152_out, and_114_out);
  and and_40 (and_40_out, and_39_out, d_ff_1_q);
  and and_41 (and_41_out, and_156_out, and_152_out, and_115_out, d_ff_1_q);
  and and_42 (and_42_out, and_157_out, and_152_out, and_115_out);
  and and_43 (and_43_out, and_42_out, d_ff_1_q);
  and and_44 (and_44_out, and_156_out, and_152_out, and_116_out, d_ff_1_q);
  and and_45 (and_45_out, and_157_out, and_152_out, and_116_out);
  and and_46 (and_46_out, and_45_out, d_ff_1_q);
  and and_47 (and_47_out, and_157_out, and_152_out, and_117_out);
  and and_48 (and_48_out, and_47_out, d_ff_1_q);
  and and_49 (and_49_out, and_157_out, and_152_out, and_118_out);
  and and_50 (and_50_out, and_49_out, d_ff_1_q);
  and and_51 (and_51_out, and_157_out, and_152_out, and_119_out);
  and and_52 (and_52_out, and_51_out, d_ff_1_q);
  and and_53 (and_53_out, and_157_out, and_153_out, and_120_out);
  and and_54 (and_54_out, and_53_out, d_ff_1_q);
  and and_55 (and_55_out, and_157_out, and_153_out, and_121_out);
  and and_56 (and_56_out, and_55_out, d_ff_1_q);
  and and_57 (and_57_out, and_156_out, and_153_out, and_122_out, d_ff_1_q);
  and and_58 (and_58_out, and_157_out, and_153_out, and_122_out);
  and and_59 (and_59_out, and_58_out, d_ff_1_q);
  and and_60 (and_60_out, and_156_out, and_153_out, and_123_out, d_ff_1_q);
  and and_61 (and_61_out, and_157_out, and_153_out, and_123_out);
  and and_62 (and_62_out, and_61_out, d_ff_1_q);
  and and_63 (and_63_out, and_157_out, and_153_out, and_124_out);
  and and_64 (and_64_out, and_63_out, d_ff_1_q);
  and and_65 (and_65_out, and_156_out, and_153_out, and_125_out, d_ff_1_q);
  and and_66 (and_66_out, and_157_out, and_153_out, and_125_out);
  and and_67 (and_67_out, and_66_out, d_ff_1_q);
  and and_68 (and_68_out, and_156_out, and_154_out, and_126_out, d_ff_1_q);
  and and_69 (and_69_out, and_157_out, and_154_out, and_126_out);
  and and_70 (and_70_out, and_69_out, d_ff_1_q);
  and and_71 (and_71_out, and_157_out, and_154_out, and_127_out);
  and and_72 (and_72_out, and_71_out, d_ff_1_q);
  and and_73 (and_73_out, and_156_out, and_154_out, and_128_out, d_ff_1_q);
  and and_74 (and_74_out, and_157_out, and_154_out, and_128_out);
  and and_75 (and_75_out, and_74_out, d_ff_1_q);
  and and_76 (and_76_out, and_156_out, and_154_out, and_129_out, d_ff_1_q);
  and and_77 (and_77_out, and_157_out, and_154_out, and_129_out);
  and and_78 (and_78_out, and_77_out, d_ff_1_q);
  and and_79 (and_79_out, and_156_out, and_154_out, and_130_out, d_ff_1_q);
  and and_80 (and_80_out, and_157_out, and_154_out, and_130_out);
  and and_81 (and_81_out, and_80_out, d_ff_1_q);
  and and_82 (and_82_out, and_156_out, and_154_out, and_131_out, d_ff_1_q);
  and and_83 (and_83_out, and_157_out, and_154_out, and_131_out);
  and and_84 (and_84_out, and_83_out, d_ff_1_q);
  and and_85 (and_85_out, and_156_out, and_155_out, and_132_out, d_ff_1_q);
  and and_86 (and_86_out, and_157_out, and_155_out, and_132_out);
  and and_87 (and_87_out, and_86_out, d_ff_1_q);
  and and_88 (and_88_out, and_157_out, and_155_out, and_133_out);
  and and_89 (and_89_out, and_88_out, d_ff_1_q);
  and and_90 (and_90_out, and_157_out, and_155_out, and_134_out);
  and and_91 (and_91_out, and_90_out, d_ff_1_q);
  and and_92 (and_92_out, and_157_out, and_155_out, and_135_out);
  and and_93 (and_93_out, and_92_out, d_ff_1_q);
  and and_94 (and_94_out, and_156_out, and_155_out, and_136_out, d_ff_1_q);
  and and_95 (and_95_out, and_157_out, and_155_out, and_136_out);
  and and_96 (and_96_out, and_95_out, d_ff_1_q);
  and and_97 (and_97_out, and_156_out, and_155_out, and_137_out, d_ff_1_q);
  and and_98 (and_98_out, and_157_out, and_155_out, and_137_out);
  and and_99 (and_99_out, and_98_out, d_ff_1_q);
  assign controlled_buffer_73_out = controlled_buffer_1_out[6] ? out_4 : 32'bz;  // Controlled_Buffer controlled_buffer_73
  and and_100 (and_100_out, d_ff_1_q, and_157_out, and_138_out);
  and and_101 (and_101_out, d_ff_1_q, and_156_out, and_103_out);
  and and_102 (and_102_out, d_ff_1_q, and_157_out, and_103_out);
  and and_103 (and_103_out, and_139_out, and_140_out);
  and and_104 (and_104_out, and_141_out, and_142_out);
  and and_105 (and_105_out, and_143_out, and_144_out);
  and and_106 (and_106_out, and_145_out, and_146_out);
  and and_107 (and_107_out, and_147_out, and_148_out);
  and and_108 (and_108_out, ~controlled_buffer_140_out[15], ~controlled_buffer_140_out[14], ~controlled_buffer_140_out[13], ~controlled_buffer_140_out[12]);  // AND_Gate
  and and_109 (and_109_out, ~controlled_buffer_140_out[15], ~controlled_buffer_140_out[14], ~controlled_buffer_140_out[13], controlled_buffer_140_out[12]);  // AND_Gate
  and and_110 (and_110_out, ~controlled_buffer_140_out[15], ~controlled_buffer_140_out[14], controlled_buffer_140_out[13], ~controlled_buffer_140_out[12]);  // AND_Gate
  and and_111 (and_111_out, ~controlled_buffer_140_out[15], ~controlled_buffer_140_out[14], controlled_buffer_140_out[13], controlled_buffer_140_out[12]);  // AND_Gate
  and and_112 (and_112_out, ~controlled_buffer_140_out[15], controlled_buffer_140_out[14], ~controlled_buffer_140_out[13], ~controlled_buffer_140_out[12]);  // AND_Gate
  and and_113 (and_113_out, ~controlled_buffer_140_out[15], controlled_buffer_140_out[14], ~controlled_buffer_140_out[13], controlled_buffer_140_out[12]);  // AND_Gate
  and and_114 (and_114_out, ~controlled_buffer_140_out[15], ~controlled_buffer_140_out[14], ~controlled_buffer_140_out[13], ~controlled_buffer_140_out[12]);  // AND_Gate
  and and_115 (and_115_out, ~controlled_buffer_140_out[15], ~controlled_buffer_140_out[14], ~controlled_buffer_140_out[13], controlled_buffer_140_out[12]);  // AND_Gate
  and and_116 (and_116_out, ~controlled_buffer_140_out[15], ~controlled_buffer_140_out[14], controlled_buffer_140_out[13], ~controlled_buffer_140_out[12]);  // AND_Gate
  and and_117 (and_117_out, ~controlled_buffer_140_out[15], ~controlled_buffer_140_out[14], controlled_buffer_140_out[13], controlled_buffer_140_out[12]);  // AND_Gate
  and and_118 (and_118_out, ~controlled_buffer_140_out[15], controlled_buffer_140_out[14], ~controlled_buffer_140_out[13], ~controlled_buffer_140_out[12]);  // AND_Gate
  and and_119 (and_119_out, ~controlled_buffer_140_out[15], controlled_buffer_140_out[14], ~controlled_buffer_140_out[13], controlled_buffer_140_out[12]);  // AND_Gate
  and and_120 (and_120_out, ~controlled_buffer_140_out[15], ~controlled_buffer_140_out[14], ~controlled_buffer_140_out[13], ~controlled_buffer_140_out[12]);  // AND_Gate
  and and_121 (and_121_out, ~controlled_buffer_140_out[15], ~controlled_buffer_140_out[14], ~controlled_buffer_140_out[13], controlled_buffer_140_out[12]);  // AND_Gate
  and and_122 (and_122_out, ~controlled_buffer_140_out[15], ~controlled_buffer_140_out[14], controlled_buffer_140_out[13], ~controlled_buffer_140_out[12]);  // AND_Gate
  and and_123 (and_123_out, ~controlled_buffer_140_out[15], ~controlled_buffer_140_out[14], controlled_buffer_140_out[13], controlled_buffer_140_out[12]);  // AND_Gate
  and and_124 (and_124_out, ~controlled_buffer_140_out[15], controlled_buffer_140_out[14], ~controlled_buffer_140_out[13], ~controlled_buffer_140_out[12]);  // AND_Gate
  and and_125 (and_125_out, ~controlled_buffer_140_out[15], controlled_buffer_140_out[14], ~controlled_buffer_140_out[13], controlled_buffer_140_out[12]);  // AND_Gate
  and and_126 (and_126_out, ~controlled_buffer_140_out[15], ~controlled_buffer_140_out[14], ~controlled_buffer_140_out[13], ~controlled_buffer_140_out[12]);  // AND_Gate
  and and_127 (and_127_out, ~controlled_buffer_140_out[15], ~controlled_buffer_140_out[14], ~controlled_buffer_140_out[13], controlled_buffer_140_out[12]);  // AND_Gate
  and and_128 (and_128_out, ~controlled_buffer_140_out[15], ~controlled_buffer_140_out[14], controlled_buffer_140_out[13], ~controlled_buffer_140_out[12]);  // AND_Gate
  and and_129 (and_129_out, ~controlled_buffer_140_out[15], ~controlled_buffer_140_out[14], controlled_buffer_140_out[13], controlled_buffer_140_out[12]);  // AND_Gate
  and and_130 (and_130_out, ~controlled_buffer_140_out[15], controlled_buffer_140_out[14], ~controlled_buffer_140_out[13], ~controlled_buffer_140_out[12]);  // AND_Gate
  and and_131 (and_131_out, ~controlled_buffer_140_out[15], controlled_buffer_140_out[14], ~controlled_buffer_140_out[13], controlled_buffer_140_out[12]);  // AND_Gate
  and and_132 (and_132_out, ~controlled_buffer_140_out[15], ~controlled_buffer_140_out[14], ~controlled_buffer_140_out[13], ~controlled_buffer_140_out[12]);  // AND_Gate
  and and_133 (and_133_out, ~controlled_buffer_140_out[15], ~controlled_buffer_140_out[14], ~controlled_buffer_140_out[13], controlled_buffer_140_out[12]);  // AND_Gate
  and and_134 (and_134_out, ~controlled_buffer_140_out[15], ~controlled_buffer_140_out[14], controlled_buffer_140_out[13], ~controlled_buffer_140_out[12]);  // AND_Gate
  and and_135 (and_135_out, ~controlled_buffer_140_out[15], ~controlled_buffer_140_out[14], controlled_buffer_140_out[13], controlled_buffer_140_out[12]);  // AND_Gate
  and and_136 (and_136_out, ~controlled_buffer_140_out[15], controlled_buffer_140_out[14], ~controlled_buffer_140_out[13], ~controlled_buffer_140_out[12]);  // AND_Gate
  and and_137 (and_137_out, ~controlled_buffer_140_out[15], controlled_buffer_140_out[14], ~controlled_buffer_140_out[13], controlled_buffer_140_out[12]);  // AND_Gate
  and and_138 (and_138_out, and_149_out, and_150_out);
  and and_139 (and_139_out, ~controlled_buffer_140_out[15], ~controlled_buffer_140_out[14], ~controlled_buffer_140_out[13], controlled_buffer_140_out[12]);  // AND_Gate
  and and_140 (and_140_out, ~controlled_buffer_140_out[11], ~controlled_buffer_140_out[10], ~controlled_buffer_140_out[9], ~controlled_buffer_140_out[8]);  // AND_Gate
  and and_141 (and_141_out, ~controlled_buffer_140_out[15], ~controlled_buffer_140_out[14], controlled_buffer_140_out[13], ~controlled_buffer_140_out[12]);  // AND_Gate
  and and_142 (and_142_out, ~controlled_buffer_140_out[11], ~controlled_buffer_140_out[10], ~controlled_buffer_140_out[9], ~controlled_buffer_140_out[8]);  // AND_Gate
  and and_143 (and_143_out, ~controlled_buffer_140_out[15], ~controlled_buffer_140_out[14], controlled_buffer_140_out[13], controlled_buffer_140_out[12]);  // AND_Gate
  and and_144 (and_144_out, ~controlled_buffer_140_out[11], ~controlled_buffer_140_out[10], ~controlled_buffer_140_out[9], ~controlled_buffer_140_out[8]);  // AND_Gate
  and and_145 (and_145_out, ~controlled_buffer_140_out[15], controlled_buffer_140_out[14], ~controlled_buffer_140_out[13], ~controlled_buffer_140_out[12]);  // AND_Gate
  and and_146 (and_146_out, ~controlled_buffer_140_out[11], ~controlled_buffer_140_out[10], ~controlled_buffer_140_out[9], ~controlled_buffer_140_out[8]);  // AND_Gate
  and and_147 (and_147_out, ~controlled_buffer_140_out[15], controlled_buffer_140_out[14], ~controlled_buffer_140_out[13], controlled_buffer_140_out[12]);  // AND_Gate
  and and_148 (and_148_out, ~controlled_buffer_140_out[11], ~controlled_buffer_140_out[10], ~controlled_buffer_140_out[9], ~controlled_buffer_140_out[8]);  // AND_Gate
  Register #(.width(32)) register_1 (
    .D(out_4), .en(controlled_buffer_1_out[0]), .Q(register_1_q), .clk(clock_1_out), .clr(in_1));
  Register #(.width(32)) register_2 (
    .D(out_4), .en(controlled_buffer_1_out[1]), .Q(register_2_q), .clk(clock_1_out), .clr(in_1));
  Register #(.width(32)) register_3 (
    .D(out_4), .en(controlled_buffer_1_out[2]), .Q(register_3_q), .clk(clock_1_out), .clr(in_1));
  Register #(.width(32)) register_4 (
    .D(out_4), .en(controlled_buffer_1_out[3]), .Q(register_4_q), .clk(clock_1_out), .clr(in_1));
  Register #(.width(32)) register_5 (
    .D(out_4), .en(controlled_buffer_1_out[4]), .Q(register_5_q), .clk(clock_1_out), .clr(in_1));
  Register #(.width(32)) register_6 (
    .D(out_4), .en(controlled_buffer_1_out[5]), .Q(register_6_q), .clk(clock_1_out), .clr(in_1));
  Register #(.width(16)) register_7 (
    .D(controlled_buffer_73_out[15:0]), .en(controlled_buffer_1_out[6]), .Q(register_7_q), .clk(clock_1_out),
    .clr(in_1));
  Register #(.width(16)) register_8 (
    .D(controlled_buffer_73_out[15:0]), .en(controlled_buffer_1_out[7]), .Q(register_8_q), .clk(clock_1_out),
    .clr(in_1));
  and and_149 (and_149_out, ~controlled_buffer_140_out[15], ~controlled_buffer_140_out[14], ~controlled_buffer_140_out[13], ~controlled_buffer_140_out[12]);  // AND_Gate
  and and_150 (and_150_out, ~controlled_buffer_140_out[11], ~controlled_buffer_140_out[10], ~controlled_buffer_140_out[9], ~controlled_buffer_140_out[8]);  // AND_Gate
  and and_151 (and_151_out, ~controlled_buffer_140_out[11], ~controlled_buffer_140_out[10], ~controlled_buffer_140_out[9], controlled_buffer_140_out[8]);  // AND_Gate
  and and_152 (and_152_out, ~controlled_buffer_140_out[11], ~controlled_buffer_140_out[10], controlled_buffer_140_out[9], ~controlled_buffer_140_out[8]);  // AND_Gate
  and and_153 (and_153_out, ~controlled_buffer_140_out[11], ~controlled_buffer_140_out[10], controlled_buffer_140_out[9], controlled_buffer_140_out[8]);  // AND_Gate
  and and_154 (and_154_out, ~controlled_buffer_140_out[11], controlled_buffer_140_out[10], ~controlled_buffer_140_out[9], ~controlled_buffer_140_out[8]);  // AND_Gate
  and and_155 (and_155_out, ~controlled_buffer_140_out[11], controlled_buffer_140_out[10], ~controlled_buffer_140_out[9], controlled_buffer_140_out[8]);  // AND_Gate
  and and_156 (and_156_out, ~controlled_buffer_140_out[7], ~controlled_buffer_140_out[6], ~controlled_buffer_140_out[5], ~controlled_buffer_140_out[4], ~controlled_buffer_140_out[3], controlled_buffer_140_out[2], controlled_buffer_140_out[1], ~controlled_buffer_140_out[0]);  // AND_Gate
  and and_157 (and_157_out, ~controlled_buffer_140_out[7], ~controlled_buffer_140_out[6], ~controlled_buffer_140_out[5], ~controlled_buffer_140_out[4], ~controlled_buffer_140_out[3], controlled_buffer_140_out[2], ~controlled_buffer_140_out[1], controlled_buffer_140_out[0]);  // AND_Gate
  or or_1 (or_1_out, and_175_out, and_174_out, and_173_out, and_172_out, and_171_out, and_170_out);
  Multiplexer #(.select(4), .width(32), .enable("false")) multiplexer_1 (
    .in0(register_1_q), .in1(register_2_q), .in2(register_3_q), .in3(register_4_q), .in4(register_5_q),
    .in5(register_6_q), .in15({32{1'b0}}), .out(multiplexer_1_out), .sel(controlled_buffer_1_out_2));  // open: in6, in7, in8, in9, in10, in11, in12, in13, in14
  Multiplexer #(.select(4), .width(32), .enable("false")) multiplexer_2 (
    .in0(register_1_q), .in1(register_2_q), .in2(register_3_q), .in3(register_4_q), .in4(register_5_q),
    .in5(register_6_q), .in15({32{1'b0}}), .out(multiplexer_2_out), .sel(controlled_buffer_1_out_3));  // open: in6, in7, in8, in9, in10, in11, in12, in13, in14
  assign out_4 = or_1_out ? {{16{1'b0}}, controlled_buffer_140_out[31:16]} : 32'bz;  // Controlled_Buffer controlled_buffer_74
  assign {controlled_buffer_1_out_6, controlled_buffer_1_out[29:24], controlled_buffer_1_out_5, controlled_buffer_1_out_4, controlled_buffer_1_out_3, controlled_buffer_1_out_2, controlled_buffer_1_out[7:0]} = and_170_out ? 32'hff01 : 32'bz;  // Controlled_Buffer controlled_buffer_75
  assign {controlled_buffer_1_out_6, controlled_buffer_1_out[29:24], controlled_buffer_1_out_5, controlled_buffer_1_out_4, controlled_buffer_1_out_3, controlled_buffer_1_out_2, controlled_buffer_1_out[7:0]} = and_171_out ? 32'hff02 : 32'bz;  // Controlled_Buffer controlled_buffer_76
  assign {controlled_buffer_1_out_6, controlled_buffer_1_out[29:24], controlled_buffer_1_out_5, controlled_buffer_1_out_4, controlled_buffer_1_out_3, controlled_buffer_1_out_2, controlled_buffer_1_out[7:0]} = and_172_out ? 32'hff04 : 32'bz;  // Controlled_Buffer controlled_buffer_77
  assign {controlled_buffer_1_out_6, controlled_buffer_1_out[29:24], controlled_buffer_1_out_5, controlled_buffer_1_out_4, controlled_buffer_1_out_3, controlled_buffer_1_out_2, controlled_buffer_1_out[7:0]} = and_173_out ? 32'hff08 : 32'bz;  // Controlled_Buffer controlled_buffer_78
  assign {controlled_buffer_1_out_6, controlled_buffer_1_out[29:24], controlled_buffer_1_out_5, controlled_buffer_1_out_4, controlled_buffer_1_out_3, controlled_buffer_1_out_2, controlled_buffer_1_out[7:0]} = and_174_out ? 32'hff10 : 32'bz;  // Controlled_Buffer controlled_buffer_79
  assign {controlled_buffer_1_out_6, controlled_buffer_1_out[29:24], controlled_buffer_1_out_5, controlled_buffer_1_out_4, controlled_buffer_1_out_3, controlled_buffer_1_out_2, controlled_buffer_1_out[7:0]} = and_175_out ? 32'hff20 : 32'bz;  // Controlled_Buffer controlled_buffer_80
  assign {controlled_buffer_1_out_6, controlled_buffer_1_out[29:24], controlled_buffer_1_out_5, controlled_buffer_1_out_4, controlled_buffer_1_out_3, controlled_buffer_1_out_2, controlled_buffer_1_out[7:0]} = and_158_out ? 32'h4600ff01 : 32'bz;  // Controlled_Buffer controlled_buffer_81
  assign {controlled_buffer_1_out_6, controlled_buffer_1_out[29:24], controlled_buffer_1_out_5, controlled_buffer_1_out_4, controlled_buffer_1_out_3, controlled_buffer_1_out_2, controlled_buffer_1_out[7:0]} = and_159_out ? 32'h4600ff02 : 32'bz;  // Controlled_Buffer controlled_buffer_82
  assign {controlled_buffer_1_out_6, controlled_buffer_1_out[29:24], controlled_buffer_1_out_5, controlled_buffer_1_out_4, controlled_buffer_1_out_3, controlled_buffer_1_out_2, controlled_buffer_1_out[7:0]} = and_160_out ? 32'h4600ff04 : 32'bz;  // Controlled_Buffer controlled_buffer_83
  assign {controlled_buffer_1_out_6, controlled_buffer_1_out[29:24], controlled_buffer_1_out_5, controlled_buffer_1_out_4, controlled_buffer_1_out_3, controlled_buffer_1_out_2, controlled_buffer_1_out[7:0]} = and_161_out ? 32'h4600ff08 : 32'bz;  // Controlled_Buffer controlled_buffer_84
  assign {controlled_buffer_1_out_6, controlled_buffer_1_out[29:24], controlled_buffer_1_out_5, controlled_buffer_1_out_4, controlled_buffer_1_out_3, controlled_buffer_1_out_2, controlled_buffer_1_out[7:0]} = and_162_out ? 32'h4600ff10 : 32'bz;  // Controlled_Buffer controlled_buffer_85
  assign {controlled_buffer_1_out_6, controlled_buffer_1_out[29:24], controlled_buffer_1_out_5, controlled_buffer_1_out_4, controlled_buffer_1_out_3, controlled_buffer_1_out_2, controlled_buffer_1_out[7:0]} = and_163_out ? 32'h4600ff20 : 32'bz;  // Controlled_Buffer controlled_buffer_86
  assign {controlled_buffer_1_out_6, controlled_buffer_1_out[29:24], controlled_buffer_1_out_5, controlled_buffer_1_out_4, controlled_buffer_1_out_3, controlled_buffer_1_out_2, controlled_buffer_1_out[7:0]} = and_164_out ? 32'h4b000f01 : 32'bz;  // Controlled_Buffer controlled_buffer_87
  assign {controlled_buffer_1_out_6, controlled_buffer_1_out[29:24], controlled_buffer_1_out_5, controlled_buffer_1_out_4, controlled_buffer_1_out_3, controlled_buffer_1_out_2, controlled_buffer_1_out[7:0]} = and_165_out ? 32'h4b000f02 : 32'bz;  // Controlled_Buffer controlled_buffer_88
  assign {controlled_buffer_1_out_6, controlled_buffer_1_out[29:24], controlled_buffer_1_out_5, controlled_buffer_1_out_4, controlled_buffer_1_out_3, controlled_buffer_1_out_2, controlled_buffer_1_out[7:0]} = and_166_out ? 32'h4b000f04 : 32'bz;  // Controlled_Buffer controlled_buffer_89
  assign {controlled_buffer_1_out_6, controlled_buffer_1_out[29:24], controlled_buffer_1_out_5, controlled_buffer_1_out_4, controlled_buffer_1_out_3, controlled_buffer_1_out_2, controlled_buffer_1_out[7:0]} = and_167_out ? 32'h4b000f08 : 32'bz;  // Controlled_Buffer controlled_buffer_90
  assign {controlled_buffer_1_out_6, controlled_buffer_1_out[29:24], controlled_buffer_1_out_5, controlled_buffer_1_out_4, controlled_buffer_1_out_3, controlled_buffer_1_out_2, controlled_buffer_1_out[7:0]} = and_168_out ? 32'h4b000f10 : 32'bz;  // Controlled_Buffer controlled_buffer_91
  assign {controlled_buffer_1_out_6, controlled_buffer_1_out[29:24], controlled_buffer_1_out_5, controlled_buffer_1_out_4, controlled_buffer_1_out_3, controlled_buffer_1_out_2, controlled_buffer_1_out[7:0]} = and_169_out ? 32'h4b000f20 : 32'bz;  // Controlled_Buffer controlled_buffer_92
  and and_158 (and_158_out, d_ff_2_q, and_176_out, and_185_out);
  and and_159 (and_159_out, d_ff_2_q, and_176_out, and_186_out);
  and and_160 (and_160_out, d_ff_2_q, and_176_out, and_187_out);
  and and_161 (and_161_out, d_ff_2_q, and_176_out, and_188_out);
  and and_162 (and_162_out, d_ff_2_q, and_176_out, and_189_out);
  and and_163 (and_163_out, d_ff_2_q, and_176_out, and_190_out);
  and and_164 (and_164_out, d_ff_2_q, and_177_out, and_191_out);
  and and_165 (and_165_out, d_ff_2_q, and_177_out, and_192_out);
  and and_166 (and_166_out, d_ff_2_q, and_177_out, and_193_out);
  and and_167 (and_167_out, d_ff_2_q, and_177_out, and_194_out);
  and and_168 (and_168_out, d_ff_2_q, and_177_out, and_195_out);
  and and_169 (and_169_out, d_ff_2_q, and_177_out, and_196_out);
  and and_170 (and_170_out, or_2_out, and_178_out, and_179_out);
  and and_171 (and_171_out, or_2_out, and_178_out, and_180_out);
  and and_172 (and_172_out, or_2_out, and_178_out, and_181_out);
  and and_173 (and_173_out, or_2_out, and_178_out, and_182_out);
  and and_174 (and_174_out, or_2_out, and_178_out, and_183_out);
  and and_175 (and_175_out, or_2_out, and_178_out, and_184_out);
  and and_176 (and_176_out, ~controlled_buffer_140_out[7], ~controlled_buffer_140_out[6], ~controlled_buffer_140_out[5], ~controlled_buffer_140_out[4], ~controlled_buffer_140_out[3], ~controlled_buffer_140_out[2], controlled_buffer_140_out[1], controlled_buffer_140_out[0]);  // AND_Gate
  and and_177 (and_177_out, ~controlled_buffer_140_out[7], ~controlled_buffer_140_out[6], ~controlled_buffer_140_out[5], ~controlled_buffer_140_out[4], ~controlled_buffer_140_out[3], controlled_buffer_140_out[2], ~controlled_buffer_140_out[1], ~controlled_buffer_140_out[0]);  // AND_Gate
  or or_2 (or_2_out, d_ff_1_q, d_ff_2_q);
  and and_178 (and_178_out, ~controlled_buffer_140_out[7], ~controlled_buffer_140_out[6], ~controlled_buffer_140_out[5], ~controlled_buffer_140_out[4], ~controlled_buffer_140_out[3], ~controlled_buffer_140_out[2], controlled_buffer_140_out[1], ~controlled_buffer_140_out[0]);  // AND_Gate
  and and_179 (and_179_out, ~controlled_buffer_140_out[11], ~controlled_buffer_140_out[10], ~controlled_buffer_140_out[9], ~controlled_buffer_140_out[8]);  // AND_Gate
  and and_180 (and_180_out, ~controlled_buffer_140_out[11], ~controlled_buffer_140_out[10], ~controlled_buffer_140_out[9], controlled_buffer_140_out[8]);  // AND_Gate
  and and_181 (and_181_out, ~controlled_buffer_140_out[11], ~controlled_buffer_140_out[10], controlled_buffer_140_out[9], ~controlled_buffer_140_out[8]);  // AND_Gate
  and and_182 (and_182_out, ~controlled_buffer_140_out[11], ~controlled_buffer_140_out[10], controlled_buffer_140_out[9], controlled_buffer_140_out[8]);  // AND_Gate
  and and_183 (and_183_out, ~controlled_buffer_140_out[11], controlled_buffer_140_out[10], ~controlled_buffer_140_out[9], ~controlled_buffer_140_out[8]);  // AND_Gate
  and and_184 (and_184_out, ~controlled_buffer_140_out[11], controlled_buffer_140_out[10], ~controlled_buffer_140_out[9], controlled_buffer_140_out[8]);  // AND_Gate
  and and_185 (and_185_out, ~controlled_buffer_140_out[11], ~controlled_buffer_140_out[10], ~controlled_buffer_140_out[9], ~controlled_buffer_140_out[8]);  // AND_Gate
  and and_186 (and_186_out, ~controlled_buffer_140_out[11], ~controlled_buffer_140_out[10], ~controlled_buffer_140_out[9], controlled_buffer_140_out[8]);  // AND_Gate
  and and_187 (and_187_out, ~controlled_buffer_140_out[11], ~controlled_buffer_140_out[10], controlled_buffer_140_out[9], ~controlled_buffer_140_out[8]);  // AND_Gate
  and and_188 (and_188_out, ~controlled_buffer_140_out[11], ~controlled_buffer_140_out[10], controlled_buffer_140_out[9], controlled_buffer_140_out[8]);  // AND_Gate
  and and_189 (and_189_out, ~controlled_buffer_140_out[11], controlled_buffer_140_out[10], ~controlled_buffer_140_out[9], ~controlled_buffer_140_out[8]);  // AND_Gate
  and and_190 (and_190_out, ~controlled_buffer_140_out[11], controlled_buffer_140_out[10], ~controlled_buffer_140_out[9], controlled_buffer_140_out[8]);  // AND_Gate
  and and_191 (and_191_out, ~controlled_buffer_140_out[11], ~controlled_buffer_140_out[10], ~controlled_buffer_140_out[9], ~controlled_buffer_140_out[8]);  // AND_Gate
  and and_192 (and_192_out, ~controlled_buffer_140_out[11], ~controlled_buffer_140_out[10], ~controlled_buffer_140_out[9], controlled_buffer_140_out[8]);  // AND_Gate
  and and_193 (and_193_out, ~controlled_buffer_140_out[11], ~controlled_buffer_140_out[10], controlled_buffer_140_out[9], ~controlled_buffer_140_out[8]);  // AND_Gate
  and and_194 (and_194_out, ~controlled_buffer_140_out[11], ~controlled_buffer_140_out[10], controlled_buffer_140_out[9], controlled_buffer_140_out[8]);  // AND_Gate
  and and_195 (and_195_out, ~controlled_buffer_140_out[11], controlled_buffer_140_out[10], ~controlled_buffer_140_out[9], ~controlled_buffer_140_out[8]);  // AND_Gate
  and and_196 (and_196_out, ~controlled_buffer_140_out[11], controlled_buffer_140_out[10], ~controlled_buffer_140_out[9], controlled_buffer_140_out[8]);  // AND_Gate
  D_Flip_Flop zf (
    .clk(clock_1_out), .D(alu32_1_out_16), .Q(zf_q[0]), .en(controlled_buffer_1_out_5[0]), .reset(in_1));  // open: Qn, preset
  alu32 alu32_1 (
    .SHR(demultiplexer_1_out7), .SHL(demultiplexer_1_out6), .XOR(demultiplexer_1_out5),
    .OR(demultiplexer_1_out4), .AND(demultiplexer_1_out3), .SUB(demultiplexer_1_out1),
    .ADD(demultiplexer_1_out0), .in_9(multiplexer_1_out), .in_10(multiplexer_2_out), .out_12(alu32_1_out_12),
    .out_14(alu32_1_out_14), .out_16(alu32_1_out_16), .out_15(alu32_1_out_15), .out_13(alu32_1_out_13),
    .out_11(alu32_1_out_11), .MUL(demultiplexer_1_out2));
  D_Flip_Flop cf (
    .clk(clock_1_out), .D(alu32_1_out_14), .Q(zf_q[1]), .en(controlled_buffer_1_out_5[1]), .reset(in_1));  // open: Qn, preset
  D_Flip_Flop sf (
    .clk(clock_1_out), .D(alu32_1_out_15), .Q(zf_q[2]), .en(controlled_buffer_1_out_5[2]), .reset(in_1));  // open: Qn, preset
  Demultiplexer #(.select(3), .enable("false")) demultiplexer_1 (
    .out0(demultiplexer_1_out0), .out1(demultiplexer_1_out1), .out2(demultiplexer_1_out2),
    .out3(demultiplexer_1_out3), .out4(demultiplexer_1_out4), .out5(demultiplexer_1_out5),
    .out6(demultiplexer_1_out6), .out7(demultiplexer_1_out7), .in(1'b1), .sel(controlled_buffer_1_out_4));
  D_Flip_Flop vf (
    .clk(clock_1_out), .D(alu32_1_out_13), .Q(zf_q[3]), .en(controlled_buffer_1_out_5[3]), .reset(in_1));  // open: Qn, preset
  D_Flip_Flop pf (
    .clk(clock_1_out), .D(alu32_1_out_11), .Q(zf_q[4]), .en(controlled_buffer_1_out_5[4]), .reset(in_1));  // open: Qn, preset
  assign {controlled_buffer_1_out_6, controlled_buffer_1_out[29:24], controlled_buffer_1_out_5, controlled_buffer_1_out_4, controlled_buffer_1_out_3, controlled_buffer_1_out_2, controlled_buffer_1_out[7:0]} = d_ff_1_q ? {2'b00, undriven} : 32'bz;  // Controlled_Buffer controlled_buffer_93
  assign out_4 = controlled_buffer_1_out[24] ? alu32_1_out_12 : 32'bz;  // Controlled_Buffer controlled_buffer_94
  assign {controlled_buffer_1_out_6, controlled_buffer_1_out[29:24], controlled_buffer_1_out_5, controlled_buffer_1_out_4, controlled_buffer_1_out_3, controlled_buffer_1_out_2, controlled_buffer_1_out[7:0]} = and_264_out ? 32'h1001f01 : 32'bz;  // Controlled_Buffer controlled_buffer_95
  assign {controlled_buffer_1_out_6, controlled_buffer_1_out[29:24], controlled_buffer_1_out_5, controlled_buffer_1_out_4, controlled_buffer_1_out_3, controlled_buffer_1_out_2, controlled_buffer_1_out[7:0]} = and_229_out ? 32'h1002f01 : 32'bz;  // Controlled_Buffer controlled_buffer_96
  assign {controlled_buffer_1_out_6, controlled_buffer_1_out[29:24], controlled_buffer_1_out_5, controlled_buffer_1_out_4, controlled_buffer_1_out_3, controlled_buffer_1_out_2, controlled_buffer_1_out[7:0]} = and_230_out ? 32'h1003f01 : 32'bz;  // Controlled_Buffer controlled_buffer_97
  assign {controlled_buffer_1_out_6, controlled_buffer_1_out[29:24], controlled_buffer_1_out_5, controlled_buffer_1_out_4, controlled_buffer_1_out_3, controlled_buffer_1_out_2, controlled_buffer_1_out[7:0]} = and_231_out ? 32'h1004f01 : 32'bz;  // Controlled_Buffer controlled_buffer_98
  assign {controlled_buffer_1_out_6, controlled_buffer_1_out[29:24], controlled_buffer_1_out_5, controlled_buffer_1_out_4, controlled_buffer_1_out_3, controlled_buffer_1_out_2, controlled_buffer_1_out[7:0]} = and_232_out ? 32'h1005f01 : 32'bz;  // Controlled_Buffer controlled_buffer_99
  assign {controlled_buffer_1_out_6, controlled_buffer_1_out[29:24], controlled_buffer_1_out_5, controlled_buffer_1_out_4, controlled_buffer_1_out_3, controlled_buffer_1_out_2, controlled_buffer_1_out[7:0]} = and_197_out ? 32'h1000f02 : 32'bz;  // Controlled_Buffer controlled_buffer_100
  assign {controlled_buffer_1_out_6, controlled_buffer_1_out[29:24], controlled_buffer_1_out_5, controlled_buffer_1_out_4, controlled_buffer_1_out_3, controlled_buffer_1_out_2, controlled_buffer_1_out[7:0]} = and_198_out ? 32'h1002f02 : 32'bz;  // Controlled_Buffer controlled_buffer_101
  assign {controlled_buffer_1_out_6, controlled_buffer_1_out[29:24], controlled_buffer_1_out_5, controlled_buffer_1_out_4, controlled_buffer_1_out_3, controlled_buffer_1_out_2, controlled_buffer_1_out[7:0]} = and_199_out ? 32'h1003f02 : 32'bz;  // Controlled_Buffer controlled_buffer_102
  assign {controlled_buffer_1_out_6, controlled_buffer_1_out[29:24], controlled_buffer_1_out_5, controlled_buffer_1_out_4, controlled_buffer_1_out_3, controlled_buffer_1_out_2, controlled_buffer_1_out[7:0]} = and_200_out ? 32'h1004f02 : 32'bz;  // Controlled_Buffer controlled_buffer_103
  assign {controlled_buffer_1_out_6, controlled_buffer_1_out[29:24], controlled_buffer_1_out_5, controlled_buffer_1_out_4, controlled_buffer_1_out_3, controlled_buffer_1_out_2, controlled_buffer_1_out[7:0]} = and_201_out ? 32'h1005f02 : 32'bz;  // Controlled_Buffer controlled_buffer_104
  assign {controlled_buffer_1_out_6, controlled_buffer_1_out[29:24], controlled_buffer_1_out_5, controlled_buffer_1_out_4, controlled_buffer_1_out_3, controlled_buffer_1_out_2, controlled_buffer_1_out[7:0]} = and_202_out ? 32'h1000f04 : 32'bz;  // Controlled_Buffer controlled_buffer_105
  assign {controlled_buffer_1_out_6, controlled_buffer_1_out[29:24], controlled_buffer_1_out_5, controlled_buffer_1_out_4, controlled_buffer_1_out_3, controlled_buffer_1_out_2, controlled_buffer_1_out[7:0]} = and_203_out ? 32'h1001f04 : 32'bz;  // Controlled_Buffer controlled_buffer_106
  assign {controlled_buffer_1_out_6, controlled_buffer_1_out[29:24], controlled_buffer_1_out_5, controlled_buffer_1_out_4, controlled_buffer_1_out_3, controlled_buffer_1_out_2, controlled_buffer_1_out[7:0]} = and_204_out ? 32'h1003f04 : 32'bz;  // Controlled_Buffer controlled_buffer_107
  assign {controlled_buffer_1_out_6, controlled_buffer_1_out[29:24], controlled_buffer_1_out_5, controlled_buffer_1_out_4, controlled_buffer_1_out_3, controlled_buffer_1_out_2, controlled_buffer_1_out[7:0]} = and_205_out ? 32'h1004f04 : 32'bz;  // Controlled_Buffer controlled_buffer_108
  assign {controlled_buffer_1_out_6, controlled_buffer_1_out[29:24], controlled_buffer_1_out_5, controlled_buffer_1_out_4, controlled_buffer_1_out_3, controlled_buffer_1_out_2, controlled_buffer_1_out[7:0]} = and_206_out ? 32'h1005f04 : 32'bz;  // Controlled_Buffer controlled_buffer_109
  assign {controlled_buffer_1_out_6, controlled_buffer_1_out[29:24], controlled_buffer_1_out_5, controlled_buffer_1_out_4, controlled_buffer_1_out_3, controlled_buffer_1_out_2, controlled_buffer_1_out[7:0]} = and_207_out ? 32'h1000f08 : 32'bz;  // Controlled_Buffer controlled_buffer_110
  assign {controlled_buffer_1_out_6, controlled_buffer_1_out[29:24], controlled_buffer_1_out_5, controlled_buffer_1_out_4, controlled_buffer_1_out_3, controlled_buffer_1_out_2, controlled_buffer_1_out[7:0]} = and_208_out ? 32'h1001f08 : 32'bz;  // Controlled_Buffer controlled_buffer_111
  assign {controlled_buffer_1_out_6, controlled_buffer_1_out[29:24], controlled_buffer_1_out_5, controlled_buffer_1_out_4, controlled_buffer_1_out_3, controlled_buffer_1_out_2, controlled_buffer_1_out[7:0]} = and_209_out ? 32'h1002f08 : 32'bz;  // Controlled_Buffer controlled_buffer_112
  assign {controlled_buffer_1_out_6, controlled_buffer_1_out[29:24], controlled_buffer_1_out_5, controlled_buffer_1_out_4, controlled_buffer_1_out_3, controlled_buffer_1_out_2, controlled_buffer_1_out[7:0]} = and_210_out ? 32'h1004f08 : 32'bz;  // Controlled_Buffer controlled_buffer_113
  assign {controlled_buffer_1_out_6, controlled_buffer_1_out[29:24], controlled_buffer_1_out_5, controlled_buffer_1_out_4, controlled_buffer_1_out_3, controlled_buffer_1_out_2, controlled_buffer_1_out[7:0]} = and_211_out ? 32'h1005f08 : 32'bz;  // Controlled_Buffer controlled_buffer_114
  assign {controlled_buffer_1_out_6, controlled_buffer_1_out[29:24], controlled_buffer_1_out_5, controlled_buffer_1_out_4, controlled_buffer_1_out_3, controlled_buffer_1_out_2, controlled_buffer_1_out[7:0]} = and_212_out ? 32'h1000f10 : 32'bz;  // Controlled_Buffer controlled_buffer_115
  assign {controlled_buffer_1_out_6, controlled_buffer_1_out[29:24], controlled_buffer_1_out_5, controlled_buffer_1_out_4, controlled_buffer_1_out_3, controlled_buffer_1_out_2, controlled_buffer_1_out[7:0]} = and_213_out ? 32'h1001f10 : 32'bz;  // Controlled_Buffer controlled_buffer_116
  assign {controlled_buffer_1_out_6, controlled_buffer_1_out[29:24], controlled_buffer_1_out_5, controlled_buffer_1_out_4, controlled_buffer_1_out_3, controlled_buffer_1_out_2, controlled_buffer_1_out[7:0]} = and_214_out ? 32'h1002f10 : 32'bz;  // Controlled_Buffer controlled_buffer_117
  assign {controlled_buffer_1_out_6, controlled_buffer_1_out[29:24], controlled_buffer_1_out_5, controlled_buffer_1_out_4, controlled_buffer_1_out_3, controlled_buffer_1_out_2, controlled_buffer_1_out[7:0]} = and_215_out ? 32'h1003f10 : 32'bz;  // Controlled_Buffer controlled_buffer_118
  assign {controlled_buffer_1_out_6, controlled_buffer_1_out[29:24], controlled_buffer_1_out_5, controlled_buffer_1_out_4, controlled_buffer_1_out_3, controlled_buffer_1_out_2, controlled_buffer_1_out[7:0]} = and_216_out ? 32'h1005f10 : 32'bz;  // Controlled_Buffer controlled_buffer_119
  assign {controlled_buffer_1_out_6, controlled_buffer_1_out[29:24], controlled_buffer_1_out_5, controlled_buffer_1_out_4, controlled_buffer_1_out_3, controlled_buffer_1_out_2, controlled_buffer_1_out[7:0]} = and_217_out ? 32'h1000f20 : 32'bz;  // Controlled_Buffer controlled_buffer_120
  assign {controlled_buffer_1_out_6, controlled_buffer_1_out[29:24], controlled_buffer_1_out_5, controlled_buffer_1_out_4, controlled_buffer_1_out_3, controlled_buffer_1_out_2, controlled_buffer_1_out[7:0]} = and_218_out ? 32'h1001f20 : 32'bz;  // Controlled_Buffer controlled_buffer_121
  assign {controlled_buffer_1_out_6, controlled_buffer_1_out[29:24], controlled_buffer_1_out_5, controlled_buffer_1_out_4, controlled_buffer_1_out_3, controlled_buffer_1_out_2, controlled_buffer_1_out[7:0]} = and_219_out ? 32'h1002f20 : 32'bz;  // Controlled_Buffer controlled_buffer_122
  assign {controlled_buffer_1_out_6, controlled_buffer_1_out[29:24], controlled_buffer_1_out_5, controlled_buffer_1_out_4, controlled_buffer_1_out_3, controlled_buffer_1_out_2, controlled_buffer_1_out[7:0]} = and_220_out ? 32'h1003f20 : 32'bz;  // Controlled_Buffer controlled_buffer_123
  assign {controlled_buffer_1_out_6, controlled_buffer_1_out[29:24], controlled_buffer_1_out_5, controlled_buffer_1_out_4, controlled_buffer_1_out_3, controlled_buffer_1_out_2, controlled_buffer_1_out[7:0]} = and_221_out ? 32'h1004f20 : 32'bz;  // Controlled_Buffer controlled_buffer_124
  assign {controlled_buffer_1_out_6, controlled_buffer_1_out[29:24], controlled_buffer_1_out_5, controlled_buffer_1_out_4, controlled_buffer_1_out_3, controlled_buffer_1_out_2, controlled_buffer_1_out[7:0]} = and_222_out ? 32'h1000f40 : 32'bz;  // Controlled_Buffer controlled_buffer_125
  assign {controlled_buffer_1_out_6, controlled_buffer_1_out[29:24], controlled_buffer_1_out_5, controlled_buffer_1_out_4, controlled_buffer_1_out_3, controlled_buffer_1_out_2, controlled_buffer_1_out[7:0]} = and_223_out ? 32'h1001f40 : 32'bz;  // Controlled_Buffer controlled_buffer_126
  assign {controlled_buffer_1_out_6, controlled_buffer_1_out[29:24], controlled_buffer_1_out_5, controlled_buffer_1_out_4, controlled_buffer_1_out_3, controlled_buffer_1_out_2, controlled_buffer_1_out[7:0]} = and_224_out ? 32'h1002f40 : 32'bz;  // Controlled_Buffer controlled_buffer_127
  assign {controlled_buffer_1_out_6, controlled_buffer_1_out[29:24], controlled_buffer_1_out_5, controlled_buffer_1_out_4, controlled_buffer_1_out_3, controlled_buffer_1_out_2, controlled_buffer_1_out[7:0]} = and_225_out ? 32'h1003f40 : 32'bz;  // Controlled_Buffer controlled_buffer_128
  assign {controlled_buffer_1_out_6, controlled_buffer_1_out[29:24], controlled_buffer_1_out_5, controlled_buffer_1_out_4, controlled_buffer_1_out_3, controlled_buffer_1_out_2, controlled_buffer_1_out[7:0]} = and_226_out ? 32'h1004f40 : 32'bz;  // Controlled_Buffer controlled_buffer_129
  assign {controlled_buffer_1_out_6, controlled_buffer_1_out[29:24], controlled_buffer_1_out_5, controlled_buffer_1_out_4, controlled_buffer_1_out_3, controlled_buffer_1_out_2, controlled_buffer_1_out[7:0]} = and_227_out ? 32'h1005f40 : 32'bz;  // Controlled_Buffer controlled_buffer_130
  assign controlled_buffer_131_out = controlled_buffer_1_out[28] ? controlled_buffer_138_out : 32'bz;  // Controlled_Buffer controlled_buffer_131
  D_Flip_Flop d_ff_1 (.clk(clock_1_out), .D(d_ff_2_q), .Q(d_ff_1_q));  // open: Qn, preset, en, reset
  eip2 eip2_1 (
    .in_1(d_ff_1_q), .in_2(controlled_buffer_1_out[28]), .in_3(controlled_buffer_132_out), .out_6(out_5),
    .in_5(in_2), .in_4(controlled_buffer_1_out[29]));
  assign controlled_buffer_132_out = controlled_buffer_1_out[28] ? controlled_buffer_131_out[15:0] : 16'bz;  // Controlled_Buffer controlled_buffer_132
  and and_197 (and_197_out, and_233_out, d_ff_1_q);
  and and_198 (and_198_out, and_234_out, d_ff_1_q);
  and and_199 (and_199_out, and_235_out, d_ff_1_q);
  and and_200 (and_200_out, and_236_out, d_ff_1_q);
  and and_201 (and_201_out, and_237_out, d_ff_1_q);
  and and_202 (and_202_out, and_238_out, d_ff_1_q);
  and and_203 (and_203_out, and_239_out, d_ff_1_q);
  and and_204 (and_204_out, and_240_out, d_ff_1_q);
  and and_205 (and_205_out, and_241_out, d_ff_1_q);
  and and_206 (and_206_out, and_242_out, d_ff_1_q);
  and and_207 (and_207_out, and_243_out, d_ff_1_q);
  and and_208 (and_208_out, and_244_out, d_ff_1_q);
  and and_209 (and_209_out, and_245_out, d_ff_1_q);
  and and_210 (and_210_out, and_246_out, d_ff_1_q);
  and and_211 (and_211_out, and_247_out, d_ff_1_q);
  and and_212 (and_212_out, and_248_out, d_ff_1_q);
  and and_213 (and_213_out, and_249_out, d_ff_1_q);
  and and_214 (and_214_out, and_250_out, d_ff_1_q);
  and and_215 (and_215_out, and_251_out, d_ff_1_q);
  and and_216 (and_216_out, and_252_out, d_ff_1_q);
  and and_217 (and_217_out, and_253_out, d_ff_1_q);
  and and_218 (and_218_out, and_254_out, d_ff_1_q);
  and and_219 (and_219_out, and_255_out, d_ff_1_q);
  and and_220 (and_220_out, and_256_out, d_ff_1_q);
  and and_221 (and_221_out, and_257_out, d_ff_1_q);
  and and_222 (and_222_out, and_258_out, d_ff_1_q);
  and and_223 (and_223_out, and_259_out, d_ff_1_q);
  and and_224 (and_224_out, and_260_out, d_ff_1_q);
  and and_225 (and_225_out, and_261_out, d_ff_1_q);
  and and_226 (and_226_out, and_262_out, d_ff_1_q);
  and and_227 (and_227_out, and_263_out, d_ff_1_q);
  and and_228 (and_228_out, d_ff_1_q, ~d_ff_2_q);  // AND_Gate
  and and_229 (and_229_out, d_ff_1_q, and_317_out, and_266_out);
  and and_230 (and_230_out, d_ff_1_q, and_317_out, and_267_out);
  and and_231 (and_231_out, and_317_out, and_268_out, d_ff_1_q);
  and and_232 (and_232_out, and_317_out, and_269_out, d_ff_1_q);
  and and_233 (and_233_out, and_317_out, and_311_out, and_270_out);
  and and_234 (and_234_out, and_317_out, and_311_out, and_271_out);
  and and_235 (and_235_out, and_317_out, and_311_out, and_272_out);
  and and_236 (and_236_out, and_317_out, and_311_out, and_273_out);
  and and_237 (and_237_out, and_317_out, and_311_out, and_274_out);
  and and_238 (and_238_out, and_317_out, and_312_out, and_275_out);
  and and_239 (and_239_out, and_317_out, and_312_out, and_276_out);
  and and_240 (and_240_out, and_317_out, and_312_out, and_277_out);
  and and_241 (and_241_out, and_317_out, and_312_out, and_278_out);
  and and_242 (and_242_out, and_317_out, and_312_out, and_279_out);
  and and_243 (and_243_out, and_317_out, and_313_out, and_280_out);
  and and_244 (and_244_out, and_317_out, and_313_out, and_281_out);
  and and_245 (and_245_out, and_317_out, and_313_out, and_282_out);
  and and_246 (and_246_out, and_317_out, and_313_out, and_283_out);
  and and_247 (and_247_out, and_317_out, and_313_out, and_284_out);
  and and_248 (and_248_out, and_317_out, and_314_out, and_285_out);
  and and_249 (and_249_out, and_317_out, and_314_out, and_286_out);
  and and_250 (and_250_out, and_317_out, and_314_out, and_287_out);
  and and_251 (and_251_out, and_317_out, and_314_out, and_288_out);
  and and_252 (and_252_out, and_317_out, and_314_out, and_289_out);
  and and_253 (and_253_out, and_317_out, and_315_out, and_290_out);
  and and_254 (and_254_out, and_317_out, and_315_out, and_291_out);
  and and_255 (and_255_out, and_317_out, and_315_out, and_292_out);
  and and_256 (and_256_out, and_317_out, and_315_out, and_293_out);
  and and_257 (and_257_out, and_317_out, and_315_out, and_294_out);
  and and_258 (and_258_out, and_317_out, and_316_out, and_295_out);
  and and_259 (and_259_out, and_317_out, and_316_out, and_296_out);
  and and_260 (and_260_out, and_317_out, and_316_out, and_297_out);
  and and_261 (and_261_out, and_317_out, and_316_out, and_298_out);
  and and_262 (and_262_out, and_317_out, and_316_out, and_299_out);
  and and_263 (and_263_out, and_317_out, and_316_out, and_300_out);
  D_Flip_Flop d_ff_2 (.clk(clock_1_out), .D(and_228_out), .Q(d_ff_2_q));  // open: Qn, preset, en, reset
  and and_264 (and_264_out, d_ff_1_q, and_317_out, and_265_out);
  and and_265 (and_265_out, and_301_out, and_302_out);
  and and_266 (and_266_out, and_303_out, and_304_out);
  and and_267 (and_267_out, and_305_out, and_306_out);
  and and_268 (and_268_out, and_307_out, and_308_out);
  and and_269 (and_269_out, and_309_out, and_310_out);
  and and_270 (and_270_out, ~controlled_buffer_140_out[15], ~controlled_buffer_140_out[14], ~controlled_buffer_140_out[13], ~controlled_buffer_140_out[12]);  // AND_Gate
  and and_271 (and_271_out, ~controlled_buffer_140_out[15], ~controlled_buffer_140_out[14], controlled_buffer_140_out[13], ~controlled_buffer_140_out[12]);  // AND_Gate
  and and_272 (and_272_out, ~controlled_buffer_140_out[15], ~controlled_buffer_140_out[14], controlled_buffer_140_out[13], controlled_buffer_140_out[12]);  // AND_Gate
  and and_273 (and_273_out, ~controlled_buffer_140_out[15], controlled_buffer_140_out[14], ~controlled_buffer_140_out[13], ~controlled_buffer_140_out[12]);  // AND_Gate
  and and_274 (and_274_out, ~controlled_buffer_140_out[15], controlled_buffer_140_out[14], ~controlled_buffer_140_out[13], controlled_buffer_140_out[12]);  // AND_Gate
  and and_275 (and_275_out, ~controlled_buffer_140_out[15], ~controlled_buffer_140_out[14], ~controlled_buffer_140_out[13], ~controlled_buffer_140_out[12]);  // AND_Gate
  and and_276 (and_276_out, ~controlled_buffer_140_out[15], ~controlled_buffer_140_out[14], ~controlled_buffer_140_out[13], controlled_buffer_140_out[12]);  // AND_Gate
  and and_277 (and_277_out, ~controlled_buffer_140_out[15], ~controlled_buffer_140_out[14], controlled_buffer_140_out[13], controlled_buffer_140_out[12]);  // AND_Gate
  and and_278 (and_278_out, ~controlled_buffer_140_out[15], controlled_buffer_140_out[14], ~controlled_buffer_140_out[13], ~controlled_buffer_140_out[12]);  // AND_Gate
  and and_279 (and_279_out, ~controlled_buffer_140_out[15], controlled_buffer_140_out[14], ~controlled_buffer_140_out[13], controlled_buffer_140_out[12]);  // AND_Gate
  and and_280 (and_280_out, ~controlled_buffer_140_out[15], ~controlled_buffer_140_out[14], ~controlled_buffer_140_out[13], ~controlled_buffer_140_out[12]);  // AND_Gate
  and and_281 (and_281_out, ~controlled_buffer_140_out[15], ~controlled_buffer_140_out[14], ~controlled_buffer_140_out[13], controlled_buffer_140_out[12]);  // AND_Gate
  and and_282 (and_282_out, ~controlled_buffer_140_out[15], ~controlled_buffer_140_out[14], controlled_buffer_140_out[13], ~controlled_buffer_140_out[12]);  // AND_Gate
  and and_283 (and_283_out, ~controlled_buffer_140_out[15], controlled_buffer_140_out[14], ~controlled_buffer_140_out[13], ~controlled_buffer_140_out[12]);  // AND_Gate
  and and_284 (and_284_out, ~controlled_buffer_140_out[15], controlled_buffer_140_out[14], ~controlled_buffer_140_out[13], controlled_buffer_140_out[12]);  // AND_Gate
  and and_285 (and_285_out, ~controlled_buffer_140_out[15], ~controlled_buffer_140_out[14], ~controlled_buffer_140_out[13], ~controlled_buffer_140_out[12]);  // AND_Gate
  and and_286 (and_286_out, ~controlled_buffer_140_out[15], ~controlled_buffer_140_out[14], ~controlled_buffer_140_out[13], controlled_buffer_140_out[12]);  // AND_Gate
  and and_287 (and_287_out, ~controlled_buffer_140_out[15], ~controlled_buffer_140_out[14], controlled_buffer_140_out[13], ~controlled_buffer_140_out[12]);  // AND_Gate
  and and_288 (and_288_out, ~controlled_buffer_140_out[15], ~controlled_buffer_140_out[14], controlled_buffer_140_out[13], controlled_buffer_140_out[12]);  // AND_Gate
  and and_289 (and_289_out, ~controlled_buffer_140_out[15], controlled_buffer_140_out[14], ~controlled_buffer_140_out[13], controlled_buffer_140_out[12]);  // AND_Gate
  and and_290 (and_290_out, ~controlled_buffer_140_out[15], ~controlled_buffer_140_out[14], ~controlled_buffer_140_out[13], ~controlled_buffer_140_out[12]);  // AND_Gate
  and and_291 (and_291_out, ~controlled_buffer_140_out[15], ~controlled_buffer_140_out[14], ~controlled_buffer_140_out[13], controlled_buffer_140_out[12]);  // AND_Gate
  and and_292 (and_292_out, ~controlled_buffer_140_out[15], ~controlled_buffer_140_out[14], controlled_buffer_140_out[13], ~controlled_buffer_140_out[12]);  // AND_Gate
  and and_293 (and_293_out, ~controlled_buffer_140_out[15], ~controlled_buffer_140_out[14], controlled_buffer_140_out[13], controlled_buffer_140_out[12]);  // AND_Gate
  and and_294 (and_294_out, ~controlled_buffer_140_out[15], controlled_buffer_140_out[14], ~controlled_buffer_140_out[13], ~controlled_buffer_140_out[12]);  // AND_Gate
  and and_295 (and_295_out, ~controlled_buffer_140_out[15], ~controlled_buffer_140_out[14], ~controlled_buffer_140_out[13], ~controlled_buffer_140_out[12]);  // AND_Gate
  and and_296 (and_296_out, ~controlled_buffer_140_out[15], ~controlled_buffer_140_out[14], ~controlled_buffer_140_out[13], controlled_buffer_140_out[12]);  // AND_Gate
  and and_297 (and_297_out, ~controlled_buffer_140_out[15], ~controlled_buffer_140_out[14], controlled_buffer_140_out[13], ~controlled_buffer_140_out[12]);  // AND_Gate
  and and_298 (and_298_out, ~controlled_buffer_140_out[15], ~controlled_buffer_140_out[14], controlled_buffer_140_out[13], controlled_buffer_140_out[12]);  // AND_Gate
  and and_299 (and_299_out, ~controlled_buffer_140_out[15], controlled_buffer_140_out[14], ~controlled_buffer_140_out[13], ~controlled_buffer_140_out[12]);  // AND_Gate
  and and_300 (and_300_out, ~controlled_buffer_140_out[15], controlled_buffer_140_out[14], ~controlled_buffer_140_out[13], controlled_buffer_140_out[12]);  // AND_Gate
  and and_301 (and_301_out, ~controlled_buffer_140_out[15], ~controlled_buffer_140_out[14], ~controlled_buffer_140_out[13], controlled_buffer_140_out[12]);  // AND_Gate
  and and_302 (and_302_out, ~controlled_buffer_140_out[11], ~controlled_buffer_140_out[10], ~controlled_buffer_140_out[9], ~controlled_buffer_140_out[8]);  // AND_Gate
  and and_303 (and_303_out, ~controlled_buffer_140_out[15], ~controlled_buffer_140_out[14], controlled_buffer_140_out[13], ~controlled_buffer_140_out[12]);  // AND_Gate
  and and_304 (and_304_out, ~controlled_buffer_140_out[11], ~controlled_buffer_140_out[10], ~controlled_buffer_140_out[9], ~controlled_buffer_140_out[8]);  // AND_Gate
  and and_305 (and_305_out, ~controlled_buffer_140_out[15], ~controlled_buffer_140_out[14], controlled_buffer_140_out[13], controlled_buffer_140_out[12]);  // AND_Gate
  and and_306 (and_306_out, ~controlled_buffer_140_out[11], ~controlled_buffer_140_out[10], ~controlled_buffer_140_out[9], ~controlled_buffer_140_out[8]);  // AND_Gate
  and and_307 (and_307_out, ~controlled_buffer_140_out[15], controlled_buffer_140_out[14], ~controlled_buffer_140_out[13], ~controlled_buffer_140_out[12]);  // AND_Gate
  and and_308 (and_308_out, ~controlled_buffer_140_out[11], ~controlled_buffer_140_out[10], ~controlled_buffer_140_out[9], ~controlled_buffer_140_out[8]);  // AND_Gate
  and and_309 (and_309_out, ~controlled_buffer_140_out[15], controlled_buffer_140_out[14], ~controlled_buffer_140_out[13], controlled_buffer_140_out[12]);  // AND_Gate
  and and_310 (and_310_out, ~controlled_buffer_140_out[11], ~controlled_buffer_140_out[10], ~controlled_buffer_140_out[9], ~controlled_buffer_140_out[8]);  // AND_Gate
  and and_311 (and_311_out, ~controlled_buffer_140_out[11], ~controlled_buffer_140_out[10], ~controlled_buffer_140_out[9], controlled_buffer_140_out[8]);  // AND_Gate
  and and_312 (and_312_out, ~controlled_buffer_140_out[11], ~controlled_buffer_140_out[10], controlled_buffer_140_out[9], ~controlled_buffer_140_out[8]);  // AND_Gate
  and and_313 (and_313_out, ~controlled_buffer_140_out[11], ~controlled_buffer_140_out[10], controlled_buffer_140_out[9], controlled_buffer_140_out[8]);  // AND_Gate
  and and_314 (and_314_out, ~controlled_buffer_140_out[11], controlled_buffer_140_out[10], ~controlled_buffer_140_out[9], ~controlled_buffer_140_out[8]);  // AND_Gate
  and and_315 (and_315_out, ~controlled_buffer_140_out[11], controlled_buffer_140_out[10], ~controlled_buffer_140_out[9], controlled_buffer_140_out[8]);  // AND_Gate
  and and_316 (and_316_out, ~controlled_buffer_140_out[11], controlled_buffer_140_out[10], controlled_buffer_140_out[9], ~controlled_buffer_140_out[8]);  // AND_Gate
  and and_317 (and_317_out, ~controlled_buffer_140_out[7], ~controlled_buffer_140_out[6], ~controlled_buffer_140_out[5], ~controlled_buffer_140_out[4], ~controlled_buffer_140_out[3], ~controlled_buffer_140_out[2], ~controlled_buffer_140_out[1], controlled_buffer_140_out[0]);  // AND_Gate
  Multiplexer #(.select(2), .width(16), .enable("false")) multiplexer_3 (
    .in0(out_5), .in1(register_7_q), .in2(register_8_q), .out(multiplexer_3_out),
    .sel(controlled_buffer_1_out_6));  // open: in3
  not not_1 (not_1_out, controlled_buffer_133_out);
  assign controlled_buffer_133_out = d_ff_1_q ? not_2_out : 1'bz;  // Controlled_Buffer controlled_buffer_133
  not not_2 (not_2_out, d_ff_1_q);
  RAM #(.addrWidth(16), .dataWidth(32), .bus("asynch")) ram_1 (
    .addr(multiplexer_3_out), .data(ram_1_data), .sel(1'b1), .ld(not_1_out));  // open: clr
  assign controlled_buffer_133_out = and_318_out ? and_322_out : 1'bz;  // Controlled_Buffer controlled_buffer_134
  not not_3 (not_3_out, and_322_out);
  assign controlled_buffer_133_out = and_319_out ? not_3_out : 1'bz;  // Controlled_Buffer controlled_buffer_135
  not not_4 (not_4_out, and_322_out);
  and and_318 (and_318_out, xor_1_out, and_321_out);
  and and_319 (and_319_out, and_320_out, xor_1_out);
  xor xor_1 (xor_1_out, and_320_out, and_321_out);
  and and_320 (and_320_out, controlled_buffer_1_out[26], and_322_out);
  and and_321 (and_321_out, controlled_buffer_1_out[27], and_322_out);
  assign ram_1_data = and_318_out ? out_4 : 32'bz;  // Controlled_Buffer controlled_buffer_136
  assign out_4 = and_319_out ? ram_1_data : 32'bz;  // Controlled_Buffer controlled_buffer_137
  and and_322 (and_322_out, not_5_out, controlled_buffer_1_out[25]);
  not not_5 (not_5_out, d_ff_1_q);
  assign controlled_buffer_138_out = xor_4_out ? {{16{1'b0}}, controlled_buffer_140_out[31:16]} : 32'bz;  // Controlled_Buffer controlled_buffer_138
  assign controlled_buffer_139_out = d_ff_1_q ? ram_1_data : 32'bz;  // Controlled_Buffer controlled_buffer_139
  Register #(.width(32), .trigger("falling")) register_9 (
    .D(controlled_buffer_139_out), .en(d_ff_1_q), .Q(register_9_q), .clk(clock_1_out));  // open: clr
  assign controlled_buffer_140_out = d_ff_2_q ? register_9_q : 32'bz;  // Controlled_Buffer controlled_buffer_140
  assign controlled_buffer_140_out = d_ff_1_q ? controlled_buffer_139_out : 32'bz;  // Controlled_Buffer controlled_buffer_141
  and and_323 (and_323_out, ~controlled_buffer_140_out[7], ~controlled_buffer_140_out[6], ~controlled_buffer_140_out[5], ~controlled_buffer_140_out[4], controlled_buffer_140_out[3], ~controlled_buffer_140_out[2], ~controlled_buffer_140_out[1], ~controlled_buffer_140_out[0]);  // AND_Gate
  and and_324 (and_324_out[0], zf_q[0], zf_q[1]);
  and and_325 (and_324_out[1], ~zf_q[0], ~zf_q[1]);  // AND_Gate
  and and_326 (and_326_out, ~controlled_buffer_140_out[15], ~controlled_buffer_140_out[14], ~controlled_buffer_140_out[13], ~controlled_buffer_140_out[12], ~controlled_buffer_140_out[11], controlled_buffer_140_out[10], ~controlled_buffer_140_out[9], controlled_buffer_140_out[8]);  // AND_Gate
  and and_327 (and_327_out, ~controlled_buffer_140_out[15], ~controlled_buffer_140_out[14], ~controlled_buffer_140_out[13], ~controlled_buffer_140_out[12], ~controlled_buffer_140_out[11], controlled_buffer_140_out[10], ~controlled_buffer_140_out[9], ~controlled_buffer_140_out[8]);  // AND_Gate
  and and_328 (and_328_out, ~controlled_buffer_140_out[15], ~controlled_buffer_140_out[14], ~controlled_buffer_140_out[13], ~controlled_buffer_140_out[12], ~controlled_buffer_140_out[11], ~controlled_buffer_140_out[10], controlled_buffer_140_out[9], controlled_buffer_140_out[8]);  // AND_Gate
  and and_329 (and_329_out, ~controlled_buffer_140_out[15], ~controlled_buffer_140_out[14], ~controlled_buffer_140_out[13], ~controlled_buffer_140_out[12], ~controlled_buffer_140_out[11], ~controlled_buffer_140_out[10], controlled_buffer_140_out[9], ~controlled_buffer_140_out[8]);  // AND_Gate
  and and_330 (and_330_out, ~controlled_buffer_140_out[15], ~controlled_buffer_140_out[14], ~controlled_buffer_140_out[13], ~controlled_buffer_140_out[12], ~controlled_buffer_140_out[11], ~controlled_buffer_140_out[10], ~controlled_buffer_140_out[9], controlled_buffer_140_out[8]);  // AND_Gate
  and and_331 (and_331_out, ~controlled_buffer_140_out[15], ~controlled_buffer_140_out[14], ~controlled_buffer_140_out[13], ~controlled_buffer_140_out[12], ~controlled_buffer_140_out[11], ~controlled_buffer_140_out[10], ~controlled_buffer_140_out[9], ~controlled_buffer_140_out[8]);  // AND_Gate
  assign {controlled_buffer_1_out_6, controlled_buffer_1_out[29:24], controlled_buffer_1_out_5, controlled_buffer_1_out_4, controlled_buffer_1_out_3, controlled_buffer_1_out_2, controlled_buffer_1_out[7:0]} = and_380_out ? 32'h1f95400 : 32'bz;  // Controlled_Buffer controlled_buffer_142
  and and_332 (and_324_out[2], ~zf_q[0], zf_q[1]);  // AND_Gate
  and and_333 (and_333_out, and_331_out, and_323_out);
  and and_334 (and_334_out, zf_q[0], zf_q[1]);
  xor xor_2 (and_324_out[3], and_334_out, and_341_out);
  and and_335 (and_335_out, and_326_out, and_323_out);
  and and_336 (and_336_out, and_327_out, and_323_out);
  and and_337 (and_337_out, and_328_out, and_323_out);
  and and_338 (and_338_out, and_329_out, and_323_out);
  and and_339 (and_339_out, and_330_out, and_323_out);
  and and_340 (and_340_out, and_323_out, and_333_out, d_ff_2_q);
  assign {controlled_buffer_1_out_6, controlled_buffer_1_out[29:24], controlled_buffer_1_out_5, controlled_buffer_1_out_4, controlled_buffer_1_out_3, controlled_buffer_1_out_2, controlled_buffer_1_out[7:0]} = and_355_out ? 32'h1f93000 : 32'bz;  // Controlled_Buffer controlled_buffer_143
  assign {controlled_buffer_1_out_6, controlled_buffer_1_out[29:24], controlled_buffer_1_out_5, controlled_buffer_1_out_4, controlled_buffer_1_out_3, controlled_buffer_1_out_2, controlled_buffer_1_out[7:0]} = and_356_out ? 32'h1f94000 : 32'bz;  // Controlled_Buffer controlled_buffer_144
  assign {controlled_buffer_1_out_6, controlled_buffer_1_out[29:24], controlled_buffer_1_out_5, controlled_buffer_1_out_4, controlled_buffer_1_out_3, controlled_buffer_1_out_2, controlled_buffer_1_out[7:0]} = and_357_out ? 32'h1f95000 : 32'bz;  // Controlled_Buffer controlled_buffer_145
  assign {controlled_buffer_1_out_6, controlled_buffer_1_out[29:24], controlled_buffer_1_out_5, controlled_buffer_1_out_4, controlled_buffer_1_out_3, controlled_buffer_1_out_2, controlled_buffer_1_out[7:0]} = and_358_out ? 32'h1f90100 : 32'bz;  // Controlled_Buffer controlled_buffer_146
  assign {controlled_buffer_1_out_6, controlled_buffer_1_out[29:24], controlled_buffer_1_out_5, controlled_buffer_1_out_4, controlled_buffer_1_out_3, controlled_buffer_1_out_2, controlled_buffer_1_out[7:0]} = and_359_out ? 32'h1f91100 : 32'bz;  // Controlled_Buffer controlled_buffer_147
  assign {controlled_buffer_1_out_6, controlled_buffer_1_out[29:24], controlled_buffer_1_out_5, controlled_buffer_1_out_4, controlled_buffer_1_out_3, controlled_buffer_1_out_2, controlled_buffer_1_out[7:0]} = and_360_out ? 32'h1f92100 : 32'bz;  // Controlled_Buffer controlled_buffer_148
  assign {controlled_buffer_1_out_6, controlled_buffer_1_out[29:24], controlled_buffer_1_out_5, controlled_buffer_1_out_4, controlled_buffer_1_out_3, controlled_buffer_1_out_2, controlled_buffer_1_out[7:0]} = and_361_out ? 32'h1f93100 : 32'bz;  // Controlled_Buffer controlled_buffer_149
  assign {controlled_buffer_1_out_6, controlled_buffer_1_out[29:24], controlled_buffer_1_out_5, controlled_buffer_1_out_4, controlled_buffer_1_out_3, controlled_buffer_1_out_2, controlled_buffer_1_out[7:0]} = and_362_out ? 32'h1f94100 : 32'bz;  // Controlled_Buffer controlled_buffer_150
  assign {controlled_buffer_1_out_6, controlled_buffer_1_out[29:24], controlled_buffer_1_out_5, controlled_buffer_1_out_4, controlled_buffer_1_out_3, controlled_buffer_1_out_2, controlled_buffer_1_out[7:0]} = and_363_out ? 32'h1f95100 : 32'bz;  // Controlled_Buffer controlled_buffer_151
  assign {controlled_buffer_1_out_6, controlled_buffer_1_out[29:24], controlled_buffer_1_out_5, controlled_buffer_1_out_4, controlled_buffer_1_out_3, controlled_buffer_1_out_2, controlled_buffer_1_out[7:0]} = and_364_out ? 32'h1f90200 : 32'bz;  // Controlled_Buffer controlled_buffer_152
  assign {controlled_buffer_1_out_6, controlled_buffer_1_out[29:24], controlled_buffer_1_out_5, controlled_buffer_1_out_4, controlled_buffer_1_out_3, controlled_buffer_1_out_2, controlled_buffer_1_out[7:0]} = and_365_out ? 32'h1f91200 : 32'bz;  // Controlled_Buffer controlled_buffer_153
  assign {controlled_buffer_1_out_6, controlled_buffer_1_out[29:24], controlled_buffer_1_out_5, controlled_buffer_1_out_4, controlled_buffer_1_out_3, controlled_buffer_1_out_2, controlled_buffer_1_out[7:0]} = and_366_out ? 32'h1f92200 : 32'bz;  // Controlled_Buffer controlled_buffer_154
  assign {controlled_buffer_1_out_6, controlled_buffer_1_out[29:24], controlled_buffer_1_out_5, controlled_buffer_1_out_4, controlled_buffer_1_out_3, controlled_buffer_1_out_2, controlled_buffer_1_out[7:0]} = and_367_out ? 32'h1f93200 : 32'bz;  // Controlled_Buffer controlled_buffer_155
  assign {controlled_buffer_1_out_6, controlled_buffer_1_out[29:24], controlled_buffer_1_out_5, controlled_buffer_1_out_4, controlled_buffer_1_out_3, controlled_buffer_1_out_2, controlled_buffer_1_out[7:0]} = and_368_out ? 32'h1f94200 : 32'bz;  // Controlled_Buffer controlled_buffer_156
  assign {controlled_buffer_1_out_6, controlled_buffer_1_out[29:24], controlled_buffer_1_out_5, controlled_buffer_1_out_4, controlled_buffer_1_out_3, controlled_buffer_1_out_2, controlled_buffer_1_out[7:0]} = and_369_out ? 32'h1f95200 : 32'bz;  // Controlled_Buffer controlled_buffer_157
  assign {controlled_buffer_1_out_6, controlled_buffer_1_out[29:24], controlled_buffer_1_out_5, controlled_buffer_1_out_4, controlled_buffer_1_out_3, controlled_buffer_1_out_2, controlled_buffer_1_out[7:0]} = and_370_out ? 32'h1f90300 : 32'bz;  // Controlled_Buffer controlled_buffer_158
  assign {controlled_buffer_1_out_6, controlled_buffer_1_out[29:24], controlled_buffer_1_out_5, controlled_buffer_1_out_4, controlled_buffer_1_out_3, controlled_buffer_1_out_2, controlled_buffer_1_out[7:0]} = and_371_out ? 32'h1f91300 : 32'bz;  // Controlled_Buffer controlled_buffer_159
  assign {controlled_buffer_1_out_6, controlled_buffer_1_out[29:24], controlled_buffer_1_out_5, controlled_buffer_1_out_4, controlled_buffer_1_out_3, controlled_buffer_1_out_2, controlled_buffer_1_out[7:0]} = and_372_out ? 32'h1f92300 : 32'bz;  // Controlled_Buffer controlled_buffer_160
  assign {controlled_buffer_1_out_6, controlled_buffer_1_out[29:24], controlled_buffer_1_out_5, controlled_buffer_1_out_4, controlled_buffer_1_out_3, controlled_buffer_1_out_2, controlled_buffer_1_out[7:0]} = and_373_out ? 32'h1f93300 : 32'bz;  // Controlled_Buffer controlled_buffer_161
  assign {controlled_buffer_1_out_6, controlled_buffer_1_out[29:24], controlled_buffer_1_out_5, controlled_buffer_1_out_4, controlled_buffer_1_out_3, controlled_buffer_1_out_2, controlled_buffer_1_out[7:0]} = and_374_out ? 32'h1f94300 : 32'bz;  // Controlled_Buffer controlled_buffer_162
  assign {controlled_buffer_1_out_6, controlled_buffer_1_out[29:24], controlled_buffer_1_out_5, controlled_buffer_1_out_4, controlled_buffer_1_out_3, controlled_buffer_1_out_2, controlled_buffer_1_out[7:0]} = and_375_out ? 32'h1f90400 : 32'bz;  // Controlled_Buffer controlled_buffer_163
  assign {controlled_buffer_1_out_6, controlled_buffer_1_out[29:24], controlled_buffer_1_out_5, controlled_buffer_1_out_4, controlled_buffer_1_out_3, controlled_buffer_1_out_2, controlled_buffer_1_out[7:0]} = and_376_out ? 32'h1f91400 : 32'bz;  // Controlled_Buffer controlled_buffer_164
  assign {controlled_buffer_1_out_6, controlled_buffer_1_out[29:24], controlled_buffer_1_out_5, controlled_buffer_1_out_4, controlled_buffer_1_out_3, controlled_buffer_1_out_2, controlled_buffer_1_out[7:0]} = and_377_out ? 32'h1f92400 : 32'bz;  // Controlled_Buffer controlled_buffer_165
  assign {controlled_buffer_1_out_6, controlled_buffer_1_out[29:24], controlled_buffer_1_out_5, controlled_buffer_1_out_4, controlled_buffer_1_out_3, controlled_buffer_1_out_2, controlled_buffer_1_out[7:0]} = and_378_out ? 32'h1f93400 : 32'bz;  // Controlled_Buffer controlled_buffer_166
  assign {controlled_buffer_1_out_6, controlled_buffer_1_out[29:24], controlled_buffer_1_out_5, controlled_buffer_1_out_4, controlled_buffer_1_out_3, controlled_buffer_1_out_2, controlled_buffer_1_out[7:0]} = and_379_out ? 32'h1f94400 : 32'bz;  // Controlled_Buffer controlled_buffer_167
  assign {controlled_buffer_1_out_6, controlled_buffer_1_out[29:24], controlled_buffer_1_out_5, controlled_buffer_1_out_4, controlled_buffer_1_out_3, controlled_buffer_1_out_2, controlled_buffer_1_out[7:0]} = and_381_out ? 32'h1f90500 : 32'bz;  // Controlled_Buffer controlled_buffer_168
  assign {controlled_buffer_1_out_6, controlled_buffer_1_out[29:24], controlled_buffer_1_out_5, controlled_buffer_1_out_4, controlled_buffer_1_out_3, controlled_buffer_1_out_2, controlled_buffer_1_out[7:0]} = and_382_out ? 32'h1f91500 : 32'bz;  // Controlled_Buffer controlled_buffer_169
  assign {controlled_buffer_1_out_6, controlled_buffer_1_out[29:24], controlled_buffer_1_out_5, controlled_buffer_1_out_4, controlled_buffer_1_out_3, controlled_buffer_1_out_2, controlled_buffer_1_out[7:0]} = and_383_out ? 32'h1f92500 : 32'bz;  // Controlled_Buffer controlled_buffer_170
  assign {controlled_buffer_1_out_6, controlled_buffer_1_out[29:24], controlled_buffer_1_out_5, controlled_buffer_1_out_4, controlled_buffer_1_out_3, controlled_buffer_1_out_2, controlled_buffer_1_out[7:0]} = and_384_out ? 32'h1f93500 : 32'bz;  // Controlled_Buffer controlled_buffer_171
  assign {controlled_buffer_1_out_6, controlled_buffer_1_out[29:24], controlled_buffer_1_out_5, controlled_buffer_1_out_4, controlled_buffer_1_out_3, controlled_buffer_1_out_2, controlled_buffer_1_out[7:0]} = and_385_out ? 32'h1f94500 : 32'bz;  // Controlled_Buffer controlled_buffer_172
  assign {controlled_buffer_1_out_6, controlled_buffer_1_out[29:24], controlled_buffer_1_out_5, controlled_buffer_1_out_4, controlled_buffer_1_out_3, controlled_buffer_1_out_2, controlled_buffer_1_out[7:0]} = and_386_out ? 32'h1f95500 : 32'bz;  // Controlled_Buffer controlled_buffer_173
  and and_341 (and_341_out, ~zf_q[0], ~zf_q[1]);  // AND_Gate
  and and_342 (and_342_out, and_335_out, d_ff_1_q);
  and and_343 (and_343_out, and_336_out, d_ff_1_q);
  and and_344 (and_344_out, and_337_out, d_ff_1_q);
  and and_345 (and_345_out, and_338_out, d_ff_1_q);
  and and_346 (and_346_out, and_339_out, d_ff_1_q);
  and and_347 (and_347_out, and_333_out, d_ff_1_q);
  assign {controlled_buffer_1_out_6, controlled_buffer_1_out[29:24], controlled_buffer_1_out_5, controlled_buffer_1_out_4, controlled_buffer_1_out_3, controlled_buffer_1_out_2, controlled_buffer_1_out[7:0]} = and_340_out ? 32'h2000ff00 : 32'bz;  // Controlled_Buffer controlled_buffer_174
  assign {controlled_buffer_1_out_6, controlled_buffer_1_out[29:24], controlled_buffer_1_out_5, controlled_buffer_1_out_4, controlled_buffer_1_out_3, controlled_buffer_1_out_2, controlled_buffer_1_out[7:0]} = and_387_out ? 32'h1f90000 : 32'bz;  // Controlled_Buffer controlled_buffer_175
  assign {controlled_buffer_1_out_6, controlled_buffer_1_out[29:24], controlled_buffer_1_out_5, controlled_buffer_1_out_4, controlled_buffer_1_out_3, controlled_buffer_1_out_2, controlled_buffer_1_out[7:0]} = and_388_out ? 32'h1f92000 : 32'bz;  // Controlled_Buffer controlled_buffer_176
  assign {controlled_buffer_1_out_6, controlled_buffer_1_out[29:24], controlled_buffer_1_out_5, controlled_buffer_1_out_4, controlled_buffer_1_out_3, controlled_buffer_1_out_2, controlled_buffer_1_out[7:0]} = and_389_out ? 32'h1f95300 : 32'bz;  // Controlled_Buffer controlled_buffer_177
  and and_348 (and_348_out, ~zf_q[0], zf_q[1]);  // AND_Gate
  and and_349 (and_349_out, zf_q[0], zf_q[1]);
  xor xor_3 (and_324_out[4], and_349_out, and_348_out);
  and and_350 (and_350_out, and_324_out[4], and_335_out, d_ff_2_q);
  and and_351 (and_351_out, and_324_out[3], and_336_out, d_ff_2_q);
  and and_352 (and_352_out, and_324_out[2], and_337_out, d_ff_2_q);
  and and_353 (and_353_out, and_324_out[1], and_338_out, d_ff_2_q);
  and and_354 (and_354_out, and_324_out[0], and_339_out, d_ff_2_q);
  assign {controlled_buffer_1_out_6, controlled_buffer_1_out[29:24], controlled_buffer_1_out_5, controlled_buffer_1_out_4, controlled_buffer_1_out_3, controlled_buffer_1_out_2, controlled_buffer_1_out[7:0]} = and_347_out ? 32'h1000ff00 : 32'bz;  // Controlled_Buffer controlled_buffer_178
  assign {controlled_buffer_1_out_6, controlled_buffer_1_out[29:24], controlled_buffer_1_out_5, controlled_buffer_1_out_4, controlled_buffer_1_out_3, controlled_buffer_1_out_2, controlled_buffer_1_out[7:0]} = and_390_out ? 32'h1f91000 : 32'bz;  // Controlled_Buffer controlled_buffer_179
  and and_355 (and_355_out, d_ff_1_q, and_449_out, and_393_out);
  and and_356 (and_356_out, d_ff_1_q, and_449_out, and_394_out);
  and and_357 (and_357_out, d_ff_1_q, and_449_out, and_395_out);
  and and_358 (and_358_out, and_449_out, and_444_out, and_396_out, d_ff_1_q);
  and and_359 (and_359_out, and_444_out, and_397_out, and_449_out, d_ff_1_q);
  and and_360 (and_360_out, and_449_out, and_444_out, and_398_out, d_ff_1_q);
  and and_361 (and_361_out, and_449_out, and_444_out, and_399_out, d_ff_1_q);
  and and_362 (and_362_out, and_449_out, and_444_out, and_400_out, d_ff_1_q);
  and and_363 (and_363_out, and_449_out, and_444_out, and_401_out, d_ff_1_q);
  and and_364 (and_364_out, and_449_out, and_445_out, and_402_out, d_ff_1_q);
  and and_365 (and_365_out, and_449_out, and_445_out, and_403_out, d_ff_1_q);
  and and_366 (and_366_out, and_449_out, and_445_out, and_404_out, d_ff_1_q);
  and and_367 (and_367_out, and_449_out, and_445_out, and_405_out, d_ff_1_q);
  and and_368 (and_368_out, and_449_out, and_445_out, and_406_out, d_ff_1_q);
  and and_369 (and_369_out, and_449_out, and_445_out, and_407_out, d_ff_1_q);
  and and_370 (and_370_out, and_449_out, and_446_out, and_408_out, d_ff_1_q);
  and and_371 (and_371_out, and_449_out, and_446_out, and_409_out, d_ff_1_q);
  and and_372 (and_372_out, and_449_out, and_446_out, and_410_out, d_ff_1_q);
  and and_373 (and_373_out, and_449_out, and_446_out, and_411_out, d_ff_1_q);
  and and_374 (and_374_out, and_449_out, and_446_out, and_412_out, d_ff_1_q);
  and and_375 (and_375_out, and_449_out, and_447_out, and_414_out, d_ff_1_q);
  and and_376 (and_376_out, and_449_out, and_447_out, and_415_out, d_ff_1_q);
  and and_377 (and_377_out, and_449_out, and_447_out, and_416_out, d_ff_1_q);
  and and_378 (and_378_out, and_449_out, and_447_out, and_417_out, d_ff_1_q);
  and and_379 (and_379_out, and_449_out, and_447_out, and_418_out, d_ff_1_q);
  and and_380 (and_380_out, and_449_out, and_447_out, and_419_out, d_ff_1_q);
  and and_381 (and_381_out, and_449_out, and_448_out, and_420_out, d_ff_1_q);
  and and_382 (and_382_out, and_449_out, and_448_out, and_421_out, d_ff_1_q);
  and and_383 (and_383_out, and_449_out, and_448_out, and_422_out, d_ff_1_q);
  and and_384 (and_384_out, and_449_out, and_448_out, and_423_out, d_ff_1_q);
  and and_385 (and_385_out, and_449_out, and_448_out, and_424_out, d_ff_1_q);
  and and_386 (and_386_out, and_449_out, and_448_out, and_425_out, d_ff_1_q);
  assign {controlled_buffer_1_out_6, controlled_buffer_1_out[29:24], controlled_buffer_1_out_5, controlled_buffer_1_out_4, controlled_buffer_1_out_3, controlled_buffer_1_out_2, controlled_buffer_1_out[7:0]} = and_350_out ? 32'h2000ff00 : 32'bz;  // Controlled_Buffer controlled_buffer_180
  assign {controlled_buffer_1_out_6, controlled_buffer_1_out[29:24], controlled_buffer_1_out_5, controlled_buffer_1_out_4, controlled_buffer_1_out_3, controlled_buffer_1_out_2, controlled_buffer_1_out[7:0]} = and_351_out ? 32'h2000ff00 : 32'bz;  // Controlled_Buffer controlled_buffer_181
  assign {controlled_buffer_1_out_6, controlled_buffer_1_out[29:24], controlled_buffer_1_out_5, controlled_buffer_1_out_4, controlled_buffer_1_out_3, controlled_buffer_1_out_2, controlled_buffer_1_out[7:0]} = and_352_out ? 32'h2000ff00 : 32'bz;  // Controlled_Buffer controlled_buffer_182
  assign {controlled_buffer_1_out_6, controlled_buffer_1_out[29:24], controlled_buffer_1_out_5, controlled_buffer_1_out_4, controlled_buffer_1_out_3, controlled_buffer_1_out_2, controlled_buffer_1_out[7:0]} = and_353_out ? 32'h2000ff00 : 32'bz;  // Controlled_Buffer controlled_buffer_183
  assign {controlled_buffer_1_out_6, controlled_buffer_1_out[29:24], controlled_buffer_1_out_5, controlled_buffer_1_out_4, controlled_buffer_1_out_3, controlled_buffer_1_out_2, controlled_buffer_1_out[7:0]} = and_354_out ? 32'h2000ff00 : 32'bz;  // Controlled_Buffer controlled_buffer_184
  and and_387 (and_387_out, d_ff_1_q, and_449_out, and_432_out);
  and and_388 (and_388_out, and_449_out, and_392_out, d_ff_1_q);
  and and_389 (and_389_out, and_449_out, and_446_out, and_413_out, d_ff_1_q);
  and and_390 (and_390_out, d_ff_1_q, and_449_out, and_391_out);
  and and_391 (and_391_out, and_434_out, and_435_out);
  and and_392 (and_392_out, and_436_out, and_437_out);
  and and_393 (and_393_out, and_438_out, and_439_out);
  and and_394 (and_394_out, and_440_out, and_441_out);
  and and_395 (and_395_out, and_442_out, and_443_out);
  and and_396 (and_396_out, ~controlled_buffer_140_out[15], ~controlled_buffer_140_out[14], ~controlled_buffer_140_out[13], ~controlled_buffer_140_out[12]);  // AND_Gate
  and and_397 (and_397_out, ~controlled_buffer_140_out[15], ~controlled_buffer_140_out[14], ~controlled_buffer_140_out[13], controlled_buffer_140_out[12]);  // AND_Gate
  and and_398 (and_398_out, ~controlled_buffer_140_out[15], ~controlled_buffer_140_out[14], controlled_buffer_140_out[13], ~controlled_buffer_140_out[12]);  // AND_Gate
  and and_399 (and_399_out, ~controlled_buffer_140_out[15], ~controlled_buffer_140_out[14], controlled_buffer_140_out[13], controlled_buffer_140_out[12]);  // AND_Gate
  and and_400 (and_400_out, ~controlled_buffer_140_out[15], controlled_buffer_140_out[14], ~controlled_buffer_140_out[13], ~controlled_buffer_140_out[12]);  // AND_Gate
  and and_401 (and_401_out, ~controlled_buffer_140_out[15], controlled_buffer_140_out[14], ~controlled_buffer_140_out[13], controlled_buffer_140_out[12]);  // AND_Gate
  and and_402 (and_402_out, ~controlled_buffer_140_out[15], ~controlled_buffer_140_out[14], ~controlled_buffer_140_out[13], ~controlled_buffer_140_out[12]);  // AND_Gate
  and and_403 (and_403_out, ~controlled_buffer_140_out[15], ~controlled_buffer_140_out[14], ~controlled_buffer_140_out[13], controlled_buffer_140_out[12]);  // AND_Gate
  and and_404 (and_404_out, ~controlled_buffer_140_out[15], ~controlled_buffer_140_out[14], controlled_buffer_140_out[13], ~controlled_buffer_140_out[12]);  // AND_Gate
  and and_405 (and_405_out, ~controlled_buffer_140_out[15], ~controlled_buffer_140_out[14], controlled_buffer_140_out[13], controlled_buffer_140_out[12]);  // AND_Gate
  and and_406 (and_406_out, ~controlled_buffer_140_out[15], controlled_buffer_140_out[14], ~controlled_buffer_140_out[13], ~controlled_buffer_140_out[12]);  // AND_Gate
  and and_407 (and_407_out, ~controlled_buffer_140_out[15], controlled_buffer_140_out[14], ~controlled_buffer_140_out[13], controlled_buffer_140_out[12]);  // AND_Gate
  and and_408 (and_408_out, ~controlled_buffer_140_out[15], ~controlled_buffer_140_out[14], ~controlled_buffer_140_out[13], ~controlled_buffer_140_out[12]);  // AND_Gate
  and and_409 (and_409_out, ~controlled_buffer_140_out[15], ~controlled_buffer_140_out[14], ~controlled_buffer_140_out[13], controlled_buffer_140_out[12]);  // AND_Gate
  and and_410 (and_410_out, ~controlled_buffer_140_out[15], ~controlled_buffer_140_out[14], controlled_buffer_140_out[13], ~controlled_buffer_140_out[12]);  // AND_Gate
  and and_411 (and_411_out, ~controlled_buffer_140_out[15], ~controlled_buffer_140_out[14], controlled_buffer_140_out[13], controlled_buffer_140_out[12]);  // AND_Gate
  and and_412 (and_412_out, ~controlled_buffer_140_out[15], controlled_buffer_140_out[14], ~controlled_buffer_140_out[13], ~controlled_buffer_140_out[12]);  // AND_Gate
  and and_413 (and_413_out, ~controlled_buffer_140_out[15], controlled_buffer_140_out[14], ~controlled_buffer_140_out[13], controlled_buffer_140_out[12]);  // AND_Gate
  and and_414 (and_414_out, ~controlled_buffer_140_out[15], ~controlled_buffer_140_out[14], ~controlled_buffer_140_out[13], ~controlled_buffer_140_out[12]);  // AND_Gate
  and and_415 (and_415_out, ~controlled_buffer_140_out[15], ~controlled_buffer_140_out[14], ~controlled_buffer_140_out[13], controlled_buffer_140_out[12]);  // AND_Gate
  and and_416 (and_416_out, ~controlled_buffer_140_out[15], ~controlled_buffer_140_out[14], controlled_buffer_140_out[13], ~controlled_buffer_140_out[12]);  // AND_Gate
  and and_417 (and_417_out, ~controlled_buffer_140_out[15], ~controlled_buffer_140_out[14], controlled_buffer_140_out[13], controlled_buffer_140_out[12]);  // AND_Gate
  and and_418 (and_418_out, ~controlled_buffer_140_out[15], controlled_buffer_140_out[14], ~controlled_buffer_140_out[13], ~controlled_buffer_140_out[12]);  // AND_Gate
  and and_419 (and_419_out, ~controlled_buffer_140_out[15], controlled_buffer_140_out[14], ~controlled_buffer_140_out[13], controlled_buffer_140_out[12]);  // AND_Gate
  and and_420 (and_420_out, ~controlled_buffer_140_out[15], ~controlled_buffer_140_out[14], ~controlled_buffer_140_out[13], ~controlled_buffer_140_out[12]);  // AND_Gate
  and and_421 (and_421_out, ~controlled_buffer_140_out[15], ~controlled_buffer_140_out[14], ~controlled_buffer_140_out[13], controlled_buffer_140_out[12]);  // AND_Gate
  and and_422 (and_422_out, ~controlled_buffer_140_out[15], ~controlled_buffer_140_out[14], controlled_buffer_140_out[13], ~controlled_buffer_140_out[12]);  // AND_Gate
  and and_423 (and_423_out, ~controlled_buffer_140_out[15], ~controlled_buffer_140_out[14], controlled_buffer_140_out[13], controlled_buffer_140_out[12]);  // AND_Gate
  and and_424 (and_424_out, ~controlled_buffer_140_out[15], controlled_buffer_140_out[14], ~controlled_buffer_140_out[13], ~controlled_buffer_140_out[12]);  // AND_Gate
  and and_425 (and_425_out, ~controlled_buffer_140_out[15], controlled_buffer_140_out[14], ~controlled_buffer_140_out[13], controlled_buffer_140_out[12]);  // AND_Gate
  and and_426 (and_426_out, and_324_out[4], and_342_out);
  and and_427 (and_427_out, and_324_out[3], and_343_out);
  and and_428 (and_428_out, and_324_out[2], and_344_out);
  and and_429 (and_429_out, and_324_out[1], and_345_out);
  and and_430 (and_430_out, and_324_out[0], and_346_out);
  and and_431 (and_431_out, ~controlled_buffer_140_out[15], ~controlled_buffer_140_out[14], ~controlled_buffer_140_out[13], ~controlled_buffer_140_out[12]);  // AND_Gate
  and and_432 (and_432_out, and_431_out, and_433_out);
  and and_433 (and_433_out, ~controlled_buffer_140_out[11], ~controlled_buffer_140_out[10], ~controlled_buffer_140_out[9], ~controlled_buffer_140_out[8]);  // AND_Gate
  and and_434 (and_434_out, ~controlled_buffer_140_out[15], ~controlled_buffer_140_out[14], ~controlled_buffer_140_out[13], controlled_buffer_140_out[12]);  // AND_Gate
  and and_435 (and_435_out, ~controlled_buffer_140_out[11], ~controlled_buffer_140_out[10], ~controlled_buffer_140_out[9], ~controlled_buffer_140_out[8]);  // AND_Gate
  and and_436 (and_436_out, ~controlled_buffer_140_out[15], ~controlled_buffer_140_out[14], controlled_buffer_140_out[13], ~controlled_buffer_140_out[12]);  // AND_Gate
  and and_437 (and_437_out, ~controlled_buffer_140_out[11], ~controlled_buffer_140_out[10], ~controlled_buffer_140_out[9], ~controlled_buffer_140_out[8]);  // AND_Gate
  and and_438 (and_438_out, ~controlled_buffer_140_out[15], ~controlled_buffer_140_out[14], controlled_buffer_140_out[13], controlled_buffer_140_out[12]);  // AND_Gate
  and and_439 (and_439_out, ~controlled_buffer_140_out[11], ~controlled_buffer_140_out[10], ~controlled_buffer_140_out[9], ~controlled_buffer_140_out[8]);  // AND_Gate
  and and_440 (and_440_out, ~controlled_buffer_140_out[15], controlled_buffer_140_out[14], ~controlled_buffer_140_out[13], ~controlled_buffer_140_out[12]);  // AND_Gate
  and and_441 (and_441_out, ~controlled_buffer_140_out[11], ~controlled_buffer_140_out[10], ~controlled_buffer_140_out[9], ~controlled_buffer_140_out[8]);  // AND_Gate
  and and_442 (and_442_out, ~controlled_buffer_140_out[15], controlled_buffer_140_out[14], ~controlled_buffer_140_out[13], controlled_buffer_140_out[12]);  // AND_Gate
  and and_443 (and_443_out, ~controlled_buffer_140_out[11], ~controlled_buffer_140_out[10], ~controlled_buffer_140_out[9], ~controlled_buffer_140_out[8]);  // AND_Gate
  assign {controlled_buffer_1_out_6, controlled_buffer_1_out[29:24], controlled_buffer_1_out_5, controlled_buffer_1_out_4, controlled_buffer_1_out_3, controlled_buffer_1_out_2, controlled_buffer_1_out[7:0]} = and_426_out ? 32'h1000ff00 : 32'bz;  // Controlled_Buffer controlled_buffer_185
  assign {controlled_buffer_1_out_6, controlled_buffer_1_out[29:24], controlled_buffer_1_out_5, controlled_buffer_1_out_4, controlled_buffer_1_out_3, controlled_buffer_1_out_2, controlled_buffer_1_out[7:0]} = and_427_out ? 32'h1000ff00 : 32'bz;  // Controlled_Buffer controlled_buffer_186
  assign {controlled_buffer_1_out_6, controlled_buffer_1_out[29:24], controlled_buffer_1_out_5, controlled_buffer_1_out_4, controlled_buffer_1_out_3, controlled_buffer_1_out_2, controlled_buffer_1_out[7:0]} = and_428_out ? 32'h1000ff00 : 32'bz;  // Controlled_Buffer controlled_buffer_187
  assign {controlled_buffer_1_out_6, controlled_buffer_1_out[29:24], controlled_buffer_1_out_5, controlled_buffer_1_out_4, controlled_buffer_1_out_3, controlled_buffer_1_out_2, controlled_buffer_1_out[7:0]} = and_429_out ? 32'h1000ff00 : 32'bz;  // Controlled_Buffer controlled_buffer_188
  assign {controlled_buffer_1_out_6, controlled_buffer_1_out[29:24], controlled_buffer_1_out_5, controlled_buffer_1_out_4, controlled_buffer_1_out_3, controlled_buffer_1_out_2, controlled_buffer_1_out[7:0]} = and_430_out ? 32'h1000ff00 : 32'bz;  // Controlled_Buffer controlled_buffer_189
  and and_444 (and_444_out, ~controlled_buffer_140_out[11], ~controlled_buffer_140_out[10], ~controlled_buffer_140_out[9], controlled_buffer_140_out[8]);  // AND_Gate
  and and_445 (and_445_out, ~controlled_buffer_140_out[11], ~controlled_buffer_140_out[10], controlled_buffer_140_out[9], ~controlled_buffer_140_out[8]);  // AND_Gate
  and and_446 (and_446_out, ~controlled_buffer_140_out[11], ~controlled_buffer_140_out[10], controlled_buffer_140_out[9], controlled_buffer_140_out[8]);  // AND_Gate
  and and_447 (and_447_out, ~controlled_buffer_140_out[11], controlled_buffer_140_out[10], ~controlled_buffer_140_out[9], ~controlled_buffer_140_out[8]);  // AND_Gate
  and and_448 (and_448_out, ~controlled_buffer_140_out[11], controlled_buffer_140_out[10], ~controlled_buffer_140_out[9], controlled_buffer_140_out[8]);  // AND_Gate
  ExactlyOne xor_4 (
    .out(xor_4_out), .in0(and_426_out), .in1(and_427_out), .in2(and_428_out), .in3(and_429_out),
    .in4(and_430_out), .in5(and_333_out));
  and and_449 (and_449_out, ~controlled_buffer_140_out[7], ~controlled_buffer_140_out[6], ~controlled_buffer_140_out[5], ~controlled_buffer_140_out[4], ~controlled_buffer_140_out[3], controlled_buffer_140_out[2], controlled_buffer_140_out[1], controlled_buffer_140_out[0]);  // AND_Gate

  // Notes on the sheet:
  //   eax
  //   ebx
  //   ecx
  //   edx
  //   esi
  //   edi
  //   esp
  //   ebp
  //   regc
  //   cbus
  //   alu
endmodule

module alu32 (
  input  SHR,
  input  SHL,
  input  XOR,
  input  OR,
  input  AND,
  input  SUB,
  input  ADD,
  input  MUL,
  input  [31:0] in_9,
  input  [31:0] in_10,
  output out_11,
  output [31:0] out_12,
  output out_13,
  output out_14,
  output out_15,
  output out_16
);

  wire and_2_out, and_3_out, and_4_out, and_5_out, and_6_out, and_7_out, and_8_out, and_9_out,
       n32b_shl_1_out_2, or_2_out, or_3_out, xor_2_out, xor_3_out, xor_4_out, xor_5_out, xor_6_out,
       xor_7_out, xor_8_out, xor_9_out, xor_10_out, xor_11_out, xor_12_out, xor_13_out, xor_14_out,
       xor_15_out, xor_16_out, xor_17_out, xor_18_out, xor_19_out, xor_20_out, xor_21_out, xor_22_out,
       xor_23_out, xor_24_out, xor_25_out, xor_26_out, xor_27_out, xor_28_out, xor_29_out, xor_30_out,
       xor_31_out;
  wire [31:0] and_1_out, multiplier_1_out, n32b_shl_1_out_3, n32bit_add_sub_1_out_5, or_1_out, undriven,
       xor_1_out;

  assign and_1_out = in_9 & in_10;  // AND_Gate and_1, 32 bits wide
  assign or_1_out = in_9 | in_10;  // OR_Gate or_1, 32 bits wide
  assign xor_1_out = in_9 ^ in_10;  // XOR_Gate xor_1, 32 bits wide
  _32b_shl u_32b_shl_1 (.in_1(in_9), .out_2(n32b_shl_1_out_2), .out_3(n32b_shl_1_out_3));
  _32b_shr u_32b_shr_1 (.in_2(in_9), .in_1(undriven));
  and and_2 (and_2_out, SHR, ~SHL, ~XOR, ~OR, ~AND, ~SUB, ~ADD, ~MUL, ~1'b0);  // AND_Gate
  and and_3 (and_3_out, ~SHR, SHL, ~XOR, ~OR, ~AND, ~SUB, ~ADD, ~MUL, ~1'b0);  // AND_Gate
  and and_4 (and_4_out, ~SHR, ~SHL, XOR, ~OR, ~AND, ~SUB, ~ADD, ~MUL, ~1'b0);  // AND_Gate
  and and_5 (and_5_out, ~SHR, ~SHL, ~XOR, OR, ~AND, ~SUB, ~ADD, ~MUL, ~1'b0);  // AND_Gate
  and and_6 (and_6_out, ~SHR, ~SHL, ~XOR, ~OR, AND, ~SUB, ~ADD, ~MUL, ~1'b0);  // AND_Gate
  and and_7 (and_7_out, ~SHR, ~SHL, ~XOR, ~OR, ~AND, SUB, ~ADD, ~MUL, ~1'b0);  // AND_Gate
  and and_8 (and_8_out, ~SHR, ~SHL, ~XOR, ~OR, ~AND, ~SUB, ADD, ~MUL, ~1'b0);  // AND_Gate
  and and_9 (and_9_out, ~SHR, ~SHL, ~XOR, ~OR, ~AND, ~SUB, ~ADD, MUL, ~1'b0);  // AND_Gate
  _32bit_add_sub u_32bit_add_sub_1 (
    .in_1(in_9), .in_2(in_10), .in_3(SUB), .out_4(out_14), .out_5(n32bit_add_sub_1_out_5));
  Multiplier #(.width(32)) multiplier_1 (.a(in_9), .b(in_10), .out(multiplier_1_out));  // open: cin, cout
  or or_2 (or_2_out, and_8_out, and_7_out);
  assign out_12 = or_2_out ? n32bit_add_sub_1_out_5 : 32'bz;  // Controlled_Buffer controlled_buffer_1
  assign out_12 = and_6_out ? and_1_out : 32'bz;  // Controlled_Buffer controlled_buffer_2
  assign out_12 = and_5_out ? or_1_out : 32'bz;  // Controlled_Buffer controlled_buffer_3
  assign out_12 = and_4_out ? xor_1_out : 32'bz;  // Controlled_Buffer controlled_buffer_4
  assign out_12 = and_3_out ? n32b_shl_1_out_3 : 32'bz;  // Controlled_Buffer controlled_buffer_5
  assign out_12 = and_2_out ? undriven : 32'bz;  // Controlled_Buffer controlled_buffer_6
  assign out_12 = and_9_out ? multiplier_1_out : 32'bz;  // Controlled_Buffer controlled_buffer_7
  or or_3 (or_3_out, and_3_out, and_8_out);
  and and_10 (out_13, out_12[31], or_3_out);
  nor nor_1 (out_16, out_12[31], out_12[30], out_12[29], out_12[28], out_12[27], out_12[26], out_12[25], out_12[24], out_12[23], out_12[22], out_12[21], out_12[20], out_12[19], out_12[18], out_12[17], out_12[16], out_12[15], out_12[14], out_12[13], out_12[12], out_12[11], out_12[10], out_12[9], out_12[8], out_12[7], out_12[6], out_12[5], out_12[4], out_12[3], out_12[2], out_12[1], out_12[0]);
  xor xor_2 (xor_2_out, out_12[0], out_12[1]);
  xor xor_3 (xor_3_out, out_12[2], out_12[3]);
  xor xor_4 (xor_4_out, out_12[4], out_12[5]);
  xor xor_5 (xor_5_out, out_12[6], out_12[7]);
  xor xor_6 (xor_6_out, out_12[8], out_12[9]);
  xor xor_7 (xor_7_out, out_12[10], out_12[11]);
  xor xor_8 (xor_8_out, out_12[12], out_12[13]);
  xor xor_9 (xor_9_out, out_12[14], out_12[15]);
  xor xor_10 (xor_10_out, out_12[16], out_12[17]);
  xor xor_11 (xor_11_out, out_12[18], out_12[19]);
  xor xor_12 (xor_12_out, out_12[20], out_12[21]);
  xor xor_13 (xor_13_out, out_12[22], out_12[23]);
  xor xor_14 (xor_14_out, out_12[24], out_12[25]);
  xor xor_15 (xor_15_out, out_12[26], out_12[27]);
  xor xor_16 (xor_16_out, out_12[28], out_12[29]);
  xor xor_17 (xor_17_out, out_12[30], out_12[31]);
  xor xor_18 (xor_18_out, xor_2_out, xor_3_out);
  xor xor_19 (xor_19_out, xor_4_out, xor_5_out);
  xor xor_20 (xor_20_out, xor_6_out, xor_7_out);
  xor xor_21 (xor_21_out, xor_8_out, xor_9_out);
  xor xor_22 (xor_22_out, xor_10_out, xor_11_out);
  xor xor_23 (xor_23_out, xor_12_out, xor_13_out);
  xor xor_24 (xor_24_out, xor_14_out, xor_15_out);
  xor xor_25 (xor_25_out, xor_16_out, xor_17_out);
  xor xor_26 (xor_26_out, xor_18_out, xor_19_out);
  xor xor_27 (xor_27_out, xor_20_out, xor_21_out);
  xor xor_28 (xor_28_out, xor_22_out, xor_23_out);
  xor xor_29 (xor_29_out, xor_24_out, xor_25_out);
  xor xor_30 (xor_30_out, xor_26_out, xor_27_out);
  xor xor_31 (xor_31_out, xor_28_out, xor_29_out);
  xor xor_32 (out_11, xor_30_out, xor_31_out);

  assign out_15 = out_12[31];
endmodule

module _32b_shl (
  input  [31:0] in_1,
  output out_2,
  output [31:0] out_3
);


  assign out_2 = in_1[31];
  assign out_3 = {in_1[30:0], 1'b0};
endmodule

module _32b_shr (
  input  [31:0] in_1,
  input  [31:0] in_2
);


  assign in_2[31:1] = in_1[30:0];
  // also tied to GND on the sheet: in_1[31]
endmodule

module eip (
  input  in_1,
  input  in_2,
  input  [15:0] in_3,
  output [15:0] out_4
);

  wire or_1_out;
  wire [15:0] adder_1_out, counter_1_q, register_1_q;

  Counter #(.width(16), .max('hffff)) counter_1 (
    .Q(counter_1_q), .clk(in_1), .clr(in_2));  // open: load, D, count, carry
  Register #(.width(16)) register_1 (.D(in_3), .en(in_2), .Q(register_1_q), .clk(in_2));  // open: clr
  Adder #(.width(16)) adder_1 (.a(counter_1_q), .b(register_1_q), .out(adder_1_out));  // open: cin, cout
  or or_1 (or_1_out, in_1, in_2);
  Register #(.width(16)) register_2 (.D(adder_1_out), .en(or_1_out), .Q(out_4), .clk(or_1_out));  // open: clr
endmodule

module eip2 (
  input  in_1,
  input  in_2,
  input  [15:0] in_3,
  input  in_4,
  input  in_5,
  output [15:0] out_6
);

  wire and_1_out, or_1_out;
  wire [15:0] counter_1_q, register_1_q;

  and and_1 (and_1_out, in_1, in_2);
  Register #(.width(16), .trigger("falling")) register_1 (
    .D(in_3), .en(1'b1), .Q(register_1_q), .clk(and_1_out), .clr(in_5));
  Counter #(.width(16), .max('hffff)) counter_1 (
    .Q(counter_1_q), .clk(in_1), .clr(or_1_out));  // open: load, D, count, carry
  or or_1 (or_1_out, in_5, in_4);
  Adder #(.width(16)) adder_1 (.a(counter_1_q), .b(register_1_q), .out(out_6));  // open: cin, cout
endmodule
